// Logisim project rv-cpu.circ as structural Verilog: 18 circuits, main circuit ◇单周期RISC-V
module \单周期RISC_V  (
  input  IR1,
  input  IR2,
  input  IR3,
  output RegWrite,
  output MemWrite,
  output [31:0] PC,
  output [31:0] IR,
  output [31:0] RDin,
  output [31:0] MDin,
  output [31:0] LedData
);

  wire alu_1_equal, alu_1_out_4, and_5_out, and_6_out, beq, bge, bge_ctrl, bne, branch, CLK, clock_1_out,
       comparator_1_eq, comparator_1_lt, comparator_2_eq, d_ff_1_q, decoder_1_out0, decoder_1_out1,
       decoder_1_out2, decoder_1_out3, ecall, Go, halt, IR1_t, IR2_t, IR3_t, IRA, IRB, IRC, Jxx_ctrl,
       nand_1_out, not_1_out, not_2_out, riscv_probe_1_p2, riscv_probe_1_p3, RST, sb, W1, W2, W3,
       \单周期硬布线控制器_1_alu_src , \单周期硬布线控制器_1_beq , \单周期硬布线控制器_1_bne , \单周期硬布线控制器_1_jal , \单周期硬布线控制器_1_jalr ,
       \单周期硬布线控制器_1_memtoreg , \单周期硬布线控制器_1_s_type ;
  wire [3:0] \单周期硬布线控制器_1_alu_op ;
  wire [4:0] multiplexer_4_out, multiplexer_5_out;
  wire [11:0] multiplexer_6_out;
  wire [12:0] CNT_num;
  wire [15:0] \总周期数 ;
  wire [31:0] ALU_out, bit_extender_1_out, bit_extender_2_out, bit_extender_3_out, bxx_pc, jal_pc, jalr_pc,
       mem_ld, multiplexer_1_out, multiplexer_2_out, multiplexer_3_out, multiplexer_7_out, multiplexer_8_out,
       PC_4, R1_out, R2_out, sb_word;

  Button \u_继续运行  (.out(Go));
  Button _1 (.out(IRA));
  Button _2 (.out(IRB));
  Button _3 (.out(IRC));
  or or_1 (Jxx_ctrl, \单周期硬布线控制器_1_jal , \单周期硬布线控制器_1_jalr );
  LED #(.active("true")) led_1 (.in(W1));
  LED #(.active("true")) led_2 (.in(W2));
  LED #(.active("true")) led_3 (.in(W3));
  Multiplexer #(.select(1), .width(32), .disabled("Z"), .enable("false")) multiplexer_1 (
    .in0(PC_4), .in1(bxx_pc), .out(multiplexer_1_out), .sel(branch));
  Multiplexer #(.select(1), .width(32), .disabled("Z"), .enable("false")) multiplexer_2 (
    .in0(multiplexer_1_out), .in1(jal_pc), .out(multiplexer_2_out), .sel(\单周期硬布线控制器_1_jal ));
  Hex_Digit_Display hex_digit_display_1 (.value(LedData[31:28]));  // open: dp
  Multiplexer #(.select(1), .width(32), .disabled("Z"), .enable("false")) multiplexer_3 (
    .in0(multiplexer_2_out), .in1(jalr_pc), .out(multiplexer_3_out), .sel(\单周期硬布线控制器_1_jalr ));
  not not_1 (not_1_out, halt);
  Adder #(.width(32)) adder_1 (.a(PC), .b(32'h4), .out(PC_4));  // open: cin, cout
  or or_2 (branch, beq, bne, bge);
  Hex_Digit_Display hex_digit_display_2 (.value(LedData[23:20]));  // open: dp
  Hex_Digit_Display hex_digit_display_3 (.value(LedData[27:24]));  // open: dp
  Counter #(.width(16), .max('hffff), .ongoal("wrap"), .trigger("rising"), .behavior("old")) counter_1 (
    .count(not_2_out), .Q(\总周期数 ), .clk(CLK));  // open: load, D, carry, clr, preset
  not not_2 (not_2_out, halt);
  Register #(.width(32), .trigger("rising"), .Select("low")) u_PC (
    .D(multiplexer_3_out), .en(not_1_out), .Q(PC), .clk(CLK), .clr(RST));
  Hex_Digit_Display hex_digit_display_4 (.value(LedData[19:16]));  // open: dp
  Hex_Digit_Display hex_digit_display_5 (.value(LedData[15:12]));  // open: dp
  Hex_Digit_Display hex_digit_display_6 (.value(LedData[11:8]));  // open: dp
  Hex_Digit_Display hex_digit_display_7 (.value(LedData[7:4]));  // open: dp
  // Probe on \总周期数 
  // RiscV_Probe riscv_probe_1: pin names not known; wires that end beside it: IR, riscv_probe_1_p2, riscv_probe_1_p3, riscv_probe_1_p3
  ROM #(.addrWidth(10), .dataWidth(32), .Select("high")) rom_1 (.addr(PC[11:2]), .data(IR));
  Hex_Digit_Display hex_digit_display_8 (.value(LedData[3:0]));  // open: dp
  \单周期硬布线控制器  \u_单周期硬布线控制器_1  (
    .Funct({IR[30], IR[25], IR[14:12]}), .OP(IR[6:2]), .ALU_OP(\单周期硬布线控制器_1_alu_op ),
    .MemToReg(\单周期硬布线控制器_1_memtoreg ), .MemWrite(MemWrite), .ALU_SRC(\单周期硬布线控制器_1_alu_src ),
    .RegWrite(RegWrite), .ecall(ecall), .S_type(\单周期硬布线控制器_1_s_type ), .Jalr(\单周期硬布线控制器_1_jalr ),
    .Beq(\单周期硬布线控制器_1_beq ), .JAL(\单周期硬布线控制器_1_jal ), .Bne(\单周期硬布线控制器_1_bne ), .in_3(IR[21]),
    .uret(riscv_probe_1_p2), .sb(sb), .bge(bge_ctrl));
  Multiplexer #(.select(1), .width(5), .disabled("Z"), .enable("false")) multiplexer_4 (
    .in0(IR[19:15]), .in1(5'b10001), .out(multiplexer_4_out), .sel(ecall));
  Multiplexer #(.select(1), .width(5), .disabled("Z"), .enable("false")) multiplexer_5 (
    .in0(IR[24:20]), .in1(5'b01010), .out(multiplexer_5_out), .sel(ecall));
  or or_3 (IR1_t, IR1, IRA);
  Multiplexer #(.select(1), .width(12), .disabled("Z"), .enable("false")) multiplexer_6 (
    .in0(IR[31:20]), .in1({IR[31:25], IR[11:7]}), .out(multiplexer_6_out), .sel(\单周期硬布线控制器_1_s_type ));
  assign bit_extender_1_out = {{19{IR[31]}}, {IR[31], IR[7], IR[30:25], IR[11:8], 1'b0}};  // Bit_Extender bit_extender_1
  assign bit_extender_2_out = {{11{IR[31]}}, {IR[31], IR[19:12], IR[20], IR[30:21], 1'b0}};  // Bit_Extender bit_extender_2
  or or_4 (IR2_t, IR2, IRB);
  Regifile regifile_1 (
    .Din(RDin), .Clk(CLK), .R1(R1_out), .R2(R2_out), .WE(RegWrite), .W_num(IR[11:7]),
    .R1_num(multiplexer_4_out), .R2_num(multiplexer_5_out));
  assign bit_extender_3_out = {{20{multiplexer_6_out[11]}}, multiplexer_6_out};  // Bit_Extender bit_extender_3
  Multiplexer #(.select(1), .width(32), .disabled("Z"), .enable("false")) multiplexer_7 (
    .in0(R2_out), .in1(bit_extender_3_out), .out(multiplexer_7_out), .sel(\单周期硬布线控制器_1_alu_src ));
  Adder #(.width(32)) adder_2 (.a(bit_extender_1_out), .b(PC), .out(bxx_pc));  // open: cin, cout
  Adder #(.width(32)) adder_3 (.a(bit_extender_2_out), .b(PC), .out(jal_pc));  // open: cin, cout
  or or_5 (IR3_t, IR3, IRC);
  and and_1 (beq, \单周期硬布线控制器_1_beq , alu_1_equal);
  and and_2 (bne, \单周期硬布线控制器_1_bne , ~alu_1_equal);  // AND_Gate
  ALU alu_1 (
    .X(R1_out), .Y(multiplexer_7_out), .AluOP(\单周期硬布线控制器_1_alu_op ), .Equal(alu_1_equal), .Result(ALU_out),
    .out_4(alu_1_out_4));  // open: Result_2, out_6
  and and_3 (bge, alu_1_out_4, bge_ctrl);
  assign jalr_pc = ALU_out & ~32'h1;  // AND_Gate and_4, 32 bits wide
  RAM #(.addrWidth(10), .dataWidth(32), .bus("separate"), .Select("high")) ram_1 (
    .addr(ALU_out[11:2]), .din(MDin), .data(mem_ld), .str(MemWrite), .clk(CLK));  // open: sel, ld, clr
  Multiplexer #(.select(1), .width(32), .disabled("Z"), .enable("false")) multiplexer_8 (
    .in0(ALU_out), .in1(mem_ld), .out(multiplexer_8_out), .sel(\单周期硬布线控制器_1_memtoreg ));
  Multiplexer #(.select(1), .width(32), .disabled("Z"), .enable("false")) multiplexer_9 (
    .in0(multiplexer_8_out), .in1(PC_4), .out(RDin), .sel(Jxx_ctrl));
  D_Flip_Flop #(.trigger("high"), .Pre_Clr_Positions("LEGACY"), .NegatePresetClear("false"), .enable("true"), .NewFFLayout("false")) d_ff_1 (.Q(d_ff_1_q));  // open: clk, D, Qn, preset, en, reset
  // Probe on 13'h60a
  Comparator #(.width(13), .mode("twosComplement")) comparator_1 (
    .a(CNT_num), .b(13'h60a), .eq(comparator_1_eq), .lt(comparator_1_lt));  // open: gt
  Clock #(.highDuration(1), .lowDuration(1)) clock_1 (.out(clock_1_out));
  Comparator #(.width(32), .mode("twosComplement")) comparator_2 (
    .a(R1_out), .b(32'h22), .eq(comparator_2_eq));  // open: gt, lt
  Counter #(.width(13), .max('h1fff), .ongoal("stay"), .trigger("rising"), .behavior("old")) counter_2 (
    .count(comparator_1_lt), .Q(CNT_num), .clk(clock_1_out));  // open: load, D, carry, clr, preset
  and and_5 (and_5_out, ecall, comparator_2_eq);
  Decoder #(.select(2), .tristate("false"), .disabled("Z"), .enable("false")) decoder_1 (
    .out0(decoder_1_out0), .out1(decoder_1_out1), .out2(decoder_1_out2), .out3(decoder_1_out3),
    .sel(ALU_out[1:0]));
  nand nand_1 (nand_1_out, d_ff_1_q, comparator_1_eq);
  and and_6 (and_6_out, ~comparator_2_eq, ecall);  // AND_Gate
  Multiplexer #(.select(1), .width(32), .disabled("Z"), .enable("false")) multiplexer_10 (
    .in0(R2_out), .in1(sb_word), .out(MDin), .sel(sb));
  assign CLK = nand_1_out ? clock_1_out : 1'bz;  // Controlled_Buffer controlled_buffer_1
  Pull_Resistor #(.pull(1)) pull_resistor_1 (.node(CLK));
  Register #(.width(32), .trigger("rising"), .Select("low")) register_1 (
    .D(R2_out), .en(and_5_out), .Q(LedData), .clk(CLK));  // open: clr
  and and_7 (halt, and_6_out, ~Go);  // AND_Gate
  Multiplexer #(.select(1), .width(8), .disabled("Z"), .enable("false")) multiplexer_11 (
    .in0(mem_ld[7:0]), .in1(R2_out[7:0]), .out(sb_word[7:0]), .sel(decoder_1_out0));
  Multiplexer #(.select(1), .width(8), .disabled("Z"), .enable("false")) multiplexer_12 (
    .in0(mem_ld[15:8]), .in1(R2_out[7:0]), .out(sb_word[15:8]), .sel(decoder_1_out1));
  Multiplexer #(.select(1), .width(8), .disabled("Z"), .enable("false")) multiplexer_13 (
    .in0(mem_ld[23:16]), .in1(R2_out[7:0]), .out(sb_word[23:16]), .sel(decoder_1_out2));
  Multiplexer #(.select(1), .width(8), .disabled("Z"), .enable("false")) multiplexer_14 (
    .in0(mem_ld[31:24]), .in1(R2_out[7:0]), .out(sb_word[31:24]), .sel(decoder_1_out3));

  // Other names for the same wires on the sheet: mem_addr[31:0] = ALU_out

  // Notes on the sheet:
  //   中断源
  //   中断等待指示
  //   数码管输出应该用寄存器锁存，否则显示数据只能一闪而过
  //   数码管输出
  //   指令探针
  //   指令存储器
  //   指令字
  //   contents of rom_1 (hex, n*v repeats v):
  //   100493 100006f 100493 200913 300993 100006f 100493 200913 300993 100006f 100493 200913 300993
  //   100006f 100493 200913 300993 3ac000ef 100413 100493 1f49493 900533 2200893 73 24d493 48463 fedff06f
  //   900533 2200893 73 100493 249493 900533 2200893 73 48463 fedff06f 100493 1f49493 900533 2200893 73
  //   4034d493 900533 2200893 73 4044d493 900533 2200893 73 4044d493 900533 2200893 73 4044d493 900533
  //   2200893 73 4044d493 900533 2200893 73 4044d493 900533 2200893 73 4044d493 900533 2200893 73 4044d493
  //   900533 2200893 73 100413 1f41993 41f9d993 433 c00913 300b13 140413 f47413 800293 100313 499993
  //   89e9b3 1300533 2200893 73 406282b3 fe0294e3 140413 f00f93 1f47433 1c41413 800293 100313 49d993
  //   89e9b3 1300533 2200893 73 406282b3 fe0294e3 1c45413 406b0b33 b0463 f95ff06f 2b3 fff2c293 829293
  //   ff2e293 500533 2200893 73 fff00413 493 84a023 140413 448493 84a023 140413 448493 84a023 140413
  //   448493 84a023 140413 448493 84a023 140413 448493 84a023 140413 448493 84a023 140413 448493 84a023
  //   140413 448493 84a023 140413 448493 84a023 140413 448493 84a023 140413 448493 84a023 140413 448493
  //   84a023 140413 448493 84a023 140413 448493 84a023 140413 448493 84a023 140413 448493 140413 433
  //   3c00493 42983 4aa03 149a2b3 28663 134a023 1442023 ffc48493 fe9412e3 800533 2200893 73 440413 3c00493
  //   fc9416e3 100293 300313 800493 849493 7648493 900533 2200893 73 800e13 5494b3 6494b3 900533 2200893
  //   73 fffe0e13 fe0e14e3 a00893 73 100293 300313 800493 849493 7648493 1449493 900533 2200893 73 800e13
  //   4054d4b3 4064d4b3 900533 2200893 73 fffe0e13 fe0e14e3 a00893 73 313 2000e13 493 100913 930023 900533
  //   2200893 73 12484b3 130313 fffe0e13 fe0e12e3 800e13 313 32483 900533 2200893 73 430313 fffe0e13
  //   fe0e14e3 a00893 73 f00493 900533 2200893 73 fff48493 fe04d8e3 a00893 73 a00893 73 413 140413 800533
  //   2200893 73 240413 800533 2200893 73 340413 800533 2200893 73 440413 800533 2200893 73 540413 800533
  //   2200893 73 640413 800533 2200893 73 740413 800533 2200893 73 840413 800533 2200893 2200893 73 8067
  //   JAL
  //   JALR
  //   URET
  //   Beq
  //   Bne
  //   MemToReg
  //   MemWrite
  //   AluOP
  //   AluSrcB
  //   RegWrite
  //   S_Type
  //   sb
  //   bge
  //   为方便自动评测，需要输出PC，IR，寄存器堆写如数据RDin
  //   数据存储器
  //   RAM写使能MemWrite、RAM写入数据MDin等信号
  //   控制位
  //   暂停节拍，不能为0
  //   用这个时钟源需要去掉电路中的其他时钟源
  //   戳工具置1进入计数暂停模式，ctrl+k时钟自动运行到对应节拍暂停
  //   ctrl+k关闭时钟连续运行，将控制位置零，进入单步调试模式调试
  //   可计数暂停的时钟源
endmodule

// 单周期硬布线控制器
module \单周期硬布线控制器  (
  input  [4:0] OP,
  input  [4:0] Funct,
  input  in_3,
  output [3:0] ALU_OP,
  output uret,
  output MemToReg,
  output ecall,
  output MemWrite,
  output ALU_SRC,
  output RegWrite,
  output S_type,
  output Beq,
  output Bne,
  output Jalr,
  output JAL,
  output sb,
  output bge
);

  wire \控制信号自动生成_1_ecall ;

  \运算控制器自动生成  \u_运算控制器自动生成_1  (
    .OP2(OP[0]), .OP3(OP[1]), .OP4(OP[2]), .OP5(OP[3]), .OP6(OP[4]), .F12(Funct[0]), .F13(Funct[1]),
    .F14(Funct[2]), .F25(Funct[3]), .F30(Funct[4]), .S0(ALU_OP[0]), .S1(ALU_OP[1]), .S2(ALU_OP[2]),
    .S3(ALU_OP[3]));
  \控制信号自动生成  \u_控制信号自动生成_1  (
    .OP2(OP[0]), .OP3(OP[1]), .MemToReg(MemToReg), .OP4(OP[2]), .OP5(OP[3]), .OP6(OP[4]), .F12(Funct[0]),
    .F13(Funct[1]), .F14(Funct[2]), .MemWrite(MemWrite), .F25(Funct[3]), .F30(Funct[4]), .ALU_SRC(ALU_SRC),
    .RegWrite(RegWrite), .ecall(\控制信号自动生成_1_ecall ), .S_Type(S_type), .BEQ(Beq), .BNE(Bne), .JALR(Jalr),
    .JAL(JAL), .sb(sb), .bge(bge));
  and and_1 (uret, in_3, \控制信号自动生成_1_ecall );
  and and_2 (ecall, ~in_3, \控制信号自动生成_1_ecall );  // AND_Gate

  // Other names for the same wires on the sheet: IR21 = in_3; OP_CODE[4:0] = OP

  // Notes on the sheet:
  //   运算器控制器，根据指令生成运算器功能选择信号
  //   控制信号生成，产生数据通路需要的其他控制信号
endmodule

// 运算器控制器
module \运算控制器自动生成  (
  input  OP2,
  input  OP3,
  input  OP4,
  input  OP5,
  input  OP6,
  input  F12,
  input  F13,
  input  F14,
  input  F25,
  input  F30,
  output S0,
  output S1,
  output S2,
  output S3
);

  wire and_1_out, and_2_out, and_3_out, and_4_out, and_5_out, and_6_out, and_7_out, and_8_out, and_9_out,
       and_10_out, and_11_out, and_12_out, and_13_out, and_14_out, and_15_out, and_16_out, and_17_out,
       and_18_out, and_19_out, and_20_out, and_21_out, and_22_out, and_23_out, and_24_out, and_25_out,
       and_26_out, and_27_out, and_28_out, and_29_out, and_30_out, and_31_out, and_32_out, and_33_out,
       and_34_out, and_35_out, and_36_out, not_1_out, not_2_out, not_3_out, not_4_out, not_5_out, not_6_out,
       not_7_out, not_8_out, not_9_out, not_10_out, not_11_out, not_12_out, not_13_out, not_14_out,
       not_15_out, not_16_out, not_17_out, not_18_out, not_19_out, not_20_out, not_21_out, not_22_out,
       not_23_out, not_24_out, not_25_out, not_26_out, not_27_out, not_28_out, not_29_out, not_30_out,
       not_31_out, not_32_out, not_33_out, not_34_out, not_35_out, not_36_out, not_37_out, not_38_out,
       not_39_out, not_40_out, not_41_out, not_42_out, not_43_out, not_44_out, not_45_out, not_46_out,
       not_47_out, not_48_out, not_49_out, not_50_out, not_51_out, not_52_out, not_53_out, not_54_out,
       not_55_out, not_56_out, not_57_out, not_58_out, not_59_out, not_60_out, not_61_out, not_62_out,
       not_63_out, not_64_out, not_65_out, not_66_out, not_67_out, not_68_out, not_69_out, not_70_out,
       not_71_out, not_72_out, not_73_out, not_74_out, not_75_out, not_76_out, not_77_out, not_78_out,
       not_79_out, not_80_out, not_81_out, not_82_out, not_83_out, not_84_out, not_85_out, not_86_out,
       not_87_out, not_88_out, not_89_out, not_90_out, not_91_out, not_92_out, not_93_out, not_94_out,
       not_95_out, not_96_out, not_97_out, not_98_out, not_99_out, not_100_out, not_101_out, not_102_out,
       not_103_out, not_104_out, not_105_out, not_106_out, not_107_out, not_108_out, not_109_out,
       not_110_out, not_111_out, not_112_out, not_113_out, not_114_out, not_115_out, not_116_out,
       not_117_out, not_118_out, not_119_out, not_120_out, not_121_out, not_122_out, not_123_out,
       not_124_out, not_125_out, not_126_out, not_127_out, not_128_out, not_129_out, not_130_out,
       not_131_out, not_132_out, not_133_out, not_134_out, not_135_out, not_136_out, not_137_out,
       not_138_out, not_139_out, not_140_out, not_141_out, not_142_out, not_143_out, not_144_out,
       not_145_out, not_146_out, not_147_out, not_148_out, not_149_out, not_150_out, not_151_out,
       not_152_out, not_153_out, not_154_out, not_155_out, not_156_out, not_157_out, not_158_out,
       not_159_out, not_160_out, not_161_out, not_162_out, not_163_out, not_164_out, not_165_out,
       not_166_out, not_167_out, not_168_out, not_169_out, not_170_out, not_171_out, not_172_out,
       not_173_out, not_174_out, not_175_out, not_176_out, not_177_out, not_178_out, not_179_out,
       not_180_out, not_181_out, not_182_out, not_183_out, not_184_out, not_185_out, not_186_out,
       not_187_out, not_188_out, not_189_out, not_190_out, not_191_out, not_192_out, not_193_out,
       not_194_out, not_195_out, not_196_out, not_197_out, not_198_out, not_199_out, not_200_out,
       not_201_out, not_202_out, not_203_out, not_204_out, not_205_out, not_206_out, not_207_out,
       not_208_out, not_209_out, not_210_out, not_211_out, not_212_out, not_213_out, not_214_out, not_215_out;

  not not_1 (not_1_out, F30);
  not not_2 (not_2_out, F25);
  not not_3 (not_3_out, F14);
  not not_4 (not_4_out, F13);
  not not_5 (not_5_out, F12);
  not not_6 (not_6_out, OP6);
  not not_7 (not_7_out, OP3);
  not not_8 (not_8_out, OP2);
  not not_9 (not_9_out, F30);
  not not_10 (not_10_out, F25);
  not not_11 (not_11_out, OP6);
  not not_12 (not_12_out, OP3);
  not not_13 (not_13_out, OP2);
  not not_14 (not_14_out, F30);
  not not_15 (not_15_out, F25);
  not not_16 (not_16_out, F14);
  not not_17 (not_17_out, F12);
  not not_18 (not_18_out, OP6);
  not not_19 (not_19_out, OP3);
  not not_20 (not_20_out, OP2);
  not not_21 (not_21_out, F14);
  not not_22 (not_22_out, F13);
  not not_23 (not_23_out, F12);
  not not_24 (not_24_out, OP6);
  not not_25 (not_25_out, OP5);
  not not_26 (not_26_out, OP3);
  not not_27 (not_27_out, OP2);
  not not_28 (not_28_out, OP6);
  not not_29 (not_29_out, OP5);
  not not_30 (not_30_out, OP3);
  not not_31 (not_31_out, OP2);
  not not_32 (not_32_out, F13);
  not not_33 (not_33_out, F12);
  not not_34 (not_34_out, OP6);
  not not_35 (not_35_out, OP5);
  not not_36 (not_36_out, OP3);
  not not_37 (not_37_out, OP2);
  not not_38 (not_38_out, F14);
  not not_39 (not_39_out, F12);
  not not_40 (not_40_out, OP6);
  not not_41 (not_41_out, OP5);
  not not_42 (not_42_out, OP3);
  not not_43 (not_43_out, OP2);
  not not_44 (not_44_out, F25);
  not not_45 (not_45_out, F13);
  not not_46 (not_46_out, OP6);
  not not_47 (not_47_out, OP5);
  not not_48 (not_48_out, OP3);
  not not_49 (not_49_out, OP2);
  not not_50 (not_50_out, F14);
  not not_51 (not_51_out, F12);
  not not_52 (not_52_out, OP6);
  not not_53 (not_53_out, OP5);
  not not_54 (not_54_out, OP4);
  not not_55 (not_55_out, OP3);
  not not_56 (not_56_out, OP2);
  not not_57 (not_57_out, F14);
  not not_58 (not_58_out, F12);
  not not_59 (not_59_out, OP6);
  not not_60 (not_60_out, OP4);
  not not_61 (not_61_out, OP3);
  not not_62 (not_62_out, OP2);
  not not_63 (not_63_out, F25);
  not not_64 (not_64_out, F13);
  not not_65 (not_65_out, OP6);
  not not_66 (not_66_out, OP3);
  not not_67 (not_67_out, OP2);
  not not_68 (not_68_out, F14);
  not not_69 (not_69_out, F13);
  not not_70 (not_70_out, F12);
  not not_71 (not_71_out, OP6);
  not not_72 (not_72_out, OP4);
  not not_73 (not_73_out, OP3);
  not not_74 (not_74_out, OP2);
  not not_75 (not_75_out, F13);
  not not_76 (not_76_out, OP4);
  not not_77 (not_77_out, OP3);
  not not_78 (not_78_out, OP2);
  not not_79 (not_79_out, F25);
  not not_80 (not_80_out, F14);
  not not_81 (not_81_out, F13);
  not not_82 (not_82_out, F12);
  not not_83 (not_83_out, OP6);
  not not_84 (not_84_out, OP3);
  not not_85 (not_85_out, OP2);
  not not_86 (not_86_out, F30);
  not not_87 (not_87_out, F25);
  not not_88 (not_88_out, OP6);
  not not_89 (not_89_out, OP3);
  not not_90 (not_90_out, OP2);
  not not_91 (not_91_out, F30);
  not not_92 (not_92_out, F25);
  not not_93 (not_93_out, F14);
  not not_94 (not_94_out, F12);
  not not_95 (not_95_out, OP6);
  not not_96 (not_96_out, OP3);
  not not_97 (not_97_out, OP2);
  not not_98 (not_98_out, OP6);
  not not_99 (not_99_out, OP5);
  not not_100 (not_100_out, OP3);
  not not_101 (not_101_out, OP2);
  not not_102 (not_102_out, F14);
  not not_103 (not_103_out, F12);
  not not_104 (not_104_out, OP6);
  not not_105 (not_105_out, OP5);
  not not_106 (not_106_out, OP3);
  not not_107 (not_107_out, OP2);
  not not_108 (not_108_out, F30);
  not not_109 (not_109_out, F25);
  not not_110 (not_110_out, F13);
  not not_111 (not_111_out, OP6);
  not not_112 (not_112_out, OP5);
  not not_113 (not_113_out, OP3);
  not not_114 (not_114_out, OP2);
  not not_115 (not_115_out, F13);
  not not_116 (not_116_out, OP4);
  not not_117 (not_117_out, OP3);
  not not_118 (not_118_out, OP2);
  not not_119 (not_119_out, F30);
  not not_120 (not_120_out, F25);
  not not_121 (not_121_out, F14);
  not not_122 (not_122_out, F13);
  not not_123 (not_123_out, F12);
  not not_124 (not_124_out, OP6);
  not not_125 (not_125_out, OP3);
  not not_126 (not_126_out, OP2);
  not not_127 (not_127_out, F25);
  not not_128 (not_128_out, F14);
  not not_129 (not_129_out, F13);
  not not_130 (not_130_out, F12);
  not not_131 (not_131_out, OP6);
  not not_132 (not_132_out, OP3);
  not not_133 (not_133_out, OP2);
  not not_134 (not_134_out, F30);
  not not_135 (not_135_out, F25);
  not not_136 (not_136_out, OP6);
  not not_137 (not_137_out, OP3);
  not not_138 (not_138_out, OP2);
  not not_139 (not_139_out, F30);
  not not_140 (not_140_out, F25);
  not not_141 (not_141_out, F14);
  not not_142 (not_142_out, OP6);
  not not_143 (not_143_out, OP3);
  not not_144 (not_144_out, OP2);
  not not_145 (not_145_out, F14);
  not not_146 (not_146_out, F13);
  not not_147 (not_147_out, F12);
  not not_148 (not_148_out, OP6);
  not not_149 (not_149_out, OP5);
  not not_150 (not_150_out, OP3);
  not not_151 (not_151_out, OP2);
  not not_152 (not_152_out, OP6);
  not not_153 (not_153_out, OP5);
  not not_154 (not_154_out, OP3);
  not not_155 (not_155_out, OP2);
  not not_156 (not_156_out, F14);
  not not_157 (not_157_out, F12);
  not not_158 (not_158_out, OP6);
  not not_159 (not_159_out, OP5);
  not not_160 (not_160_out, OP4);
  not not_161 (not_161_out, OP3);
  not not_162 (not_162_out, OP2);
  not not_163 (not_163_out, F14);
  not not_164 (not_164_out, F12);
  not not_165 (not_165_out, OP6);
  not not_166 (not_166_out, OP4);
  not not_167 (not_167_out, OP3);
  not not_168 (not_168_out, OP2);
  not not_169 (not_169_out, F14);
  not not_170 (not_170_out, F13);
  not not_171 (not_171_out, F12);
  not not_172 (not_172_out, OP6);
  not not_173 (not_173_out, OP4);
  not not_174 (not_174_out, OP3);
  not not_175 (not_175_out, OP2);
  not not_176 (not_176_out, F30);
  not not_177 (not_177_out, F25);
  not not_178 (not_178_out, F12);
  not not_179 (not_179_out, OP6);
  not not_180 (not_180_out, OP3);
  not not_181 (not_181_out, OP2);
  not not_182 (not_182_out, F30);
  not not_183 (not_183_out, F25);
  not not_184 (not_184_out, F14);
  not not_185 (not_185_out, F12);
  not not_186 (not_186_out, OP6);
  not not_187 (not_187_out, OP3);
  not not_188 (not_188_out, OP2);
  not not_189 (not_189_out, F30);
  not not_190 (not_190_out, F25);
  not not_191 (not_191_out, F14);
  not not_192 (not_192_out, OP6);
  not not_193 (not_193_out, OP3);
  not not_194 (not_194_out, OP2);
  not not_195 (not_195_out, F12);
  not not_196 (not_196_out, OP6);
  not not_197 (not_197_out, OP5);
  not not_198 (not_198_out, OP3);
  not not_199 (not_199_out, OP2);
  not not_200 (not_200_out, F13);
  not not_201 (not_201_out, F12);
  not not_202 (not_202_out, OP6);
  not not_203 (not_203_out, OP5);
  not not_204 (not_204_out, OP3);
  not not_205 (not_205_out, OP2);
  not not_206 (not_206_out, F14);
  not not_207 (not_207_out, F12);
  not not_208 (not_208_out, OP6);
  not not_209 (not_209_out, OP5);
  not not_210 (not_210_out, OP3);
  not not_211 (not_211_out, OP2);
  not not_212 (not_212_out, F13);
  not not_213 (not_213_out, OP4);
  not not_214 (not_214_out, OP3);
  not not_215 (not_215_out, OP2);
  and and_1 (and_1_out, not_1_out, not_2_out, not_3_out, not_4_out, not_5_out, not_6_out, OP5, OP4, not_7_out, not_8_out);
  and and_2 (and_2_out, not_9_out, not_10_out, F14, F13, F12, not_11_out, OP5, OP4, not_12_out, not_13_out);
  and and_3 (and_3_out, not_14_out, not_15_out, not_16_out, F13, not_17_out, not_18_out, OP5, OP4, not_19_out, not_20_out);
  and and_4 (and_4_out, not_21_out, not_22_out, not_23_out, not_24_out, not_25_out, OP4, not_26_out, not_27_out);
  and and_5 (and_5_out, F14, F13, F12, not_28_out, not_29_out, OP4, not_30_out, not_31_out);
  and and_6 (and_6_out, F14, not_32_out, not_33_out, not_34_out, not_35_out, OP4, not_36_out, not_37_out);
  and and_7 (and_7_out, not_38_out, F13, not_39_out, not_40_out, not_41_out, OP4, not_42_out, not_43_out);
  and and_8 (and_8_out, F30, not_44_out, F14, not_45_out, F12, not_46_out, not_47_out, OP4, not_48_out, not_49_out);
  and and_9 (and_9_out, not_50_out, F13, not_51_out, not_52_out, not_53_out, not_54_out, not_55_out, not_56_out);
  and and_10 (and_10_out, not_57_out, F13, not_58_out, not_59_out, OP5, not_60_out, not_61_out, not_62_out);
  and and_11 (and_11_out, F30, not_63_out, F14, not_64_out, F12, not_65_out, OP5, OP4, not_66_out, not_67_out);
  and and_12 (and_12_out, not_68_out, not_69_out, not_70_out, not_71_out, OP5, not_72_out, not_73_out, not_74_out);
  and and_13 (and_13_out, F14, not_75_out, F12, OP6, OP5, not_76_out, not_77_out, not_78_out);
  and and_14 (and_14_out, F30, not_79_out, not_80_out, not_81_out, not_82_out, not_83_out, OP5, OP4, not_84_out, not_85_out);
  and and_15 (and_15_out, not_86_out, not_87_out, F14, F13, F12, not_88_out, OP5, OP4, not_89_out, not_90_out);
  and and_16 (and_16_out, not_91_out, not_92_out, not_93_out, F13, not_94_out, not_95_out, OP5, OP4, not_96_out, not_97_out);
  and and_17 (and_17_out, F14, F13, F12, not_98_out, not_99_out, OP4, not_100_out, not_101_out);
  and and_18 (and_18_out, not_102_out, F13, not_103_out, not_104_out, not_105_out, OP4, not_106_out, not_107_out);
  and and_19 (and_19_out, not_108_out, not_109_out, F14, not_110_out, F12, not_111_out, not_112_out, OP4, not_113_out, not_114_out);
  and and_20 (and_20_out, F14, not_115_out, F12, OP6, OP5, not_116_out, not_117_out, not_118_out);
  and and_21 (and_21_out, not_119_out, not_120_out, not_121_out, not_122_out, not_123_out, not_124_out, OP5, OP4, not_125_out, not_126_out);
  and and_22 (and_22_out, F30, not_127_out, not_128_out, not_129_out, not_130_out, not_131_out, OP5, OP4, not_132_out, not_133_out);
  and and_23 (and_23_out, not_134_out, not_135_out, F14, F13, F12, not_136_out, OP5, OP4, not_137_out, not_138_out);
  and and_24 (and_24_out, not_139_out, not_140_out, not_141_out, F13, F12, not_142_out, OP5, OP4, not_143_out, not_144_out);
  and and_25 (and_25_out, not_145_out, not_146_out, not_147_out, not_148_out, not_149_out, OP4, not_150_out, not_151_out);
  and and_26 (and_26_out, F14, F13, F12, not_152_out, not_153_out, OP4, not_154_out, not_155_out);
  and and_27 (and_27_out, not_156_out, F13, not_157_out, not_158_out, not_159_out, not_160_out, not_161_out, not_162_out);
  and and_28 (and_28_out, not_163_out, F13, not_164_out, not_165_out, OP5, not_166_out, not_167_out, not_168_out);
  and and_29 (and_29_out, not_169_out, not_170_out, not_171_out, not_172_out, OP5, not_173_out, not_174_out, not_175_out);
  and and_30 (and_30_out, not_176_out, not_177_out, F14, F13, not_178_out, not_179_out, OP5, OP4, not_180_out, not_181_out);
  and and_31 (and_31_out, not_182_out, not_183_out, not_184_out, F13, not_185_out, not_186_out, OP5, OP4, not_187_out, not_188_out);
  and and_32 (and_32_out, not_189_out, not_190_out, not_191_out, F13, F12, not_192_out, OP5, OP4, not_193_out, not_194_out);
  and and_33 (and_33_out, F14, F13, not_195_out, not_196_out, not_197_out, OP4, not_198_out, not_199_out);
  and and_34 (and_34_out, F14, not_200_out, not_201_out, not_202_out, not_203_out, OP4, not_204_out, not_205_out);
  and and_35 (and_35_out, not_206_out, F13, not_207_out, not_208_out, not_209_out, OP4, not_210_out, not_211_out);
  and and_36 (and_36_out, F14, not_212_out, F12, OP6, OP5, not_213_out, not_214_out, not_215_out);
  or or_1 (S0, and_1_out, and_2_out, and_3_out, and_4_out, and_5_out, and_6_out, and_7_out, and_8_out, and_9_out, and_10_out, and_11_out, and_12_out, and_13_out);
  or or_2 (S1, and_14_out, and_15_out, and_16_out, and_17_out, and_18_out, and_19_out, and_20_out);
  or or_3 (S2, and_21_out, and_22_out, and_23_out, and_24_out, and_25_out, and_26_out, and_27_out, and_28_out, and_29_out);
  or or_4 (S3, and_30_out, and_31_out, and_32_out, and_33_out, and_34_out, and_35_out, and_36_out);
endmodule

// 控制信号生成
module \控制信号自动生成  (
  input  OP2,
  input  OP3,
  input  OP4,
  input  OP5,
  input  OP6,
  input  F12,
  input  F13,
  input  F14,
  input  F25,
  input  F30,
  output MemToReg,
  output MemWrite,
  output ALU_SRC,
  output RegWrite,
  output ecall,
  output S_Type,
  output BEQ,
  output BNE,
  output JALR,
  output JAL,
  output sb,
  output bge
);

  wire and_2_out, and_3_out, and_4_out, and_5_out, and_6_out, and_7_out, and_8_out, and_9_out, and_10_out,
       and_11_out, and_12_out, and_13_out, and_14_out, and_15_out, and_16_out, and_17_out, and_18_out,
       and_19_out, and_20_out, and_21_out, and_22_out, and_23_out, and_24_out, and_25_out, and_26_out,
       and_27_out, and_28_out, and_29_out, and_30_out, and_31_out, and_32_out, and_33_out, and_35_out,
       and_36_out, not_1_out, not_2_out, not_3_out, not_4_out, not_5_out, not_6_out, not_7_out, not_8_out,
       not_9_out, not_10_out, not_11_out, not_12_out, not_13_out, not_14_out, not_15_out, not_16_out,
       not_17_out, not_18_out, not_19_out, not_20_out, not_21_out, not_22_out, not_23_out, not_24_out,
       not_25_out, not_26_out, not_27_out, not_28_out, not_29_out, not_30_out, not_31_out, not_32_out,
       not_33_out, not_34_out, not_35_out, not_36_out, not_37_out, not_38_out, not_39_out, not_40_out,
       not_41_out, not_42_out, not_43_out, not_44_out, not_45_out, not_46_out, not_47_out, not_48_out,
       not_49_out, not_50_out, not_51_out, not_52_out, not_53_out, not_54_out, not_55_out, not_56_out,
       not_57_out, not_58_out, not_59_out, not_60_out, not_61_out, not_62_out, not_63_out, not_64_out,
       not_65_out, not_66_out, not_67_out, not_68_out, not_69_out, not_70_out, not_71_out, not_72_out,
       not_73_out, not_74_out, not_75_out, not_76_out, not_77_out, not_78_out, not_79_out, not_80_out,
       not_81_out, not_82_out, not_83_out, not_84_out, not_85_out, not_86_out, not_87_out, not_88_out,
       not_89_out, not_90_out, not_91_out, not_92_out, not_93_out, not_94_out, not_95_out, not_96_out,
       not_97_out, not_98_out, not_99_out, not_100_out, not_101_out, not_102_out, not_103_out, not_104_out,
       not_105_out, not_106_out, not_107_out, not_108_out, not_109_out, not_110_out, not_111_out,
       not_112_out, not_113_out, not_114_out, not_115_out, not_116_out, not_117_out, not_118_out,
       not_119_out, not_120_out, not_121_out, not_122_out, not_123_out, not_124_out, not_125_out,
       not_126_out, not_127_out, not_128_out, not_129_out, not_130_out, not_131_out, not_132_out,
       not_133_out, not_134_out, not_135_out, not_136_out, not_137_out, not_138_out, not_139_out,
       not_140_out, not_141_out, not_142_out, not_143_out, not_144_out, not_145_out, not_146_out,
       not_147_out, not_148_out, not_149_out, not_150_out, not_151_out, not_152_out, not_153_out,
       not_154_out, not_155_out, not_156_out, not_157_out, not_158_out, not_159_out, not_160_out,
       not_161_out, not_162_out, not_163_out, not_164_out, not_165_out, not_166_out, not_167_out,
       not_168_out, not_169_out, not_170_out, not_171_out, not_172_out, not_173_out, not_174_out,
       not_175_out, not_176_out, not_177_out, not_178_out, not_179_out, not_180_out, not_181_out,
       not_182_out, not_183_out, not_184_out, not_185_out, not_186_out, not_187_out, not_188_out,
       not_189_out, not_190_out, not_191_out, not_192_out, not_193_out, not_194_out, not_195_out,
       not_196_out, not_197_out, not_198_out, not_199_out, not_200_out, not_201_out, not_202_out,
       not_203_out, not_204_out, not_205_out, not_206_out, not_207_out, not_208_out, not_209_out,
       not_210_out, not_211_out, not_212_out, not_213_out, not_214_out, not_215_out, not_216_out,
       not_217_out, not_218_out, not_219_out, not_220_out, not_221_out, not_222_out, not_223_out,
       not_224_out, not_225_out, not_226_out, not_227_out, not_228_out, not_229_out, not_230_out,
       not_231_out, not_232_out, not_233_out, not_234_out, not_235_out, not_236_out, not_237_out,
       not_238_out, not_239_out, not_240_out, not_241_out, not_242_out, not_243_out, not_244_out,
       not_245_out, not_246_out, not_247_out, not_248_out, not_249_out, not_250_out;

  not not_1 (not_1_out, F14);
  not not_2 (not_2_out, F12);
  not not_3 (not_3_out, OP6);
  not not_4 (not_4_out, OP5);
  not not_5 (not_5_out, OP4);
  not not_6 (not_6_out, OP3);
  not not_7 (not_7_out, OP2);
  not not_8 (not_8_out, F14);
  not not_9 (not_9_out, F12);
  not not_10 (not_10_out, OP6);
  not not_11 (not_11_out, OP4);
  not not_12 (not_12_out, OP3);
  not not_13 (not_13_out, OP2);
  not not_14 (not_14_out, F14);
  not not_15 (not_15_out, F13);
  not not_16 (not_16_out, F12);
  not not_17 (not_17_out, OP6);
  not not_18 (not_18_out, OP4);
  not not_19 (not_19_out, OP3);
  not not_20 (not_20_out, OP2);
  not not_21 (not_21_out, F14);
  not not_22 (not_22_out, F13);
  not not_23 (not_23_out, F12);
  not not_24 (not_24_out, OP6);
  not not_25 (not_25_out, OP5);
  not not_26 (not_26_out, OP3);
  not not_27 (not_27_out, OP2);
  not not_28 (not_28_out, OP6);
  not not_29 (not_29_out, OP5);
  not not_30 (not_30_out, OP3);
  not not_31 (not_31_out, OP2);
  not not_32 (not_32_out, F12);
  not not_33 (not_33_out, OP6);
  not not_34 (not_34_out, OP5);
  not not_35 (not_35_out, OP3);
  not not_36 (not_36_out, OP2);
  not not_37 (not_37_out, F13);
  not not_38 (not_38_out, F12);
  not not_39 (not_39_out, OP6);
  not not_40 (not_40_out, OP5);
  not not_41 (not_41_out, OP3);
  not not_42 (not_42_out, OP2);
  not not_43 (not_43_out, F14);
  not not_44 (not_44_out, F12);
  not not_45 (not_45_out, OP6);
  not not_46 (not_46_out, OP5);
  not not_47 (not_47_out, OP3);
  not not_48 (not_48_out, OP2);
  not not_49 (not_49_out, F30);
  not not_50 (not_50_out, F25);
  not not_51 (not_51_out, F14);
  not not_52 (not_52_out, F13);
  not not_53 (not_53_out, OP6);
  not not_54 (not_54_out, OP5);
  not not_55 (not_55_out, OP3);
  not not_56 (not_56_out, OP2);
  not not_57 (not_57_out, F30);
  not not_58 (not_58_out, F25);
  not not_59 (not_59_out, F13);
  not not_60 (not_60_out, OP6);
  not not_61 (not_61_out, OP5);
  not not_62 (not_62_out, OP3);
  not not_63 (not_63_out, OP2);
  not not_64 (not_64_out, F25);
  not not_65 (not_65_out, F13);
  not not_66 (not_66_out, OP6);
  not not_67 (not_67_out, OP5);
  not not_68 (not_68_out, OP3);
  not not_69 (not_69_out, OP2);
  not not_70 (not_70_out, F14);
  not not_71 (not_71_out, F12);
  not not_72 (not_72_out, OP6);
  not not_73 (not_73_out, OP5);
  not not_74 (not_74_out, OP4);
  not not_75 (not_75_out, OP3);
  not not_76 (not_76_out, OP2);
  not not_77 (not_77_out, F14);
  not not_78 (not_78_out, F12);
  not not_79 (not_79_out, OP6);
  not not_80 (not_80_out, OP4);
  not not_81 (not_81_out, OP3);
  not not_82 (not_82_out, OP2);
  not not_83 (not_83_out, F14);
  not not_84 (not_84_out, F13);
  not not_85 (not_85_out, F12);
  not not_86 (not_86_out, OP6);
  not not_87 (not_87_out, OP4);
  not not_88 (not_88_out, OP3);
  not not_89 (not_89_out, OP2);
  not not_90 (not_90_out, F30);
  not not_91 (not_91_out, F25);
  not not_92 (not_92_out, F14);
  not not_93 (not_93_out, F13);
  not not_94 (not_94_out, F12);
  not not_95 (not_95_out, OP6);
  not not_96 (not_96_out, OP3);
  not not_97 (not_97_out, OP2);
  not not_98 (not_98_out, F25);
  not not_99 (not_99_out, F14);
  not not_100 (not_100_out, F13);
  not not_101 (not_101_out, F12);
  not not_102 (not_102_out, OP6);
  not not_103 (not_103_out, OP3);
  not not_104 (not_104_out, OP2);
  not not_105 (not_105_out, F30);
  not not_106 (not_106_out, F25);
  not not_107 (not_107_out, OP6);
  not not_108 (not_108_out, OP3);
  not not_109 (not_109_out, OP2);
  not not_110 (not_110_out, F30);
  not not_111 (not_111_out, F25);
  not not_112 (not_112_out, F12);
  not not_113 (not_113_out, OP6);
  not not_114 (not_114_out, OP3);
  not not_115 (not_115_out, OP2);
  not not_116 (not_116_out, F30);
  not not_117 (not_117_out, F25);
  not not_118 (not_118_out, F14);
  not not_119 (not_119_out, F12);
  not not_120 (not_120_out, OP6);
  not not_121 (not_121_out, OP3);
  not not_122 (not_122_out, OP2);
  not not_123 (not_123_out, F30);
  not not_124 (not_124_out, F25);
  not not_125 (not_125_out, F14);
  not not_126 (not_126_out, OP6);
  not not_127 (not_127_out, OP3);
  not not_128 (not_128_out, OP2);
  not not_129 (not_129_out, F14);
  not not_130 (not_130_out, F13);
  not not_131 (not_131_out, F12);
  not not_132 (not_132_out, OP6);
  not not_133 (not_133_out, OP5);
  not not_134 (not_134_out, OP3);
  not not_135 (not_135_out, OP2);
  not not_136 (not_136_out, OP6);
  not not_137 (not_137_out, OP5);
  not not_138 (not_138_out, OP3);
  not not_139 (not_139_out, OP2);
  not not_140 (not_140_out, F12);
  not not_141 (not_141_out, OP6);
  not not_142 (not_142_out, OP5);
  not not_143 (not_143_out, OP3);
  not not_144 (not_144_out, OP2);
  not not_145 (not_145_out, F13);
  not not_146 (not_146_out, F12);
  not not_147 (not_147_out, OP6);
  not not_148 (not_148_out, OP5);
  not not_149 (not_149_out, OP3);
  not not_150 (not_150_out, OP2);
  not not_151 (not_151_out, F14);
  not not_152 (not_152_out, F12);
  not not_153 (not_153_out, OP6);
  not not_154 (not_154_out, OP5);
  not not_155 (not_155_out, OP3);
  not not_156 (not_156_out, OP2);
  not not_157 (not_157_out, F30);
  not not_158 (not_158_out, F25);
  not not_159 (not_159_out, F14);
  not not_160 (not_160_out, F13);
  not not_161 (not_161_out, OP6);
  not not_162 (not_162_out, OP5);
  not not_163 (not_163_out, OP3);
  not not_164 (not_164_out, OP2);
  not not_165 (not_165_out, F30);
  not not_166 (not_166_out, F25);
  not not_167 (not_167_out, F13);
  not not_168 (not_168_out, OP6);
  not not_169 (not_169_out, OP5);
  not not_170 (not_170_out, OP3);
  not not_171 (not_171_out, OP2);
  not not_172 (not_172_out, F25);
  not not_173 (not_173_out, F13);
  not not_174 (not_174_out, OP6);
  not not_175 (not_175_out, OP5);
  not not_176 (not_176_out, OP3);
  not not_177 (not_177_out, OP2);
  not not_178 (not_178_out, F14);
  not not_179 (not_179_out, F12);
  not not_180 (not_180_out, OP6);
  not not_181 (not_181_out, OP5);
  not not_182 (not_182_out, OP4);
  not not_183 (not_183_out, OP3);
  not not_184 (not_184_out, OP2);
  not not_185 (not_185_out, OP4);
  not not_186 (not_186_out, F14);
  not not_187 (not_187_out, F13);
  not not_188 (not_188_out, F12);
  not not_189 (not_189_out, OP4);
  not not_190 (not_190_out, OP3);
  not not_191 (not_191_out, F30);
  not not_192 (not_192_out, F25);
  not not_193 (not_193_out, F14);
  not not_194 (not_194_out, F13);
  not not_195 (not_195_out, OP6);
  not not_196 (not_196_out, OP3);
  not not_197 (not_197_out, OP2);
  not not_198 (not_198_out, F25);
  not not_199 (not_199_out, F13);
  not not_200 (not_200_out, OP6);
  not not_201 (not_201_out, OP3);
  not not_202 (not_202_out, OP2);
  not not_203 (not_203_out, F30);
  not not_204 (not_204_out, F25);
  not not_205 (not_205_out, F14);
  not not_206 (not_206_out, F13);
  not not_207 (not_207_out, F12);
  not not_208 (not_208_out, OP3);
  not not_209 (not_209_out, OP2);
  not not_210 (not_210_out, F14);
  not not_211 (not_211_out, F12);
  not not_212 (not_212_out, OP6);
  not not_213 (not_213_out, OP4);
  not not_214 (not_214_out, OP3);
  not not_215 (not_215_out, OP2);
  not not_216 (not_216_out, F14);
  not not_217 (not_217_out, F13);
  not not_218 (not_218_out, F12);
  not not_219 (not_219_out, OP6);
  not not_220 (not_220_out, OP4);
  not not_221 (not_221_out, OP3);
  not not_222 (not_222_out, OP2);
  not not_223 (not_223_out, F14);
  not not_224 (not_224_out, F13);
  not not_225 (not_225_out, F12);
  not not_226 (not_226_out, OP4);
  not not_227 (not_227_out, OP3);
  not not_228 (not_228_out, OP2);
  not not_229 (not_229_out, F14);
  not not_230 (not_230_out, F13);
  not not_231 (not_231_out, OP4);
  not not_232 (not_232_out, OP3);
  not not_233 (not_233_out, OP2);
  not not_234 (not_234_out, F14);
  not not_235 (not_235_out, F13);
  not not_236 (not_236_out, F12);
  not not_237 (not_237_out, OP4);
  not not_238 (not_238_out, OP3);
  not not_239 (not_239_out, OP4);
  not not_240 (not_240_out, F14);
  not not_241 (not_241_out, F13);
  not not_242 (not_242_out, F12);
  not not_243 (not_243_out, OP6);
  not not_244 (not_244_out, OP4);
  not not_245 (not_245_out, OP3);
  not not_246 (not_246_out, OP2);
  not not_247 (not_247_out, F13);
  not not_248 (not_248_out, OP4);
  not not_249 (not_249_out, OP3);
  not not_250 (not_250_out, OP2);
  and and_1 (MemToReg, not_1_out, F13, not_2_out, not_3_out, not_4_out, not_5_out, not_6_out, not_7_out);
  and and_2 (and_2_out, not_8_out, F13, not_9_out, not_10_out, OP5, not_11_out, not_12_out, not_13_out);
  and and_3 (and_3_out, not_14_out, not_15_out, not_16_out, not_17_out, OP5, not_18_out, not_19_out, not_20_out);
  and and_4 (and_4_out, not_21_out, not_22_out, not_23_out, not_24_out, not_25_out, OP4, not_26_out, not_27_out);
  and and_5 (and_5_out, F14, F13, F12, not_28_out, not_29_out, OP4, not_30_out, not_31_out);
  and and_6 (and_6_out, F14, F13, not_32_out, not_33_out, not_34_out, OP4, not_35_out, not_36_out);
  and and_7 (and_7_out, F14, not_37_out, not_38_out, not_39_out, not_40_out, OP4, not_41_out, not_42_out);
  and and_8 (and_8_out, not_43_out, F13, not_44_out, not_45_out, not_46_out, OP4, not_47_out, not_48_out);
  and and_9 (and_9_out, not_49_out, not_50_out, not_51_out, not_52_out, F12, not_53_out, not_54_out, OP4, not_55_out, not_56_out);
  and and_10 (and_10_out, not_57_out, not_58_out, F14, not_59_out, F12, not_60_out, not_61_out, OP4, not_62_out, not_63_out);
  and and_11 (and_11_out, F30, not_64_out, F14, not_65_out, F12, not_66_out, not_67_out, OP4, not_68_out, not_69_out);
  and and_12 (and_12_out, not_70_out, F13, not_71_out, not_72_out, not_73_out, not_74_out, not_75_out, not_76_out);
  and and_13 (and_13_out, not_77_out, F13, not_78_out, not_79_out, OP5, not_80_out, not_81_out, not_82_out);
  and and_14 (and_14_out, not_83_out, not_84_out, not_85_out, not_86_out, OP5, not_87_out, not_88_out, not_89_out);
  and and_15 (and_15_out, not_90_out, not_91_out, not_92_out, not_93_out, not_94_out, not_95_out, OP5, OP4, not_96_out, not_97_out);
  and and_16 (and_16_out, F30, not_98_out, not_99_out, not_100_out, not_101_out, not_102_out, OP5, OP4, not_103_out, not_104_out);
  and and_17 (and_17_out, not_105_out, not_106_out, F14, F13, F12, not_107_out, OP5, OP4, not_108_out, not_109_out);
  and and_18 (and_18_out, not_110_out, not_111_out, F14, F13, not_112_out, not_113_out, OP5, OP4, not_114_out, not_115_out);
  and and_19 (and_19_out, not_116_out, not_117_out, not_118_out, F13, not_119_out, not_120_out, OP5, OP4, not_121_out, not_122_out);
  and and_20 (and_20_out, not_123_out, not_124_out, not_125_out, F13, F12, not_126_out, OP5, OP4, not_127_out, not_128_out);
  and and_21 (and_21_out, not_129_out, not_130_out, not_131_out, not_132_out, not_133_out, OP4, not_134_out, not_135_out);
  and and_22 (and_22_out, F14, F13, F12, not_136_out, not_137_out, OP4, not_138_out, not_139_out);
  and and_23 (and_23_out, F14, F13, not_140_out, not_141_out, not_142_out, OP4, not_143_out, not_144_out);
  and and_24 (and_24_out, F14, not_145_out, not_146_out, not_147_out, not_148_out, OP4, not_149_out, not_150_out);
  and and_25 (and_25_out, not_151_out, F13, not_152_out, not_153_out, not_154_out, OP4, not_155_out, not_156_out);
  and and_26 (and_26_out, not_157_out, not_158_out, not_159_out, not_160_out, F12, not_161_out, not_162_out, OP4, not_163_out, not_164_out);
  and and_27 (and_27_out, not_165_out, not_166_out, F14, not_167_out, F12, not_168_out, not_169_out, OP4, not_170_out, not_171_out);
  and and_28 (and_28_out, F30, not_172_out, F14, not_173_out, F12, not_174_out, not_175_out, OP4, not_176_out, not_177_out);
  and and_29 (and_29_out, not_178_out, F13, not_179_out, not_180_out, not_181_out, not_182_out, not_183_out, not_184_out);
  and and_30 (and_30_out, OP6, OP5, not_185_out, OP3, OP2);
  and and_31 (and_31_out, not_186_out, not_187_out, not_188_out, OP6, OP5, not_189_out, not_190_out, OP2);
  and and_32 (and_32_out, not_191_out, not_192_out, not_193_out, not_194_out, F12, not_195_out, OP5, OP4, not_196_out, not_197_out);
  and and_33 (and_33_out, F30, not_198_out, F14, not_199_out, F12, not_200_out, OP5, OP4, not_201_out, not_202_out);
  and and_34 (ecall, not_203_out, not_204_out, not_205_out, not_206_out, not_207_out, OP6, OP5, OP4, not_208_out, not_209_out);
  and and_35 (and_35_out, not_210_out, F13, not_211_out, not_212_out, OP5, not_213_out, not_214_out, not_215_out);
  and and_36 (and_36_out, not_216_out, not_217_out, not_218_out, not_219_out, OP5, not_220_out, not_221_out, not_222_out);
  and and_37 (BEQ, not_223_out, not_224_out, not_225_out, OP6, OP5, not_226_out, not_227_out, not_228_out);
  and and_38 (BNE, not_229_out, not_230_out, F12, OP6, OP5, not_231_out, not_232_out, not_233_out);
  and and_39 (JALR, not_234_out, not_235_out, not_236_out, OP6, OP5, not_237_out, not_238_out, OP2);
  and and_40 (JAL, OP6, OP5, not_239_out, OP3, OP2);
  and and_41 (sb, not_240_out, not_241_out, not_242_out, not_243_out, OP5, not_244_out, not_245_out, not_246_out);
  and and_42 (bge, F14, not_247_out, F12, OP6, OP5, not_248_out, not_249_out, not_250_out);
  or or_1 (MemWrite, and_2_out, and_3_out);
  or or_2 (S_Type, and_35_out, and_36_out);
  or or_3 (ALU_SRC, and_4_out, and_5_out, and_6_out, and_7_out, and_8_out, and_9_out, and_10_out, and_11_out, and_12_out, and_13_out, and_14_out);
  or or_4 (RegWrite, and_15_out, and_16_out, and_17_out, and_18_out, and_19_out, and_20_out, and_21_out, and_22_out, and_23_out, and_24_out, and_25_out, and_26_out, and_27_out, and_28_out, and_29_out, and_30_out, and_31_out, and_32_out, and_33_out);
endmodule

// ALU
module ALU (
  input  [31:0] X,
  input  [31:0] Y,
  input  [3:0] AluOP,
  output out_4,
  output Equal,
  output out_6,
  output [31:0] Result,
  output [31:0] Result_2
);

  wire [0:0] comparator_1_lt, comparator_2_lt;
  wire [31:0] adder_1_out, AND_out, divider_1_out, divider_1_rem, multiplier_1_cout, multiplier_1_out,
       NOR_out, OR_out, shifter_1_out, shifter_2_out, shifter_3_out, subtractor_1_out, XOR_out;

  assign AND_out = X & Y;  // AND_Gate AND, 32 bits wide
  assign OR_out = X | Y;  // OR_Gate OR, 32 bits wide
  Shifter #(.width(32), .shift("ll")) shifter_1 (.in(X), .\dist (Y[4:0]), .out(shifter_1_out));
  Shifter #(.width(32), .shift("ar")) shifter_2 (.in(X), .\dist (Y[4:0]), .out(shifter_2_out));
  Shifter #(.width(32), .shift("lr")) shifter_3 (.in(X), .\dist (Y[4:0]), .out(shifter_3_out));
  Multiplier #(.width(32)) multiplier_1 (.a(X), .b(Y), .out(multiplier_1_out), .cout(multiplier_1_cout));  // open: cin
  Divider #(.width(32)) divider_1 (.a(X), .b(Y), .out(divider_1_out), .rem(divider_1_rem));  // open: upper
  Adder #(.width(32)) adder_1 (.a(X), .b(Y), .out(adder_1_out));  // open: cin, cout
  Subtractor #(.width(32)) subtractor_1 (.a(X), .b(Y), .out(subtractor_1_out));  // open: bin, bout
  assign XOR_out = X ^ Y;  // XOR_Gate XOR, 32 bits wide
  assign NOR_out = ~(X | Y);  // NOR_Gate NOR, 32 bits wide
  Comparator #(.width(32), .mode("twosComplement")) comparator_1 (
    .a(X), .b(Y), .eq(Equal), .lt(comparator_1_lt[0]));  // open: gt
  Comparator #(.width(32), .mode("unsigned")) comparator_2 (.a(X), .b(Y), .lt(comparator_2_lt[0]));  // open: gt, eq
  Multiplexer #(.select(4), .width(32), .disabled("Z"), .enable("false")) multiplexer_1 (
    .in0(shifter_1_out), .in1(shifter_2_out), .in2(shifter_3_out), .in3(multiplier_1_out),
    .in4(divider_1_out), .in5(adder_1_out), .in6(subtractor_1_out), .in7(AND_out), .in8(OR_out),
    .in9(XOR_out), .in10(NOR_out), .in11({{31{1'b0}}, comparator_1_lt[0]}),
    .in12({{31{1'b0}}, comparator_2_lt[0]}), .in13({32{1'b0}}), .in14({32{1'b0}}), .in15({32{1'b0}}),
    .out(Result), .sel(AluOP));
  Multiplexer #(.select(4), .width(32), .disabled("Z"), .enable("false")) multiplexer_2 (
    .in0({32{1'b0}}), .in1({32{1'b0}}), .in2({32{1'b0}}), .in3(multiplier_1_cout), .in4(divider_1_rem),
    .in5({32{1'b0}}), .in6({32{1'b0}}), .in7({32{1'b0}}), .in8({32{1'b0}}), .in9({32{1'b0}}),
    .in10({32{1'b0}}), .in11({32{1'b0}}), .in12({32{1'b0}}), .in13({32{1'b0}}), .in14({32{1'b0}}),
    .in15({32{1'b0}}), .out(Result_2), .sel(AluOP));
  Multiplexer #(.select(4), .width(1), .disabled("Z"), .enable("false")) multiplexer_3 (
    .in0(1'b0), .in1(1'b0), .in2(1'b0), .in3(1'b0), .in4(1'b0), .in5(1'b0), .in6(1'b0), .in7(1'b0),
    .in8(1'b0), .in9(1'b0), .in10(1'b0), .in11(comparator_1_lt[0]), .in12(comparator_2_lt[0]), .in13(1'b0),
    .in14(1'b0), .in15(1'b0), .out(out_6), .sel(AluOP));
  not not_1 (out_4, out_6);

  // Other names for the same wires on the sheet: Result2[31:0] = Result_2; S[3:0] = AluOP; tunnel = out_6;
  //   tunnel_t = out_4

  // Notes on the sheet:
  //   不要改变此引脚区域内容，也不要改变ALU封装形式
  //   输入引脚
  //   输出引脚
endmodule

module Regifile (
  input  [31:0] Din,
  input  Clk,
  input  WE,
  input  [4:0] R1_num,
  input  [4:0] W_num,
  input  [4:0] R2_num,
  output [31:0] R1,
  output [31:0] R2
);

  // RegisterFile registerfile_1: pin names not known; wires that end beside it: Din, Clk, WE, W_num, R1_num, R2_num, R1, R2
endmodule

module \理想流水线  (
  output RegWrite,
  output MemWrite,
  output [31:0] IF_PC,
  output [31:0] ID_PC,
  output [31:0] EX_PC,
  output [31:0] M_PC,
  output [31:0] WB_PC,
  output [31:0] RDin,
  output [31:0] MDin,
  output [31:0] LedData
);

  wire and_1_out, and_2_out, CLK, clock_1_out, comparator_1_eq, comparator_1_lt, comparator_2_eq, d_ff_1_q,
       Go, halt, ID_ecall, IR1, IR2, IR3, nand_1_out, not_1_out, not_2_out, or_1_out, RST, W1, W2, W3,
       WB_ecall, \单周期硬布线控制器_1_p4 , \单周期硬布线控制器_1_p7 , \单周期硬布线控制器_1_p8 , \单周期硬布线控制器_1_p10 , \单周期硬布线控制器_1_p11 ,
       \单周期硬布线控制器_1_p12 , \理想流水寄存器_2_alu_src_out , \理想流水寄存器_2_ecall_out , \理想流水寄存器_2_memtoreg_out ,
       \理想流水寄存器_2_memwrite_out , \理想流水寄存器_2_regwrite_out , \理想流水寄存器_3_ecall_out , \理想流水寄存器_3_memtoreg_out ,
       \理想流水寄存器_3_regwrite_out , \理想流水寄存器_4_memtoreg_out ;
  wire [3:0] \单周期硬布线控制器_1_p9 , \理想流水寄存器_2_alu_op_out ;
  wire [4:0] multiplexer_1_out, multiplexer_2_out, \理想流水寄存器_2_writereg__out , \理想流水寄存器_3_writereg__out ,
       \理想流水寄存器_4_writereg__out ;
  wire [11:0] multiplexer_3_out;
  wire [12:0] CNT_num;
  wire [15:0] \LoadUse次数 , \总周期数 , \插入气泡数 , \无条件分支数 , \条件分支成功数 ;
  wire [31:0] alu_1_result, EX_IR, ID_Imm, ID_IR, ID_R1, ID_R2, IF_IR, mem_addr, MEM_IR, mem_ld,
       multiplexer_4_out, PC_4, WB_IR, WB_R1, WB_R2, \理想流水寄存器_2_imm_out , \理想流水寄存器_2_r1_out ,
       \理想流水寄存器_2_r2_out , \理想流水寄存器_3_r1_out , \理想流水寄存器_4_alu_out , \理想流水寄存器_4_memdata_out ;

  Button \u_总复位  (.out(RST));
  Button _1 (.out(IR1));
  Button _2 (.out(IR2));
  Button _3 (.out(IR3));
  // Probe on \总周期数 
  // Probe on \总周期数 
  not not_1 (not_1_out, halt);
  Button \u_继续运行  (.out(Go));
  LED #(.active("true")) led_1 (.in(W1));
  LED #(.active("true")) led_2 (.in(W2));
  LED #(.active("true")) led_3 (.in(W3));
  not not_2 (not_2_out, halt);
  Register #(.width(32), .trigger("rising"), .Select("low")) PC (
    .D(PC_4), .en(not_1_out), .Q(IF_PC), .clk(CLK), .clr(RST));
  Hex_Digit_Display hex_digit_display_1 (.value(LedData[31:28]));  // open: dp
  // Probe on IF_PC[19:0]
  // RiscV_Probe riscv_probe_1: pin names not known; wires that end beside it: IF_IR
  Counter #(.width(16), .max('hffff), .ongoal("wrap"), .trigger("rising"), .behavior("old")) counter_1 (
    .count(not_2_out), .Q(\总周期数 ), .clk(CLK));  // open: load, D, carry, clr, preset
  Adder #(.width(32)) adder_1 (.a(IF_PC), .b(32'h4), .out(PC_4));  // open: cin, cout
  Hex_Digit_Display hex_digit_display_2 (.value(LedData[23:20]));  // open: dp
  Hex_Digit_Display hex_digit_display_3 (.value(LedData[27:24]));  // open: dp
  // Probe on ID_PC[19:0]
  // RiscV_Probe riscv_probe_2: pin names not known; wires that end beside it: ID_IR
  ROM #(.addrWidth(10), .dataWidth(32), .Select("high")) rom_1 (.addr(IF_PC[11:2]), .data(IF_IR));
  Hex_Digit_Display hex_digit_display_4 (.value(LedData[19:16]));  // open: dp
  Hex_Digit_Display hex_digit_display_5 (.value(LedData[15:12]));  // open: dp
  Hex_Digit_Display hex_digit_display_6 (.value(LedData[7:4]));  // open: dp
  Hex_Digit_Display hex_digit_display_7 (.value(LedData[11:8]));  // open: dp
  // Probe on EX_PC[19:0]
  // RiscV_Probe riscv_probe_3: pin names not known; wires that end beside it: EX_IR
  \理想流水寄存器  \u_理想流水寄存器_1  (
    .Instr(IF_IR), .Instr_out(ID_IR), .clk(CLK), .PC(IF_PC), .PC_out(ID_PC));  // open: ALU_src, ALU_op, ecall, MemWrite, RegWrite, MemToReg, R1, R2, Imm, ALU, MemData, ALU_src_out, ALU_op_out, ecall_out, MemWrite_out, RegWrite_out, MemToReg_out, R1_out, R2_out, Imm_out, ALU_out, MemData_out, WriteReg_num, WriteReg__out
  Hex_Digit_Display hex_digit_display_8 (.value(LedData[3:0]));  // open: dp
  // Probe on \总周期数 
  // Probe on M_PC[19:0]
  // RiscV_Probe riscv_probe_4: pin names not known; wires that end beside it: MEM_IR
  // 单周期硬布线控制器 单周期硬布线控制器_1: pin names not known; wires that end beside it: ID_IR[21], ID_IR[6:2], {ID_IR[30], ID_IR[25], ID_IR[14:12]}, \单周期硬布线控制器_1_p4 , \单周期硬布线控制器_1_p4 , ID_ecall, \单周期硬布线控制器_1_p7 , \单周期硬布线控制器_1_p8 , \单周期硬布线控制器_1_p9 , \单周期硬布线控制器_1_p10 , \单周期硬布线控制器_1_p11 , \单周期硬布线控制器_1_p12 
  Multiplexer #(.select(1), .width(5), .disabled("Z"), .enable("false")) multiplexer_1 (
    .in0(ID_IR[19:15]), .in1(5'b10001), .out(multiplexer_1_out), .sel(ID_ecall));
  Multiplexer #(.select(1), .width(5), .disabled("Z"), .enable("false")) multiplexer_2 (
    .in0(ID_IR[24:20]), .in1(5'b01010), .out(multiplexer_2_out), .sel(ID_ecall));
  // Probe on \总周期数 
  // Probe on \无条件分支数 
  // Probe on \条件分支成功数 
  // Probe on \插入气泡数 
  // Probe on \LoadUse次数 
  Multiplexer #(.select(1), .width(12), .disabled("Z"), .enable("false")) multiplexer_3 (
    .in0(ID_IR[31:20]), .in1({ID_IR[31:25], ID_IR[11:7]}), .out(multiplexer_3_out), .sel(\单周期硬布线控制器_1_p12 ));
  // Probe on IF_PC[11:0]
  // Probe on WB_PC[19:0]
  // RiscV_Probe riscv_probe_5: pin names not known; wires that end beside it: WB_IR
  Regifile regifile_1 (
    .Din(RDin), .Clk(CLK), .R1(ID_R1), .R2(ID_R2), .WE(RegWrite), .W_num(\理想流水寄存器_4_writereg__out ),
    .R1_num(multiplexer_1_out), .R2_num(multiplexer_2_out));
  assign ID_Imm = {{20{multiplexer_3_out[11]}}, multiplexer_3_out};  // Bit_Extender bit_extender_1
  // Probe on EX_PC[11:0]
  // Probe on ID_PC[11:0]
  \理想流水寄存器  \u_理想流水寄存器_2  (
    .ALU_src(\单周期硬布线控制器_1_p10 ), .ALU_op(\单周期硬布线控制器_1_p9 ), .ecall(ID_ecall), .MemWrite(\单周期硬布线控制器_1_p8 ),
    .RegWrite(\单周期硬布线控制器_1_p11 ), .MemToReg(\单周期硬布线控制器_1_p7 ), .Instr(ID_IR), .R1(ID_R1), .R2(ID_R2),
    .Imm(ID_Imm), .ALU_src_out(\理想流水寄存器_2_alu_src_out ), .ALU_op_out(\理想流水寄存器_2_alu_op_out ),
    .ecall_out(\理想流水寄存器_2_ecall_out ), .MemWrite_out(\理想流水寄存器_2_memwrite_out ),
    .RegWrite_out(\理想流水寄存器_2_regwrite_out ), .MemToReg_out(\理想流水寄存器_2_memtoreg_out ), .Instr_out(EX_IR),
    .R1_out(\理想流水寄存器_2_r1_out ), .R2_out(\理想流水寄存器_2_r2_out ), .Imm_out(\理想流水寄存器_2_imm_out ), .clk(CLK),
    .PC(ID_PC), .PC_out(EX_PC), .WriteReg_num(ID_IR[11:7]), .WriteReg__out(\理想流水寄存器_2_writereg__out ));  // open: ALU, MemData, ALU_out, MemData_out
  // Probe on M_PC[11:0]
  D_Flip_Flop #(.trigger("high"), .Pre_Clr_Positions("LEGACY"), .NegatePresetClear("false"), .enable("true"), .NewFFLayout("false")) d_ff_1 (.Q(d_ff_1_q));  // open: clk, D, Qn, preset, en, reset
  // Probe on 13'hc
  // Probe on WB_PC[11:0]
  Comparator #(.width(13), .mode("twosComplement")) comparator_1 (
    .a(CNT_num), .b(13'hc), .eq(comparator_1_eq), .lt(comparator_1_lt));  // open: gt
  Clock #(.highDuration(1), .lowDuration(1)) clock_1 (.out(clock_1_out));
  Multiplexer #(.select(1), .width(32), .disabled("Z"), .enable("false")) multiplexer_4 (
    .in0(\理想流水寄存器_2_r2_out ), .in1(\理想流水寄存器_2_imm_out ), .out(multiplexer_4_out),
    .sel(\理想流水寄存器_2_alu_src_out ));
  nand nand_1 (nand_1_out, d_ff_1_q, comparator_1_eq);
  Counter #(.width(13), .max('h1fff), .ongoal("stay"), .trigger("rising"), .behavior("old")) counter_2 (
    .count(comparator_1_lt), .Q(CNT_num), .clk(clock_1_out));  // open: load, D, carry, clr, preset
  ALU alu_1 (
    .X(\理想流水寄存器_2_r1_out ), .Y(multiplexer_4_out), .AluOP(\理想流水寄存器_2_alu_op_out ), .Result(alu_1_result));  // open: Equal, Result_2, out_4, out_6
  assign CLK = nand_1_out ? clock_1_out : 1'bz;  // Controlled_Buffer controlled_buffer_1
  \理想流水寄存器  \u_理想流水寄存器_3  (
    .ecall(\理想流水寄存器_2_ecall_out ), .MemWrite(\理想流水寄存器_2_memwrite_out ), .RegWrite(\理想流水寄存器_2_regwrite_out ),
    .MemToReg(\理想流水寄存器_2_memtoreg_out ), .Instr(EX_IR), .R1(\理想流水寄存器_2_r1_out ), .R2(\理想流水寄存器_2_r2_out ),
    .ALU(alu_1_result), .ecall_out(\理想流水寄存器_3_ecall_out ), .MemWrite_out(MemWrite),
    .RegWrite_out(\理想流水寄存器_3_regwrite_out ), .MemToReg_out(\理想流水寄存器_3_memtoreg_out ), .Instr_out(MEM_IR),
    .R1_out(\理想流水寄存器_3_r1_out ), .R2_out(MDin), .ALU_out(mem_addr), .clk(CLK), .PC(EX_PC), .PC_out(M_PC),
    .WriteReg_num(\理想流水寄存器_2_writereg__out ), .WriteReg__out(\理想流水寄存器_3_writereg__out ));  // open: ALU_src, ALU_op, Imm, MemData, ALU_src_out, ALU_op_out, Imm_out, MemData_out
  Pull_Resistor #(.pull(1)) pull_resistor_1 (.node(CLK));
  RAM #(.addrWidth(10), .dataWidth(32), .bus("separate"), .Select("high")) ram_1 (
    .addr(mem_addr[11:2]), .din(MDin), .data(mem_ld), .str(MemWrite), .clk(CLK));  // open: sel, ld, clr
  Comparator #(.width(32), .mode("twosComplement")) comparator_2 (
    .a(WB_R1), .b(32'h22), .eq(comparator_2_eq));  // open: gt, lt
  \理想流水寄存器  \u_理想流水寄存器_4  (
    .ecall(\理想流水寄存器_3_ecall_out ), .RegWrite(\理想流水寄存器_3_regwrite_out ), .MemToReg(\理想流水寄存器_3_memtoreg_out ),
    .Instr(MEM_IR), .R1(\理想流水寄存器_3_r1_out ), .R2(MDin), .ALU(mem_addr), .MemData(mem_ld),
    .ecall_out(WB_ecall), .RegWrite_out(RegWrite), .MemToReg_out(\理想流水寄存器_4_memtoreg_out ),
    .Instr_out(WB_IR), .R1_out(WB_R1), .R2_out(WB_R2), .ALU_out(\理想流水寄存器_4_alu_out ),
    .MemData_out(\理想流水寄存器_4_memdata_out ), .clk(CLK), .PC(M_PC), .PC_out(WB_PC),
    .WriteReg_num(\理想流水寄存器_3_writereg__out ), .WriteReg__out(\理想流水寄存器_4_writereg__out ));  // open: ALU_src, ALU_op, MemWrite, Imm, ALU_src_out, ALU_op_out, MemWrite_out, Imm_out
  and and_1 (and_1_out, WB_ecall, comparator_2_eq);
  and and_2 (and_2_out, ~comparator_2_eq, WB_ecall);  // AND_Gate
  or or_1 (or_1_out, Go, ~halt);  // OR_Gate
  Multiplexer #(.select(1), .width(32), .disabled("Z"), .enable("false")) multiplexer_5 (
    .in0(\理想流水寄存器_4_alu_out ), .in1(\理想流水寄存器_4_memdata_out ), .out(RDin), .sel(\理想流水寄存器_4_memtoreg_out ));
  Register #(.width(32), .trigger("rising"), .Select("low")) register_1 (
    .D(WB_R2), .en(and_1_out), .Q(LedData), .clk(CLK));  // open: clr
  Register #(.width(1), .trigger("rising"), .Select("low")) register_2 (
    .D(and_2_out), .en(or_1_out), .Q(halt), .clk(CLK));  // open: clr

  // Other names for the same wires on the sheet: ID_WriteReg_num[4:0] = ID_IR[11:7]; MEM_PC[31:0] = M_PC;
  //   WB_RegWrite = RegWrite

  // Notes on the sheet:
  //   中断源
  //   时空图监测，可删除
  //   中断等待指示
  //   指令存储器
  //   contents of rom_1 (hex, n*v repeats v):
  //   413 493 913 993 46413 14e493 296913 39e993 842023 942223 1242423 1342623 a00893 493 913 993 73
  //   数码管输出
  //   IF/ ID
  //   指令字
  //   AluOP
  //   AluSrcB
  //   RegWrite
  //   S_Type
  //   MemToReg
  //   MemWrite
  //   控制位
  //   ID / EX
  //   流水调试日志用
  //   暂停节拍，不能为0
  //   戳工具置1进入计数暂停模式，ctrl+k时钟自动运行到对应节拍暂停
  //   ctrl+k关闭时钟连续运行，将控制位置零，进入单步调试模式调试
  //   用这个时钟源需要去掉电路中的其他时钟源
  //   可计数暂停的时钟源
  //   EX / MEM
  //   数据存储器
  //   为方便自动评测，需要输出流水线各段保存的PC值，注意是PC不是PC+4，另外ID段寄存器写入信息，Mem段内存写入信息也要输出
  //   MEM / WB
endmodule

module \气泡流水线  (
  output RegWrite,
  output MemWrite,
  output [31:0] IF_PC,
  output [31:0] ID_PC,
  output [31:0] EX_PC,
  output [31:0] M_PC,
  output [31:0] WB_PC,
  output [31:0] RDin,
  output [31:0] MDin,
  output [31:0] LedData
);

  wire alu_1_equal, alu_1_out_4, and_1_out, and_2_out, and_3_out, and_4_out, and_5_out, and_8_out, and_9_out,
       BGE, branch, CLK, clock_1_out, clock_2_out, comparator_1_eq, comparator_1_lt, comparator_2_eq,
       d_ff_1_q, DataHazzard, decoder_1_out0, decoder_1_out1, decoder_1_out2, decoder_1_out3, EX_BGE, EX_jal,
       EX_jalr, EX_RegWrite, Flush, Go, halt, ID_ALUSrc, ID_BEQ, ID_BGE, ID_BNE, ID_ecall, ID_JAL, ID_JALR,
       ID_MemWrite, IR1, IR2, IR3, MEM_RegWrite, MEM_SB, nand_1_out, not_1_out, not_2_out, not_5_out,
       not_6_out, not_7_out, or_1_out, or_2_out, or_5_out, or_6_out, R1Used, R2Used, RST, W1, W2, W3,
       WB_ecall, WB_JAL, WB_JALR, \单周期硬布线控制器_1_p6 , \单周期硬布线控制器_1_p11 , \单周期硬布线控制器_1_p15 , \单周期硬布线控制器_1_p16 ,
       \单周期硬布线控制器_1_p17 , \气泡流水线寄存器_2_alu_src_out , \气泡流水线寄存器_2_beq_out , \气泡流水线寄存器_2_bne_out ,
       \气泡流水线寄存器_2_ecall_out , \气泡流水线寄存器_2_memtoreg_out , \气泡流水线寄存器_2_memwrite_out , \气泡流水线寄存器_2_sb_out ,
       \气泡流水线寄存器_3_ecall_out , \气泡流水线寄存器_3_jal_out , \气泡流水线寄存器_3_jalr_out , \气泡流水线寄存器_3_memtoreg_out ,
       \气泡流水线寄存器_4_memtoreg_out ;
  wire [3:0] \单周期硬布线控制器_1_p13 , \气泡流水线寄存器_2_alu_op_out ;
  wire [4:0] EX_WriteReg_num, ID_Reg_1, ID_Reg_2, MEM_WriteReg_num, WB_WriteReg_num;
  wire [11:0] multiplexer_6_out;
  wire [12:0] CNT_num;
  wire [15:0] \LoadUse次数 , \总周期数 , \插入气泡数 , \无条件分支数 , \条件分支成功数 ;
  wire [31:0] bit_extender_2_out, bit_extender_3_out, EX_ALU, EX_bxx_pc, EX_IR, ID_Imm, ID_IR, ID_R1, ID_R2,
       IF_IR, jal_pc, jalr_pc, MEM_addr, MEM_IR, mem_ld, MEM_R2, multiplexer_1_out, multiplexer_2_out,
       multiplexer_3_out, multiplexer_7_out, multiplexer_13_out, PC_4, sb_word, WB_ALU, WB_IR, WB_PC_4,
       WB_R1, WB_R2, \气泡流水线寄存器_2_imm_out , \气泡流水线寄存器_2_r1_out , \气泡流水线寄存器_2_r2_out , \气泡流水线寄存器_3_r1_out ,
       \气泡流水线寄存器_4_memdata_out ;

  Button \u_总复位  (.out(RST));
  Button _1 (.out(IR1));
  Button _2 (.out(IR2));
  Button _3 (.out(IR3));
  // Probe on \总周期数 
  // Probe on \总周期数 
  Button \u_继续运行  (.out(Go));
  LED #(.active("true")) led_1 (.in(W1));
  LED #(.active("true")) led_2 (.in(W2));
  LED #(.active("true")) led_3 (.in(W3));
  Multiplexer #(.select(1), .width(32), .disabled("Z"), .enable("false")) multiplexer_1 (
    .in0(PC_4), .in1(EX_bxx_pc), .out(multiplexer_1_out), .sel(branch));
  Multiplexer #(.select(1), .width(32), .disabled("Z"), .enable("false")) multiplexer_2 (
    .in0(multiplexer_1_out), .in1(jal_pc), .out(multiplexer_2_out), .sel(EX_jal));
  Hex_Digit_Display hex_digit_display_1 (.value(LedData[31:28]));  // open: dp
  // Probe on IF_PC[19:0]
  // RiscV_Probe riscv_probe_1: pin names not known; wires that end beside it: IF_IR
  Multiplexer #(.select(1), .width(32), .disabled("Z"), .enable("false")) multiplexer_3 (
    .in0(multiplexer_2_out), .in1(jalr_pc), .out(multiplexer_3_out), .sel(EX_jalr));
  and and_1 (and_1_out, not_2_out, not_1_out);
  not not_1 (not_1_out, halt);
  not not_2 (not_2_out, DataHazzard);
  Hex_Digit_Display hex_digit_display_2 (.value(LedData[27:24]));  // open: dp
  Hex_Digit_Display hex_digit_display_3 (.value(LedData[23:20]));  // open: dp
  // Probe on ID_PC[19:0]
  // RiscV_Probe riscv_probe_2: pin names not known; wires that end beside it: ID_IR
  Register #(.width(32), .trigger("rising"), .Select("low")) PC (
    .D(multiplexer_3_out), .en(and_1_out), .Q(IF_PC), .clk(CLK), .clr(RST));
  Hex_Digit_Display hex_digit_display_4 (.value(LedData[19:16]));  // open: dp
  Hex_Digit_Display hex_digit_display_5 (.value(LedData[15:12]));  // open: dp
  or or_1 (or_1_out, ID_JAL, ID_JALR);
  not not_3 (R1Used, or_1_out);
  and and_2 (and_2_out, ID_ALUSrc, ~ID_MemWrite);  // AND_Gate
  not not_4 (R2Used, and_2_out);
  Hex_Digit_Display hex_digit_display_6 (.value(LedData[11:8]));  // open: dp
  Hex_Digit_Display hex_digit_display_7 (.value(LedData[7:4]));  // open: dp
  // Probe on EX_PC[19:0]
  // RiscV_Probe riscv_probe_3: pin names not known; wires that end beside it: EX_IR
  ROM #(.addrWidth(10), .dataWidth(32), .Select("high")) rom_1 (.addr(IF_PC[11:2]), .data(IF_IR));
  Adder #(.width(32)) adder_1 (.a(IF_PC), .b(32'h4), .out(PC_4));  // open: cin, cout
  Hex_Digit_Display hex_digit_display_8 (.value(LedData[3:0]));  // open: dp
  not not_5 (not_5_out, DataHazzard);
  // Probe on \总周期数 
  // Probe on M_PC[19:0]
  // RiscV_Probe riscv_probe_4: pin names not known; wires that end beside it: MEM_IR
  \气泡流水线寄存器  \u_气泡流水线寄存器_1  (
    .PC(IF_PC), .Instr(IF_IR), .PC_out(ID_PC), .Instr_out(ID_IR), .Flush(Flush), .Enable(not_5_out), .clk(CLK));  // open: ALU_src, ALU_op, BGE, BNE, BEQ, SB, MemWrite, RegWrite, MemToReg, ecall, JAL, JALR, R1, R2, Imm, ALU, MemData, ALU_src_out, ALU_op_out, BGE_out, BNE_out, BEQ_out, SB_out, MemWrite_out, RegWrite_out, MemToReg_out, ecall_out, JAL_out, JALR_out, R1_out, R2_out, Imm_out, ALU_out, MemData_out, WriteReg_num, WriteReg__out
  // Probe on \总周期数 
  // Probe on \无条件分支数 
  // Probe on \条件分支成功数 
  // Probe on \插入气泡数 
  // Probe on \LoadUse次数 
  // Probe on IF_PC[11:0]
  // Probe on WB_PC[19:0]
  // RiscV_Probe riscv_probe_5: pin names not known; wires that end beside it: WB_IR
  // 单周期硬布线控制器 单周期硬布线控制器_1: pin names not known; wires that end beside it: ID_JAL, ID_JALR, ID_IR[21], ID_IR[6:2], {ID_IR[30], ID_IR[25], ID_IR[14:12]}, \单周期硬布线控制器_1_p6 , \单周期硬布线控制器_1_p6 , ID_ecall, ID_BEQ, ID_BNE, \单周期硬布线控制器_1_p11 , ID_MemWrite, \单周期硬布线控制器_1_p13 , ID_ALUSrc, \单周期硬布线控制器_1_p15 , \单周期硬布线控制器_1_p16 , \单周期硬布线控制器_1_p17 , ID_BGE
  Multiplexer #(.select(1), .width(5), .disabled("Z"), .enable("false")) multiplexer_4 (
    .in0(ID_IR[24:20]), .in1(5'b01010), .out(ID_Reg_2), .sel(ID_ecall));
  DataHazzard datahazzard_1 (
    .rs_used(R1Used), .rt_used(R2Used), .rs(ID_Reg_1), .rt(ID_Reg_2), .EX_RW(EX_RegWrite),
    .MEM_RW(MEM_RegWrite), .EX_Reg(EX_WriteReg_num), .MEM_Reg(MEM_WriteReg_num), .DataHazzard(DataHazzard));
  // Probe on EX_PC[11:0]
  // Probe on ID_PC[11:0]
  Multiplexer #(.select(1), .width(5), .disabled("Z"), .enable("false")) multiplexer_5 (
    .in0(ID_IR[19:15]), .in1(5'b10001), .out(ID_Reg_1), .sel(ID_ecall));
  Multiplexer #(.select(1), .width(12), .disabled("Z"), .enable("false")) multiplexer_6 (
    .in0(ID_IR[31:20]), .in1({ID_IR[31:25], ID_IR[11:7]}), .out(multiplexer_6_out), .sel(\单周期硬布线控制器_1_p16 ));
  // Probe on M_PC[11:0]
  D_Flip_Flop #(.trigger("high"), .Pre_Clr_Positions("LEGACY"), .NegatePresetClear("false"), .enable("true"), .NewFFLayout("false")) d_ff_1 (.Q(d_ff_1_q));  // open: clk, D, Qn, preset, en, reset
  // Probe on 13'he27
  assign ID_Imm = {{20{multiplexer_6_out[11]}}, multiplexer_6_out};  // Bit_Extender bit_extender_1
  // Probe on WB_PC[11:0]
  Comparator #(.width(13), .mode("twosComplement")) comparator_1 (
    .a(CNT_num), .b(13'he27), .eq(comparator_1_eq), .lt(comparator_1_lt));  // open: gt
  Clock #(.highDuration(1), .lowDuration(1)) clock_1 (.out(clock_1_out));
  Regifile regifile_1 (
    .Din(RDin), .Clk(CLK), .R1(ID_R1), .R2(ID_R2), .WE(RegWrite), .W_num(WB_WriteReg_num), .R1_num(ID_Reg_1),
    .R2_num(ID_Reg_2));
  not not_6 (not_6_out, halt);
  nand nand_1 (nand_1_out, d_ff_1_q, comparator_1_eq);
  Counter #(.width(13), .max('h1fff), .ongoal("stay"), .trigger("rising"), .behavior("old")) counter_1 (
    .count(comparator_1_lt), .Q(CNT_num), .clk(clock_1_out));  // open: load, D, carry, clr, preset
  and and_3 (and_3_out, not_6_out, nand_1_out);
  assign CLK = and_3_out ? clock_1_out : 1'bz;  // Controlled_Buffer controlled_buffer_1
  or or_2 (or_2_out, Flush, DataHazzard);
  Pull_Resistor #(.pull(1)) pull_resistor_1 (.node(CLK));
  \气泡流水线寄存器  \u_气泡流水线寄存器_2  (
    .ALU_src(ID_ALUSrc), .ALU_op(\单周期硬布线控制器_1_p13 ), .BGE(ID_BGE), .BNE(ID_BNE), .BEQ(ID_BEQ),
    .SB(\单周期硬布线控制器_1_p17 ), .MemWrite(ID_MemWrite), .RegWrite(\单周期硬布线控制器_1_p15 ),
    .MemToReg(\单周期硬布线控制器_1_p11 ), .ecall(ID_ecall), .JAL(ID_JAL), .JALR(ID_JALR), .PC(ID_PC), .Instr(ID_IR),
    .R1(ID_R1), .R2(ID_R2), .Imm(ID_Imm), .ALU_src_out(\气泡流水线寄存器_2_alu_src_out ),
    .ALU_op_out(\气泡流水线寄存器_2_alu_op_out ), .BGE_out(EX_BGE), .BNE_out(\气泡流水线寄存器_2_bne_out ),
    .BEQ_out(\气泡流水线寄存器_2_beq_out ), .SB_out(\气泡流水线寄存器_2_sb_out ), .MemWrite_out(\气泡流水线寄存器_2_memwrite_out ),
    .RegWrite_out(EX_RegWrite), .MemToReg_out(\气泡流水线寄存器_2_memtoreg_out ), .ecall_out(\气泡流水线寄存器_2_ecall_out ),
    .JAL_out(EX_jal), .JALR_out(EX_jalr), .PC_out(EX_PC), .Instr_out(EX_IR), .R1_out(\气泡流水线寄存器_2_r1_out ),
    .R2_out(\气泡流水线寄存器_2_r2_out ), .Imm_out(\气泡流水线寄存器_2_imm_out ), .Flush(or_2_out), .Enable(1'b1), .clk(CLK),
    .WriteReg_num(ID_IR[11:7]), .WriteReg__out(EX_WriteReg_num));  // open: ALU, MemData, ALU_out, MemData_out
  Multiplexer #(.select(1), .width(32), .disabled("Z"), .enable("false")) multiplexer_7 (
    .in0(\气泡流水线寄存器_2_r2_out ), .in1(\气泡流水线寄存器_2_imm_out ), .out(multiplexer_7_out),
    .sel(\气泡流水线寄存器_2_alu_src_out ));
  ALU alu_1 (
    .X(\气泡流水线寄存器_2_r1_out ), .Y(multiplexer_7_out), .AluOP(\气泡流水线寄存器_2_alu_op_out ), .Equal(alu_1_equal),
    .Result(EX_ALU), .out_4(alu_1_out_4));  // open: Result_2, out_6
  not not_7 (not_7_out, halt);
  and and_4 (and_4_out, \气泡流水线寄存器_2_bne_out , ~alu_1_equal);  // AND_Gate
  and and_5 (and_5_out, \气泡流水线寄存器_2_beq_out , alu_1_equal);
  and and_6 (BGE, alu_1_out_4, EX_BGE);
  assign bit_extender_2_out = {{19{EX_IR[31]}}, {EX_IR[31], EX_IR[7], EX_IR[30:25], EX_IR[11:8], 1'b0}};  // Bit_Extender bit_extender_2
  assign bit_extender_3_out = {{11{EX_IR[31]}}, {EX_IR[31], EX_IR[19:12], EX_IR[20], EX_IR[30:21], 1'b0}};  // Bit_Extender bit_extender_3
  assign jalr_pc = EX_ALU & ~32'h1;  // AND_Gate and_7, 32 bits wide
  Counter #(.width(16), .max('hffff), .ongoal("wrap"), .trigger("rising"), .behavior("old")) counter_2 (
    .count(not_7_out), .Q(\总周期数 ), .clk(CLK));  // open: load, D, carry, clr, preset
  or or_3 (branch, and_4_out, and_5_out, BGE);
  Adder #(.width(32)) adder_2 (.a(bit_extender_2_out), .b(EX_PC), .out(EX_bxx_pc));  // open: cin, cout
  Adder #(.width(32)) adder_3 (.a(bit_extender_3_out), .b(EX_PC), .out(jal_pc));  // open: cin, cout
  \气泡流水线寄存器  \u_气泡流水线寄存器_3  (
    .SB(\气泡流水线寄存器_2_sb_out ), .MemWrite(\气泡流水线寄存器_2_memwrite_out ), .RegWrite(EX_RegWrite),
    .MemToReg(\气泡流水线寄存器_2_memtoreg_out ), .ecall(\气泡流水线寄存器_2_ecall_out ), .JAL(EX_jal), .JALR(EX_jalr),
    .PC(EX_PC), .Instr(EX_IR), .R1(\气泡流水线寄存器_2_r1_out ), .R2(\气泡流水线寄存器_2_r2_out ), .ALU(EX_ALU),
    .SB_out(MEM_SB), .MemWrite_out(MemWrite), .RegWrite_out(MEM_RegWrite),
    .MemToReg_out(\气泡流水线寄存器_3_memtoreg_out ), .ecall_out(\气泡流水线寄存器_3_ecall_out ),
    .JAL_out(\气泡流水线寄存器_3_jal_out ), .JALR_out(\气泡流水线寄存器_3_jalr_out ), .PC_out(M_PC), .Instr_out(MEM_IR),
    .R1_out(\气泡流水线寄存器_3_r1_out ), .R2_out(MEM_R2), .ALU_out(MEM_addr), .Flush(1'b0), .Enable(1'b1),
    .clk(CLK), .WriteReg_num(EX_WriteReg_num), .WriteReg__out(MEM_WriteReg_num));  // open: ALU_src, ALU_op, BGE, BNE, BEQ, Imm, MemData, ALU_src_out, ALU_op_out, BGE_out, BNE_out, BEQ_out, Imm_out, MemData_out
  or or_4 (Flush, branch, EX_jal, EX_jalr);
  Decoder #(.select(2), .tristate("false"), .disabled("Z"), .enable("false")) decoder_1 (
    .out0(decoder_1_out0), .out1(decoder_1_out1), .out2(decoder_1_out2), .out3(decoder_1_out3),
    .sel(MEM_addr[1:0]));
  Multiplexer #(.select(1), .width(8), .disabled("Z"), .enable("false")) multiplexer_8 (
    .in0(mem_ld[7:0]), .in1(MEM_R2[7:0]), .out(sb_word[7:0]), .sel(decoder_1_out0));
  RAM #(.addrWidth(10), .dataWidth(32), .bus("separate"), .Select("high")) ram_1 (
    .addr(MEM_addr[11:2]), .din(MDin), .data(mem_ld), .str(MemWrite), .clk(CLK));  // open: sel, ld, clr
  Multiplexer #(.select(1), .width(8), .disabled("Z"), .enable("false")) multiplexer_9 (
    .in0(mem_ld[15:8]), .in1(MEM_R2[7:0]), .out(sb_word[15:8]), .sel(decoder_1_out1));
  Multiplexer #(.select(1), .width(8), .disabled("Z"), .enable("false")) multiplexer_10 (
    .in0(mem_ld[23:16]), .in1(MEM_R2[7:0]), .out(sb_word[23:16]), .sel(decoder_1_out2));
  Multiplexer #(.select(1), .width(8), .disabled("Z"), .enable("false")) multiplexer_11 (
    .in0(mem_ld[31:24]), .in1(MEM_R2[7:0]), .out(sb_word[31:24]), .sel(decoder_1_out3));
  Multiplexer #(.select(1), .width(32), .disabled("Z"), .enable("false")) multiplexer_12 (
    .in0(MEM_R2), .in1(sb_word), .out(MDin), .sel(MEM_SB));
  \气泡流水线寄存器  \u_气泡流水线寄存器_4  (
    .RegWrite(MEM_RegWrite), .MemToReg(\气泡流水线寄存器_3_memtoreg_out ), .ecall(\气泡流水线寄存器_3_ecall_out ),
    .JAL(\气泡流水线寄存器_3_jal_out ), .JALR(\气泡流水线寄存器_3_jalr_out ), .PC(M_PC), .Instr(MEM_IR),
    .R1(\气泡流水线寄存器_3_r1_out ), .R2(MEM_R2), .ALU(MEM_addr), .MemData(mem_ld), .RegWrite_out(RegWrite),
    .MemToReg_out(\气泡流水线寄存器_4_memtoreg_out ), .ecall_out(WB_ecall), .JAL_out(WB_JAL), .JALR_out(WB_JALR),
    .PC_out(WB_PC), .Instr_out(WB_IR), .R1_out(WB_R1), .R2_out(WB_R2), .ALU_out(WB_ALU),
    .MemData_out(\气泡流水线寄存器_4_memdata_out ), .Flush(1'b0), .Enable(1'b1), .clk(CLK),
    .WriteReg_num(MEM_WriteReg_num), .WriteReg__out(WB_WriteReg_num));  // open: ALU_src, ALU_op, BGE, BNE, BEQ, SB, MemWrite, Imm, ALU_src_out, ALU_op_out, BGE_out, BNE_out, BEQ_out, SB_out, MemWrite_out, Imm_out
  Comparator #(.width(32), .mode("twosComplement")) comparator_2 (
    .a(WB_R1), .b(32'h22), .eq(comparator_2_eq));  // open: gt, lt
  or or_5 (or_5_out, WB_JAL, WB_JALR);
  Multiplexer #(.select(1), .width(32), .disabled("Z"), .enable("false")) multiplexer_13 (
    .in0(WB_ALU), .in1(\气泡流水线寄存器_4_memdata_out ), .out(multiplexer_13_out), .sel(\气泡流水线寄存器_4_memtoreg_out ));
  Adder #(.width(32)) adder_4 (.a(WB_PC), .b(32'h4), .out(WB_PC_4));  // open: cin, cout
  Multiplexer #(.select(1), .width(32), .disabled("Z"), .enable("false")) multiplexer_14 (
    .in0(multiplexer_13_out), .in1(WB_PC_4), .out(RDin), .sel(or_5_out));
  and and_8 (and_8_out, WB_ecall, comparator_2_eq);
  and and_9 (and_9_out, ~comparator_2_eq, WB_ecall);  // AND_Gate
  or or_6 (or_6_out, Go, ~halt);  // OR_Gate
  Register #(.width(32), .trigger("rising"), .Select("low")) register_1 (
    .D(WB_R2), .en(and_8_out), .Q(LedData), .clk(CLK));  // open: clr
  Register #(.width(1), .trigger("rising"), .Select("low")) register_2 (
    .D(and_9_out), .en(or_6_out), .Q(halt), .clk(clock_2_out));  // open: clr
  Clock #(.highDuration(1), .lowDuration(1)) clock_2 (.out(clock_2_out));

  // Other names for the same wires on the sheet: ID_WriteReg_num[4:0] = ID_IR[11:7]; MEM_ALU[31:0] = MEM_addr;
  //   MEM_MemWrite = MemWrite; MEM_PC[31:0] = M_PC; WB_RegVal[31:0] = RDin; WB_RegWrite = RegWrite

  // Notes on the sheet:
  //   中断源
  //   时空图监测，可删除
  //   中断等待指示
  //   数码管输出
  //   指令存储器
  //   contents of rom_1 (hex, n*v repeats v):
  //   100493 100006f 100493 200913 300993 100006f 100493 200913 300993 100006f 100493 200913 300993
  //   100006f 100493 200913 300993 3ac000ef 100413 100493 1f49493 900533 2200893 73 24d493 48463 fedff06f
  //   900533 2200893 73 100493 249493 900533 2200893 73 48463 fedff06f 100493 1f49493 900533 2200893 73
  //   4034d493 900533 2200893 73 4044d493 900533 2200893 73 4044d493 900533 2200893 73 4044d493 900533
  //   2200893 73 4044d493 900533 2200893 73 4044d493 900533 2200893 73 4044d493 900533 2200893 73 4044d493
  //   900533 2200893 73 100413 1f41993 41f9d993 433 c00913 300b13 140413 f47413 800293 100313 499993
  //   89e9b3 1300533 2200893 73 406282b3 fe0294e3 140413 f00f93 1f47433 1c41413 800293 100313 49d993
  //   89e9b3 1300533 2200893 73 406282b3 fe0294e3 1c45413 406b0b33 b0463 f95ff06f 2b3 fff2c293 829293
  //   ff2e293 500533 2200893 73 fff00413 493 84a023 140413 448493 84a023 140413 448493 84a023 140413
  //   448493 84a023 140413 448493 84a023 140413 448493 84a023 140413 448493 84a023 140413 448493 84a023
  //   140413 448493 84a023 140413 448493 84a023 140413 448493 84a023 140413 448493 84a023 140413 448493
  //   84a023 140413 448493 84a023 140413 448493 84a023 140413 448493 84a023 140413 448493 140413 433
  //   3c00493 42983 4aa03 149a2b3 28663 134a023 1442023 ffc48493 fe9412e3 800533 2200893 73 440413 3c00493
  //   fc9416e3 3200893 73 100293 300313 800493 849493 7648493 900533 2200893 73 800e13 5494b3 6494b3
  //   900533 2200893 73 fffe0e13 fe0e14e3 a00893 73 100293 300313 800493 849493 7648493 1449493 900533
  //   2200893 73 800e13 4054d4b3 4064d4b3 900533 2200893 73 fffe0e13 fe0e14e3 a00893 73 313 2000e13 493
  //   100913 930023 900533 2200893 73 12484b3 130313 fffe0e13 fe0e12e3 800e13 313 32483 900533 2200893 73
  //   430313 fffe0e13 fe0e14e3 a00893 73 f00493 900533 2200893 73 fff48493 fe04d8e3 a00893 73 413 140413
  //   800533 2200893 73 240413 800533 2200893 73 340413 800533 2200893 73 440413 800533 2200893 73 540413
  //   800533 2200893 73 640413 800533 2200893 73 740413 800533 2200893 73 840413 800533 2200893 2200893 73
  //   8067
  //   IF/ ID
  //   指令字
  //   控制位
  //   MemToReg
  //   MemWrite
  //   AluOP
  //   AluSrcB
  //   RegWrite
  //   S_Type
  //   流水调试日志用
  //   暂停节拍，不能为0
  //   戳工具置1进入计数暂停模式，ctrl+k时钟自动运行到对应节拍暂停
  //   ctrl+k关闭时钟连续运行，将控制位置零，进入单步调试模式调试
  //   可计数暂停的时钟源
  //   ID / EX
  //   为方便自动评测，需要输出流水线各段保存的PC值，注意是PC不是PC+4，另外ID段寄存器写入信息，Mem段内存写入信息也要输出
  //   EX / MEM
  //   数据存储器
  //   MEM / WB
endmodule

module \重定向流水线  (
  output RegWrite,
  output MemWrite,
  output [31:0] IF_PC,
  output [31:0] ID_PC,
  output [31:0] EX_PC,
  output [31:0] M_PC,
  output [31:0] WB_PC,
  output [31:0] RDin,
  output [31:0] MDin,
  output [31:0] LedData
);

  wire alu_1_equal, alu_1_out_4, and_1_out, and_2_out, and_3_out, and_4_out, and_5_out, and_8_out, and_9_out,
       BGE, branch, CLK, clock_1_out, clock_2_out, comparator_1_eq, comparator_1_lt, comparator_2_eq,
       d_ff_1_q, decoder_1_out0, decoder_1_out1, decoder_1_out2, decoder_1_out3, EX_ALUSrc, EX_BGE, EX_JAL,
       EX_JALR, EX_MemToReg, EX_MemWrite, EX_RegWrite, Flush, Go, halt, ID_ALUSrc, ID_BEQ, ID_BGE, ID_BNE,
       ID_ecall, ID_JAL, ID_JALR, ID_MemWrite, IR1, IR2, IR3, Load_Use, MEM_MemToReg, MEM_RegWrite, MEM_SB,
       nand_1_out, not_1_out, not_2_out, not_5_out, not_6_out, not_7_out, or_1_out, or_2_out, or_5_out,
       or_6_out, R1Used, R2Used, RST, W1, W2, W3, WB_ecall, WB_JAL, WB_JALR, \单周期硬布线控制器_1_p6 ,
       \单周期硬布线控制器_1_p11 , \单周期硬布线控制器_1_p15 , \单周期硬布线控制器_1_p16 , \单周期硬布线控制器_1_p17 , \气泡流水线寄存器_1_ecall_out ,
       \气泡流水线寄存器_1_jal_out , \气泡流水线寄存器_1_jalr_out , \气泡流水线寄存器_2_memtoreg_out , \重定向流水寄存器_2_beq_out ,
       \重定向流水寄存器_2_bne_out , \重定向流水寄存器_2_ecall_out , \重定向流水寄存器_2_sb_out ;
  wire [1:0] EX_rs_fwd, EX_rt_fwd, ID_rs_fwd, ID_rt_fwd;
  wire [3:0] \单周期硬布线控制器_1_p13 , \重定向流水寄存器_2_alu_op_out ;
  wire [4:0] EX_WriteReg_num, ID_Reg_1, ID_Reg_2, MEM_WriteReg_num, WB_WriteReg_num;
  wire [11:0] multiplexer_6_out;
  wire [12:0] CNT_num;
  wire [15:0] \LoadUse次数 , \总周期数 , \插入气泡数 , \无条件分支数 , \条件分支成功数 ;
  wire [31:0] bit_extender_2_out, bit_extender_3_out, EX_ALU, EX_bxx_pc, EX_Imm, EX_IR, EX_R2, ID_Imm, ID_IR,
       ID_R1, ID_R2, IF_IR, jal_pc, jalr_pc, MEM_addr, MEM_IR, mem_ld, MEM_R2, multiplexer_1_out,
       multiplexer_2_out, multiplexer_3_out, multiplexer_7_out, multiplexer_9_out, multiplexer_15_out, PC_4,
       sb_word, WB_ALU, WB_IR, WB_PC_4, WB_R1, WB_R2, \气泡流水线寄存器_1_r1_out , \气泡流水线寄存器_2_memdata_out ,
       \重定向流水寄存器_2_r1_out , \重定向流水寄存器_2_r2_out ;

  Button \u_总复位  (.out(RST));
  Button _1 (.out(IR1));
  Button _2 (.out(IR2));
  Button _3 (.out(IR3));
  // Probe on \总周期数 
  // Probe on \总周期数 
  Button \u_继续运行  (.out(Go));
  LED #(.active("true")) led_1 (.in(W1));
  LED #(.active("true")) led_2 (.in(W2));
  LED #(.active("true")) led_3 (.in(W3));
  Hex_Digit_Display hex_digit_display_1 (.value(LedData[31:28]));  // open: dp
  // Probe on IF_PC[19:0]
  // RiscV_Probe riscv_probe_1: pin names not known; wires that end beside it: IF_IR
  Multiplexer #(.select(1), .width(32), .disabled("Z"), .enable("false")) multiplexer_1 (
    .in0(PC_4), .in1(EX_bxx_pc), .out(multiplexer_1_out), .sel(branch));
  Multiplexer #(.select(1), .width(32), .disabled("Z"), .enable("false")) multiplexer_2 (
    .in0(multiplexer_1_out), .in1(jal_pc), .out(multiplexer_2_out), .sel(EX_JAL));
  Hex_Digit_Display hex_digit_display_2 (.value(LedData[27:24]));  // open: dp
  Hex_Digit_Display hex_digit_display_3 (.value(LedData[23:20]));  // open: dp
  // Probe on ID_PC[19:0]
  // RiscV_Probe riscv_probe_2: pin names not known; wires that end beside it: ID_IR
  Multiplexer #(.select(1), .width(32), .disabled("Z"), .enable("false")) multiplexer_3 (
    .in0(multiplexer_2_out), .in1(jalr_pc), .out(multiplexer_3_out), .sel(EX_JALR));
  and and_1 (and_1_out, not_2_out, not_1_out);
  not not_1 (not_1_out, halt);
  not not_2 (not_2_out, Load_Use);
  Hex_Digit_Display hex_digit_display_4 (.value(LedData[15:12]));  // open: dp
  Hex_Digit_Display hex_digit_display_5 (.value(LedData[19:16]));  // open: dp
  Register #(.width(32), .trigger("rising"), .Select("low")) PC (
    .D(multiplexer_3_out), .en(and_1_out), .Q(IF_PC), .clk(CLK), .clr(RST));
  Hex_Digit_Display hex_digit_display_6 (.value(LedData[11:8]));  // open: dp
  Hex_Digit_Display hex_digit_display_7 (.value(LedData[7:4]));  // open: dp
  // Probe on EX_PC[19:0]
  // RiscV_Probe riscv_probe_3: pin names not known; wires that end beside it: EX_IR
  not not_3 (R1Used, or_1_out);
  or or_1 (or_1_out, ID_JAL, ID_JALR);
  and and_2 (and_2_out, ID_ALUSrc, ~ID_MemWrite);  // AND_Gate
  not not_4 (R2Used, and_2_out);
  Hex_Digit_Display hex_digit_display_8 (.value(LedData[3:0]));  // open: dp
  ROM #(.addrWidth(10), .dataWidth(32), .Select("high")) rom_1 (.addr(IF_PC[11:2]), .data(IF_IR));
  Adder #(.width(32)) adder_1 (.a(IF_PC), .b(32'h4), .out(PC_4));  // open: cin, cout
  // Probe on \总周期数 
  // Probe on M_PC[19:0]
  // RiscV_Probe riscv_probe_4: pin names not known; wires that end beside it: MEM_IR
  not not_5 (not_5_out, Load_Use);
  // Probe on \总周期数 
  // Probe on \无条件分支数 
  // Probe on \条件分支成功数 
  // Probe on \插入气泡数 
  // Probe on \LoadUse次数 
  \重定向流水寄存器  \u_重定向流水寄存器_1  (
    .Instr(IF_PC), .R1(IF_IR), .Instr_out(ID_PC), .R1_out(ID_IR), .Flush(Flush), .Enable(not_5_out), .clk(CLK));  // open: ALU_src, ALU_op, BGE, BNE, BEQ, SB, MemWrite, RegWrite, MemToReg, ecall, JAL, JALR, PC, R2, Imm, ALU, MemData, WriteReg_num, Rs_fwd, Rt_fwd, ALU_src_out, ALU_op_out, BGE_out, BNE_out, BEQ_out, SB_out, MemWrite_out, RegWrite_out, MemToReg_out, ecall_out, JAL_out, JALR_out, PC_out, R2_out, Imm_out, ALU_out, MemData_out, WriteReg__out, Rs_fwd_out, Rt_fwd_out
  // Probe on IF_PC[11:0]
  // Probe on WB_PC[19:0]
  // RiscV_Probe riscv_probe_5: pin names not known; wires that end beside it: WB_IR
  // Probe on EX_PC[11:0]
  // Probe on ID_PC[11:0]
  // 单周期硬布线控制器 单周期硬布线控制器_1: pin names not known; wires that end beside it: ID_JAL, ID_JALR, ID_IR[21], ID_IR[6:2], {ID_IR[30], ID_IR[25], ID_IR[14:12]}, \单周期硬布线控制器_1_p6 , \单周期硬布线控制器_1_p6 , ID_ecall, ID_BEQ, ID_BNE, \单周期硬布线控制器_1_p11 , ID_MemWrite, \单周期硬布线控制器_1_p13 , ID_ALUSrc, \单周期硬布线控制器_1_p15 , \单周期硬布线控制器_1_p16 , \单周期硬布线控制器_1_p17 , ID_BGE
  Multiplexer #(.select(1), .width(5), .disabled("Z"), .enable("false")) multiplexer_4 (
    .in0(ID_IR[24:20]), .in1(5'b01010), .out(ID_Reg_2), .sel(ID_ecall));
  foward foward_1 (
    .rs_used(R1Used), .EX_MemToReg(EX_MemToReg), .rt_used(R2Used), .ID_rs(ID_Reg_1), .ID_rt(ID_Reg_2),
    .EX_RW(EX_RegWrite), .MEM_RW(MEM_RegWrite), .EX_Reg(EX_WriteReg_num), .MEM_Reg(MEM_WriteReg_num),
    .Load_Use(Load_Use), .ID_rs_forward(ID_rs_fwd), .ID_rt_forward(ID_rt_fwd));
  // Probe on M_PC[11:0]
  D_Flip_Flop #(.trigger("high"), .Pre_Clr_Positions("LEGACY"), .NegatePresetClear("false"), .enable("true"), .NewFFLayout("false")) d_ff_1 (.Q(d_ff_1_q));  // open: clk, D, Qn, preset, en, reset
  // Probe on 13'h37
  Multiplexer #(.select(1), .width(5), .disabled("Z"), .enable("false")) multiplexer_5 (
    .in0(ID_IR[19:15]), .in1(5'b10001), .out(ID_Reg_1), .sel(ID_ecall));
  Multiplexer #(.select(1), .width(12), .disabled("Z"), .enable("false")) multiplexer_6 (
    .in0(ID_IR[31:20]), .in1({ID_IR[31:25], ID_IR[11:7]}), .out(multiplexer_6_out), .sel(\单周期硬布线控制器_1_p16 ));
  // Probe on WB_PC[11:0]
  Comparator #(.width(13), .mode("twosComplement")) comparator_1 (
    .a(CNT_num), .b(13'h37), .eq(comparator_1_eq), .lt(comparator_1_lt));  // open: gt
  Clock #(.highDuration(1), .lowDuration(1)) clock_1 (.out(clock_1_out));
  assign ID_Imm = {{20{multiplexer_6_out[11]}}, multiplexer_6_out};  // Bit_Extender bit_extender_1
  not not_6 (not_6_out, halt);
  nand nand_1 (nand_1_out, d_ff_1_q, comparator_1_eq);
  Counter #(.width(13), .max('h1fff), .ongoal("stay"), .trigger("rising"), .behavior("old")) counter_1 (
    .count(comparator_1_lt), .Q(CNT_num), .clk(clock_1_out));  // open: load, D, carry, clr, preset
  Regifile regifile_1 (
    .Din(RDin), .Clk(CLK), .R1(ID_R1), .R2(ID_R2), .WE(RegWrite), .W_num(WB_WriteReg_num), .R1_num(ID_Reg_1),
    .R2_num(ID_Reg_2));
  and and_3 (and_3_out, not_6_out, nand_1_out);
  assign CLK = and_3_out ? clock_1_out : 1'bz;  // Controlled_Buffer controlled_buffer_1
  Pull_Resistor #(.pull(1)) pull_resistor_1 (.node(CLK));
  or or_2 (or_2_out, Flush, Load_Use);
  \重定向流水寄存器  \u_重定向流水寄存器_2  (
    .ALU_src(ID_ALUSrc), .ALU_op(\单周期硬布线控制器_1_p13 ), .BGE(ID_BGE), .BNE(ID_BNE), .BEQ(ID_BEQ),
    .SB(\单周期硬布线控制器_1_p17 ), .MemWrite(ID_MemWrite), .RegWrite(\单周期硬布线控制器_1_p15 ),
    .MemToReg(\单周期硬布线控制器_1_p11 ), .ecall(ID_ecall), .JAL(ID_JAL), .JALR(ID_JALR), .PC(ID_PC), .Instr(ID_IR),
    .R1(ID_R1), .R2(ID_R2), .Imm(ID_Imm), .WriteReg_num(ID_IR[11:7]), .Rs_fwd(ID_rs_fwd), .Rt_fwd(ID_rt_fwd),
    .ALU_src_out(EX_ALUSrc), .ALU_op_out(\重定向流水寄存器_2_alu_op_out ), .BGE_out(EX_BGE),
    .BNE_out(\重定向流水寄存器_2_bne_out ), .BEQ_out(\重定向流水寄存器_2_beq_out ), .SB_out(\重定向流水寄存器_2_sb_out ),
    .MemWrite_out(EX_MemWrite), .RegWrite_out(EX_RegWrite), .MemToReg_out(EX_MemToReg),
    .ecall_out(\重定向流水寄存器_2_ecall_out ), .JAL_out(EX_JAL), .JALR_out(EX_JALR), .PC_out(EX_PC),
    .Instr_out(EX_IR), .R1_out(\重定向流水寄存器_2_r1_out ), .R2_out(\重定向流水寄存器_2_r2_out ), .Imm_out(EX_Imm),
    .WriteReg__out(EX_WriteReg_num), .Rs_fwd_out(EX_rs_fwd), .Rt_fwd_out(EX_rt_fwd), .Flush(or_2_out),
    .Enable(1'b1), .clk(CLK));  // open: ALU, MemData, ALU_out, MemData_out
  or or_3 (Flush, branch, EX_JAL, EX_JALR);
  Multiplexer #(.select(2), .width(32), .disabled("Z"), .enable("false")) multiplexer_7 (
    .in0(\重定向流水寄存器_2_r1_out ), .in1(MEM_addr), .in2(RDin), .in3(MEM_addr), .out(multiplexer_7_out),
    .sel(EX_rs_fwd));
  Multiplexer #(.select(2), .width(32), .disabled("Z"), .enable("false")) multiplexer_8 (
    .in0(\重定向流水寄存器_2_r2_out ), .in1(MEM_addr), .in2(RDin), .in3(MEM_addr), .out(EX_R2), .sel(EX_rt_fwd));
  Multiplexer #(.select(1), .width(32), .disabled("Z"), .enable("false")) multiplexer_9 (
    .in0(EX_R2), .in1(EX_Imm), .out(multiplexer_9_out), .sel(EX_ALUSrc));
  and and_4 (and_4_out, \重定向流水寄存器_2_bne_out , ~alu_1_equal);  // AND_Gate
  and and_5 (and_5_out, \重定向流水寄存器_2_beq_out , alu_1_equal);
  ALU alu_1 (
    .X(multiplexer_7_out), .Y(multiplexer_9_out), .AluOP(\重定向流水寄存器_2_alu_op_out ), .Equal(alu_1_equal),
    .Result(EX_ALU), .out_4(alu_1_out_4));  // open: Result_2, out_6
  assign bit_extender_2_out = {{19{EX_IR[31]}}, {EX_IR[31], EX_IR[7], EX_IR[30:25], EX_IR[11:8], 1'b0}};  // Bit_Extender bit_extender_2
  assign bit_extender_3_out = {{11{EX_IR[31]}}, {EX_IR[31], EX_IR[19:12], EX_IR[20], EX_IR[30:21], 1'b0}};  // Bit_Extender bit_extender_3
  assign jalr_pc = EX_ALU & ~32'h1;  // AND_Gate and_6, 32 bits wide
  or or_4 (branch, and_4_out, and_5_out, BGE);
  and and_7 (BGE, alu_1_out_4, EX_BGE);
  Adder #(.width(32)) adder_2 (.a(bit_extender_2_out), .b(EX_PC), .out(EX_bxx_pc));  // open: cin, cout
  Adder #(.width(32)) adder_3 (.a(bit_extender_3_out), .b(EX_PC), .out(jal_pc));  // open: cin, cout
  \气泡流水线寄存器  \u_气泡流水线寄存器_1  (
    .SB(\重定向流水寄存器_2_sb_out ), .MemWrite(EX_MemWrite), .RegWrite(EX_RegWrite), .MemToReg(EX_MemToReg),
    .ecall(\重定向流水寄存器_2_ecall_out ), .JAL(EX_JAL), .JALR(EX_JALR), .PC(EX_PC), .Instr(EX_IR),
    .R1(multiplexer_7_out), .R2(EX_R2), .ALU(EX_ALU), .SB_out(MEM_SB), .MemWrite_out(MemWrite),
    .RegWrite_out(MEM_RegWrite), .MemToReg_out(MEM_MemToReg), .ecall_out(\气泡流水线寄存器_1_ecall_out ),
    .JAL_out(\气泡流水线寄存器_1_jal_out ), .JALR_out(\气泡流水线寄存器_1_jalr_out ), .PC_out(M_PC), .Instr_out(MEM_IR),
    .R1_out(\气泡流水线寄存器_1_r1_out ), .R2_out(MEM_R2), .ALU_out(MEM_addr), .Flush(1'b0), .Enable(1'b1),
    .clk(CLK), .WriteReg_num(EX_WriteReg_num), .WriteReg__out(MEM_WriteReg_num));  // open: ALU_src, ALU_op, BGE, BNE, BEQ, Imm, MemData, ALU_src_out, ALU_op_out, BGE_out, BNE_out, BEQ_out, Imm_out, MemData_out
  Decoder #(.select(2), .tristate("false"), .disabled("Z"), .enable("false")) decoder_1 (
    .out0(decoder_1_out0), .out1(decoder_1_out1), .out2(decoder_1_out2), .out3(decoder_1_out3),
    .sel(MEM_addr[1:0]));
  Multiplexer #(.select(1), .width(8), .disabled("Z"), .enable("false")) multiplexer_10 (
    .in0(mem_ld[7:0]), .in1(MEM_R2[7:0]), .out(sb_word[7:0]), .sel(decoder_1_out0));
  RAM #(.addrWidth(10), .dataWidth(32), .bus("separate"), .Select("high")) ram_1 (
    .addr(MEM_addr[11:2]), .din(MDin), .data(mem_ld), .str(MemWrite), .clk(CLK));  // open: sel, ld, clr
  Multiplexer #(.select(1), .width(8), .disabled("Z"), .enable("false")) multiplexer_11 (
    .in0(mem_ld[15:8]), .in1(MEM_R2[7:0]), .out(sb_word[15:8]), .sel(decoder_1_out1));
  Multiplexer #(.select(1), .width(8), .disabled("Z"), .enable("false")) multiplexer_12 (
    .in0(mem_ld[23:16]), .in1(MEM_R2[7:0]), .out(sb_word[23:16]), .sel(decoder_1_out2));
  not not_7 (not_7_out, halt);
  Multiplexer #(.select(1), .width(8), .disabled("Z"), .enable("false")) multiplexer_13 (
    .in0(mem_ld[31:24]), .in1(MEM_R2[7:0]), .out(sb_word[31:24]), .sel(decoder_1_out3));
  Counter #(.width(16), .max('hffff), .ongoal("wrap"), .trigger("rising"), .behavior("old")) counter_2 (
    .count(not_7_out), .Q(\总周期数 ), .clk(CLK));  // open: load, D, carry, clr, preset
  Multiplexer #(.select(1), .width(32), .disabled("Z"), .enable("false")) multiplexer_14 (
    .in0(MEM_R2), .in1(sb_word), .out(MDin), .sel(MEM_SB));
  \气泡流水线寄存器  \u_气泡流水线寄存器_2  (
    .RegWrite(MEM_RegWrite), .MemToReg(MEM_MemToReg), .ecall(\气泡流水线寄存器_1_ecall_out ),
    .JAL(\气泡流水线寄存器_1_jal_out ), .JALR(\气泡流水线寄存器_1_jalr_out ), .PC(M_PC), .Instr(MEM_IR),
    .R1(\气泡流水线寄存器_1_r1_out ), .R2(MEM_R2), .ALU(MEM_addr), .MemData(mem_ld), .RegWrite_out(RegWrite),
    .MemToReg_out(\气泡流水线寄存器_2_memtoreg_out ), .ecall_out(WB_ecall), .JAL_out(WB_JAL), .JALR_out(WB_JALR),
    .PC_out(WB_PC), .Instr_out(WB_IR), .R1_out(WB_R1), .R2_out(WB_R2), .ALU_out(WB_ALU),
    .MemData_out(\气泡流水线寄存器_2_memdata_out ), .Flush(1'b0), .Enable(1'b1), .clk(CLK),
    .WriteReg_num(MEM_WriteReg_num), .WriteReg__out(WB_WriteReg_num));  // open: ALU_src, ALU_op, BGE, BNE, BEQ, SB, MemWrite, Imm, ALU_src_out, ALU_op_out, BGE_out, BNE_out, BEQ_out, SB_out, MemWrite_out, Imm_out
  or or_5 (or_5_out, WB_JAL, WB_JALR);
  Multiplexer #(.select(1), .width(32), .disabled("Z"), .enable("false")) multiplexer_15 (
    .in0(WB_ALU), .in1(\气泡流水线寄存器_2_memdata_out ), .out(multiplexer_15_out), .sel(\气泡流水线寄存器_2_memtoreg_out ));
  Adder #(.width(32)) adder_4 (.a(WB_PC), .b(32'h4), .out(WB_PC_4));  // open: cin, cout
  Multiplexer #(.select(1), .width(32), .disabled("Z"), .enable("false")) multiplexer_16 (
    .in0(multiplexer_15_out), .in1(WB_PC_4), .out(RDin), .sel(or_5_out));
  Comparator #(.width(32), .mode("twosComplement")) comparator_2 (
    .a(WB_R1), .b(32'h22), .eq(comparator_2_eq));  // open: gt, lt
  and and_8 (and_8_out, WB_ecall, comparator_2_eq);
  and and_9 (and_9_out, ~comparator_2_eq, WB_ecall);  // AND_Gate
  or or_6 (or_6_out, Go, ~halt);  // OR_Gate
  Register #(.width(32), .trigger("rising"), .Select("low")) register_1 (
    .D(WB_R2), .en(and_8_out), .Q(LedData), .clk(CLK));  // open: clr
  Register #(.width(1), .trigger("rising"), .Select("low")) register_2 (
    .D(and_9_out), .en(or_6_out), .Q(halt), .clk(clock_2_out));  // open: clr
  Clock #(.highDuration(1), .lowDuration(1)) clock_2 (.out(clock_2_out));

  // Other names for the same wires on the sheet: ID_WriteReg_num[4:0] = ID_IR[11:7]; MEM_ALU[31:0] = MEM_addr;
  //   MEM_MemWrite = MemWrite; MEM_PC[31:0] = M_PC; WB_RegVal[31:0] = RDin; WB_RegWrite = RegWrite

  // Notes on the sheet:
  //   中断源
  //   时空图监测，可删除
  //   中断等待指示
  //   数码管输出
  //   指令存储器
  //   contents of rom_1 (hex, n*v repeats v):
  //   100493 100006f 100493 200913 300993 100006f 100493 200913 300993 100006f 100493 200913 300993
  //   100006f 100493 200913 300993 3ac000ef 100413 100493 1f49493 900533 2200893 73 24d493 48463 fedff06f
  //   900533 2200893 73 100493 249493 900533 2200893 73 48463 fedff06f 100493 1f49493 900533 2200893 73
  //   4034d493 900533 2200893 73 4044d493 900533 2200893 73 4044d493 900533 2200893 73 4044d493 900533
  //   2200893 73 4044d493 900533 2200893 73 4044d493 900533 2200893 73 4044d493 900533 2200893 73 4044d493
  //   900533 2200893 73 100413 1f41993 41f9d993 433 c00913 300b13 140413 f47413 800293 100313 499993
  //   89e9b3 1300533 2200893 73 406282b3 fe0294e3 140413 f00f93 1f47433 1c41413 800293 100313 49d993
  //   89e9b3 1300533 2200893 73 406282b3 fe0294e3 1c45413 406b0b33 b0463 f95ff06f 2b3 fff2c293 829293
  //   ff2e293 500533 2200893 73 fff00413 493 84a023 140413 448493 84a023 140413 448493 84a023 140413
  //   448493 84a023 140413 448493 84a023 140413 448493 84a023 140413 448493 84a023 140413 448493 84a023
  //   140413 448493 84a023 140413 448493 84a023 140413 448493 84a023 140413 448493 84a023 140413 448493
  //   84a023 140413 448493 84a023 140413 448493 84a023 140413 448493 84a023 140413 448493 140413 433
  //   3c00493 42983 4aa03 149a2b3 28663 134a023 1442023 ffc48493 fe9412e3 800533 2200893 73 440413 3c00493
  //   fc9416e3 3200893 73 100293 300313 800493 849493 7648493 900533 2200893 73 800e13 5494b3 6494b3
  //   900533 2200893 73 fffe0e13 fe0e14e3 a00893 73 100293 300313 800493 849493 7648493 1449493 900533
  //   2200893 73 800e13 4054d4b3 4064d4b3 900533 2200893 73 fffe0e13 fe0e14e3 a00893 73 313 2000e13 493
  //   100913 930023 900533 2200893 73 12484b3 130313 fffe0e13 fe0e12e3 800e13 313 32483 900533 2200893 73
  //   430313 fffe0e13 fe0e14e3 a00893 73 f00493 900533 2200893 73 fff48493 fe04d8e3 a00893 73 413 140413
  //   800533 2200893 73 240413 800533 2200893 73 340413 800533 2200893 73 440413 800533 2200893 73 540413
  //   800533 2200893 73 640413 800533 2200893 73 740413 800533 2200893 73 840413 800533 2200893 2200893 73
  //   8067
  //   IF/ ID
  //   指令字
  //   控制位
  //   流水调试日志用
  //   暂停节拍，不能为0
  //   MemToReg
  //   MemWrite
  //   AluOP
  //   AluSrcB
  //   RegWrite
  //   S_Type
  //   戳工具置1进入计数暂停模式，ctrl+k时钟自动运行到对应节拍暂停
  //   ctrl+k关闭时钟连续运行，将控制位置零，进入单步调试模式调试
  //   可计数暂停的时钟源
  //   ID / EX
  //   为方便自动评测，需要输出流水线各段保存的PC值，注意是PC不是PC+4，另外ID段寄存器写入信息，Mem段内存写入信息也要输出
  //   EX / MEM
  //   数据存储器
  //   MEM / WB
endmodule

module \中断按键参考电路  (
  input  CLK,
  input  IR,
  input  reset,
  output \与中断屏蔽位与 ,
  output \wait 
);

  wire and_1_out, d_ff_1_q, or_2_out;

  or or_1 (\wait , \与中断屏蔽位与 , d_ff_1_q);
  D_Flip_Flop #(.trigger("rising"), .Pre_Clr_Positions("LEGACY"), .NegatePresetClear("false"), .enable("true"), .NewFFLayout("false")) d_ff_1 (
    .clk(IR), .D(1'b1), .Q(d_ff_1_q), .reset(\与中断屏蔽位与 ));  // open: Qn, preset, en
  or or_2 (or_2_out, d_ff_1_q, \与中断屏蔽位与 );
  and and_1 (and_1_out, or_2_out, ~reset);  // AND_Gate
  Pull_Resistor #(.pull(0)) pull_resistor_1 (.node(reset));
  D_Flip_Flop #(.trigger("rising"), .Pre_Clr_Positions("LEGACY"), .NegatePresetClear("false"), .enable("true"), .NewFFLayout("false")) IR1 (
    .clk(CLK), .D(and_1_out), .Q(\与中断屏蔽位与 ));  // open: Qn, preset, en, reset

  // Notes on the sheet:
  //   中断信号采样参考电路
  //   Reset 
endmodule
module \单周期_单级中断  (
  input  IR1,
  input  IR2,
  input  IR3,
  output RegWrite,
  output MemWrite,
  output [31:0] PC,
  output [31:0] IR,
  output [31:0] RDin,
  output [31:0] MDin,
  output [31:0] LedData
);

  wire alu_1_equal, alu_1_out_4, and_6_out, and_7_out, beq, bge, bge_ctrl, bne, branch, CLK, clock_1_out,
       comparator_2_eq, comparator_3_eq, comparator_4_eq, comparator_5_eq, comparator_6_eq, comparator_6_lt,
       comparator_7_eq, d_ff_1_qn, d_ff_2_q, decoder_2_out0, decoder_2_out1, decoder_2_out2, decoder_2_out3,
       ecall, Go, halt, INT_SIG, IR1_t, IR2_t, IR3_t, IRA, IRB, IRC, Jxx_ctrl, nand_1_out, not_1_out,
       not_2_out, or_2_out, or_7_out, priority_encoder_1_gs, riscv_probe_1_p2, riscv_probe_1_p3, RST, RST1,
       RST2, RST3, sb, uret, W1, W2, W3, \中断按键参考电路_1_与中断屏蔽位与 , \中断按键参考电路_2_与中断屏蔽位与 , \中断按键参考电路_3_与中断屏蔽位与 ,
       \单周期硬布线控制器_1_alu_src , \单周期硬布线控制器_1_beq , \单周期硬布线控制器_1_bne , \单周期硬布线控制器_1_jal , \单周期硬布线控制器_1_jalr ,
       \单周期硬布线控制器_1_memtoreg , \单周期硬布线控制器_1_s_type ;
  wire [1:0] priority_encoder_1_out, register_1_q;
  wire [3:0] \单周期硬布线控制器_1_alu_op ;
  wire [4:0] multiplexer_7_out, multiplexer_8_out;
  wire [11:0] multiplexer_9_out;
  wire [12:0] CNT_num;
  wire [15:0] \总周期数 ;
  wire [31:0] ALU_out, bit_extender_1_out, bit_extender_2_out, bit_extender_3_out, bxx_pc, INT_Handle,
       jal_pc, jalr_pc, mem_ld, mEPC, multiplexer_1_out, multiplexer_2_out, multiplexer_4_out,
       multiplexer_5_out, multiplexer_10_out, multiplexer_11_out, nextPC, PC_4, R1_out, R2_out, sb_word;

  Button \u_继续运行  (.out(Go));
  Button _1 ();  // open: out
  Button _2 ();  // open: out
  Button _3 ();  // open: out
  or or_1 (Jxx_ctrl, \单周期硬布线控制器_1_jal , \单周期硬布线控制器_1_jalr );
  LED #(.active("true")) led_1 (.in(W1));
  LED #(.active("true")) led_2 (.in(W2));
  LED #(.active("true")) led_3 (.in(W3));
  Multiplexer #(.select(1), .width(32), .disabled("Z"), .enable("false")) multiplexer_1 (
    .in0(PC_4), .in1(bxx_pc), .out(multiplexer_1_out), .sel(branch));
  Multiplexer #(.select(1), .width(32), .disabled("Z"), .enable("false")) multiplexer_2 (
    .in0(multiplexer_1_out), .in1(jal_pc), .out(multiplexer_2_out), .sel(\单周期硬布线控制器_1_jal ));
  Hex_Digit_Display hex_digit_display_1 (.value(LedData[31:28]));  // open: dp
  \中断按键参考电路  \u_中断按键参考电路_1  (.\与中断屏蔽位与 (\中断按键参考电路_1_与中断屏蔽位与 ), .reset(RST1), .CLK(CLK), .IR(IR1_t), .\wait (W1));
  \中断按键参考电路  \u_中断按键参考电路_2  (.\与中断屏蔽位与 (\中断按键参考电路_2_与中断屏蔽位与 ), .reset(RST2), .CLK(CLK), .IR(IR2_t), .\wait (W2));
  \中断按键参考电路  \u_中断按键参考电路_3  (.\与中断屏蔽位与 (\中断按键参考电路_3_与中断屏蔽位与 ), .reset(RST3), .CLK(CLK), .IR(IR3_t), .\wait (W3));
  Multiplexer #(.select(1), .width(32), .disabled("Z"), .enable("false")) multiplexer_3 (
    .in0(multiplexer_2_out), .in1(jalr_pc), .out(nextPC), .sel(\单周期硬布线控制器_1_jalr ));
  Hex_Digit_Display hex_digit_display_2 (.value(LedData[23:20]));  // open: dp
  Hex_Digit_Display hex_digit_display_3 (.value(LedData[27:24]));  // open: dp
  D_Flip_Flop #(.trigger("rising"), .Pre_Clr_Positions("LEGACY"), .NegatePresetClear("false"), .enable("true"), .NewFFLayout("false")) d_ff_1 (
    .clk(CLK), .D(INT_SIG), .Qn(d_ff_1_qn), .en(or_2_out));  // open: Q, preset, reset
  or or_2 (or_2_out, uret, INT_SIG);
  Multiplexer #(.select(1), .width(32), .disabled("Z"), .enable("false")) multiplexer_4 (
    .in0(nextPC), .in1(mEPC), .out(multiplexer_4_out), .sel(uret));
  Multiplexer #(.select(1), .width(32), .disabled("Z"), .enable("false")) multiplexer_5 (
    .in0(multiplexer_4_out), .in1(INT_Handle), .out(multiplexer_5_out), .sel(INT_SIG));
  not not_1 (not_1_out, halt);
  Hex_Digit_Display hex_digit_display_4 (.value(LedData[15:12]));  // open: dp
  Hex_Digit_Display hex_digit_display_5 (.value(LedData[19:16]));  // open: dp
  Priority_Encoder #(.select(2), .disabled("Z")) priority_encoder_1 (
    .in0(\中断按键参考电路_1_与中断屏蔽位与 ), .in1(\中断按键参考电路_2_与中断屏蔽位与 ), .in2(\中断按键参考电路_3_与中断屏蔽位与 ),
    .out(priority_encoder_1_out), .gs(priority_encoder_1_gs));  // open: in3, en_out, en_in
  not not_2 (not_2_out, halt);
  Register #(.width(32), .trigger("rising"), .Select("low")) u_PC (
    .D(multiplexer_5_out), .en(not_1_out), .Q(PC), .clk(CLK), .clr(RST));
  Hex_Digit_Display hex_digit_display_6 (.value(LedData[7:4]));  // open: dp
  Hex_Digit_Display hex_digit_display_7 (.value(LedData[11:8]));  // open: dp
  // Probe on \总周期数 
  Multiplexer #(.select(2), .width(32), .disabled("Z"), .enable("false")) multiplexer_6 (
    .in0(32'h30ac), .in1(32'h3150), .in2(32'h31f4), .out(INT_Handle), .sel(priority_encoder_1_out));  // open: in3
  and and_1 (INT_SIG, priority_encoder_1_gs, d_ff_1_qn);
  Counter #(.width(16), .max('hffff), .ongoal("wrap"), .trigger("rising"), .behavior("old")) counter_1 (
    .count(not_2_out), .Q(\总周期数 ), .clk(CLK));  // open: load, D, carry, clr, preset
  Adder #(.width(32)) adder_1 (.a(PC), .b(32'h4), .out(PC_4));  // open: cin, cout
  Hex_Digit_Display hex_digit_display_8 (.value(LedData[3:0]));  // open: dp
  Register #(.width(2), .trigger("rising"), .Select("low")) register_1 (
    .D(priority_encoder_1_out), .en(INT_SIG), .Q(register_1_q), .clk(CLK));  // open: clr
  Register #(.width(32), .trigger("rising"), .Select("low")) u_mEPC (
    .D(nextPC), .en(INT_SIG), .Q(mEPC), .clk(CLK));  // open: clr
  // RiscV_Probe riscv_probe_1: pin names not known; wires that end beside it: IR, riscv_probe_1_p2, riscv_probe_1_p3, riscv_probe_1_p3
  ROM #(.addrWidth(10), .dataWidth(32), .Select("high")) rom_1 (.addr(PC[11:2]), .data(IR));
  Decoder #(.select(2), .tristate("false"), .disabled("Z"), .enable("true")) decoder_1 (
    .out0(RST1), .out1(RST2), .out2(RST3), .sel(register_1_q), .en(uret));  // open: out3
  or or_3 (IR1_t, IR1, IRA);
  \单周期硬布线控制器  \u_单周期硬布线控制器_1  (
    .Funct({IR[30], IR[25], IR[14:12]}), .OP(IR[6:2]), .ALU_OP(\单周期硬布线控制器_1_alu_op ),
    .MemToReg(\单周期硬布线控制器_1_memtoreg ), .MemWrite(MemWrite), .ALU_SRC(\单周期硬布线控制器_1_alu_src ),
    .RegWrite(RegWrite), .ecall(ecall), .S_type(\单周期硬布线控制器_1_s_type ), .Jalr(\单周期硬布线控制器_1_jalr ),
    .Beq(\单周期硬布线控制器_1_beq ), .JAL(\单周期硬布线控制器_1_jal ), .Bne(\单周期硬布线控制器_1_bne ), .in_3(IR[21]),
    .uret(riscv_probe_1_p2), .sb(sb), .bge(bge_ctrl));
  Multiplexer #(.select(1), .width(5), .disabled("Z"), .enable("false")) multiplexer_7 (
    .in0(IR[19:15]), .in1(5'b10001), .out(multiplexer_7_out), .sel(ecall));
  Multiplexer #(.select(1), .width(5), .disabled("Z"), .enable("false")) multiplexer_8 (
    .in0(IR[24:20]), .in1(5'b01010), .out(multiplexer_8_out), .sel(ecall));
  Comparator #(.width(32), .mode("twosComplement")) comparator_1 (.a(IR), .b(32'h200073), .eq(uret));  // open: gt, lt
  or or_4 (IR2_t, IR2, IRB);
  Multiplexer #(.select(1), .width(12), .disabled("Z"), .enable("false")) multiplexer_9 (
    .in0(IR[31:20]), .in1({IR[31:25], IR[11:7]}), .out(multiplexer_9_out), .sel(\单周期硬布线控制器_1_s_type ));
  assign bit_extender_1_out = {{19{IR[31]}}, {IR[31], IR[7], IR[30:25], IR[11:8], 1'b0}};  // Bit_Extender bit_extender_1
  assign bit_extender_2_out = {{11{IR[31]}}, {IR[31], IR[19:12], IR[20], IR[30:21], 1'b0}};  // Bit_Extender bit_extender_2
  Regifile regifile_1 (
    .Din(RDin), .Clk(CLK), .R1(R1_out), .R2(R2_out), .WE(RegWrite), .W_num(IR[11:7]),
    .R1_num(multiplexer_7_out), .R2_num(multiplexer_8_out));
  assign bit_extender_3_out = {{20{multiplexer_9_out[11]}}, multiplexer_9_out};  // Bit_Extender bit_extender_3
  or or_5 (IR3_t, IR3, IRC);
  Multiplexer #(.select(1), .width(32), .disabled("Z"), .enable("false")) multiplexer_10 (
    .in0(R2_out), .in1(bit_extender_3_out), .out(multiplexer_10_out), .sel(\单周期硬布线控制器_1_alu_src ));
  Adder #(.width(32)) adder_2 (.a(bit_extender_1_out), .b(PC), .out(bxx_pc));  // open: cin, cout
  Adder #(.width(32)) adder_3 (.a(bit_extender_2_out), .b(PC), .out(jal_pc));  // open: cin, cout
  or or_6 (branch, beq, bne, bge);
  and and_2 (beq, \单周期硬布线控制器_1_beq , alu_1_equal);
  and and_3 (bne, \单周期硬布线控制器_1_bne , ~alu_1_equal);  // AND_Gate
  ALU alu_1 (
    .X(R1_out), .Y(multiplexer_10_out), .AluOP(\单周期硬布线控制器_1_alu_op ), .Equal(alu_1_equal), .Result(ALU_out),
    .out_4(alu_1_out_4));  // open: Result_2, out_6
  and and_4 (bge, alu_1_out_4, bge_ctrl);
  assign jalr_pc = ALU_out & ~32'h1;  // AND_Gate and_5, 32 bits wide
  Comparator #(.width(16), .mode("twosComplement")) comparator_2 (
    .a(16'h23b), .b(\总周期数 ), .eq(comparator_2_eq));  // open: gt, lt
  Comparator #(.width(16), .mode("twosComplement")) comparator_3 (
    .a(\总周期数 ), .b(16'h1), .eq(comparator_3_eq));  // open: gt, lt
  Comparator #(.width(16), .mode("twosComplement")) comparator_4 (
    .a(\总周期数 ), .b(16'h4), .eq(comparator_4_eq));  // open: gt, lt
  Comparator #(.width(16), .mode("twosComplement")) comparator_5 (
    .a(\总周期数 ), .b(16'h7), .eq(comparator_5_eq));  // open: gt, lt
  RAM #(.addrWidth(10), .dataWidth(32), .bus("separate"), .Select("high")) ram_1 (
    .addr(ALU_out[11:2]), .din(MDin), .data(mem_ld), .str(MemWrite), .clk(CLK));  // open: sel, ld, clr
  or or_7 (or_7_out, comparator_2_eq, comparator_3_eq);
  assign IRA = or_7_out ? ~CLK : 1'bz;  // Controlled_Inverter controlled_inverter_1
  assign IRB = comparator_4_eq ? ~CLK : 1'bz;  // Controlled_Inverter controlled_inverter_2
  assign IRC = comparator_5_eq ? ~CLK : 1'bz;  // Controlled_Inverter controlled_inverter_3
  Multiplexer #(.select(1), .width(32), .disabled("Z"), .enable("false")) multiplexer_11 (
    .in0(ALU_out), .in1(mem_ld), .out(multiplexer_11_out), .sel(\单周期硬布线控制器_1_memtoreg ));
  D_Flip_Flop #(.trigger("high"), .Pre_Clr_Positions("LEGACY"), .NegatePresetClear("false"), .enable("true"), .NewFFLayout("false")) d_ff_2 (.Q(d_ff_2_q));  // open: clk, D, Qn, preset, en, reset
  // Probe on 13'hc
  Pull_Resistor #(.pull(0)) pull_resistor_1 (.node(IRA));
  Pull_Resistor #(.pull(0)) pull_resistor_2 (.node(IRB));
  Pull_Resistor #(.pull(0)) pull_resistor_3 (.node(IRC));
  Multiplexer #(.select(1), .width(32), .disabled("Z"), .enable("false")) multiplexer_12 (
    .in0(multiplexer_11_out), .in1(PC_4), .out(RDin), .sel(Jxx_ctrl));
  Comparator #(.width(13), .mode("twosComplement")) comparator_6 (
    .a(CNT_num), .b(13'hc), .eq(comparator_6_eq), .lt(comparator_6_lt));  // open: gt
  Clock #(.highDuration(1), .lowDuration(1)) clock_1 (.out(clock_1_out));
  Counter #(.width(13), .max('h1fff), .ongoal("stay"), .trigger("rising"), .behavior("old")) counter_2 (
    .count(comparator_6_lt), .Q(CNT_num), .clk(clock_1_out));  // open: load, D, carry, clr, preset
  Comparator #(.width(32), .mode("twosComplement")) comparator_7 (
    .a(R1_out), .b(32'h22), .eq(comparator_7_eq));  // open: gt, lt
  nand nand_1 (nand_1_out, d_ff_2_q, comparator_6_eq);
  Decoder #(.select(2), .tristate("false"), .disabled("Z"), .enable("false")) decoder_2 (
    .out0(decoder_2_out0), .out1(decoder_2_out1), .out2(decoder_2_out2), .out3(decoder_2_out3),
    .sel(ALU_out[1:0]));
  assign CLK = nand_1_out ? clock_1_out : 1'bz;  // Controlled_Buffer controlled_buffer_1
  Pull_Resistor #(.pull(1)) pull_resistor_4 (.node(CLK));
  and and_6 (and_6_out, ecall, comparator_7_eq);
  and and_7 (and_7_out, ~comparator_7_eq, ecall);  // AND_Gate
  Register #(.width(32), .trigger("rising"), .Select("low")) register_2 (
    .D(R2_out), .en(and_6_out), .Q(LedData), .clk(CLK));  // open: clr
  and and_8 (halt, and_7_out, ~Go);  // AND_Gate
  Multiplexer #(.select(1), .width(8), .disabled("Z"), .enable("false")) multiplexer_13 (
    .in0(mem_ld[7:0]), .in1(R2_out[7:0]), .out(sb_word[7:0]), .sel(decoder_2_out0));
  Multiplexer #(.select(1), .width(8), .disabled("Z"), .enable("false")) multiplexer_14 (
    .in0(mem_ld[15:8]), .in1(R2_out[7:0]), .out(sb_word[15:8]), .sel(decoder_2_out1));
  Multiplexer #(.select(1), .width(32), .disabled("Z"), .enable("false")) multiplexer_15 (
    .in0(R2_out), .in1(sb_word), .out(MDin), .sel(sb));
  Multiplexer #(.select(1), .width(8), .disabled("Z"), .enable("false")) multiplexer_16 (
    .in0(mem_ld[23:16]), .in1(R2_out[7:0]), .out(sb_word[23:16]), .sel(decoder_2_out2));
  Multiplexer #(.select(1), .width(8), .disabled("Z"), .enable("false")) multiplexer_17 (
    .in0(mem_ld[31:24]), .in1(R2_out[7:0]), .out(sb_word[31:24]), .sel(decoder_2_out3));

  // Other names for the same wires on the sheet: mem_addr[31:0] = ALU_out

  // Notes on the sheet:
  //   中断源
  //   中断等待指示
  //   总复位信号应将除ROM以外所有存储组件全部清零
  //   数码管输出
  //   数码管输出应该用寄存器锁存，否则显示数据只能一闪而过
  //   指令探针
  //   指令存储器
  //   指令字
  //   contents of rom_1 (hex, n*v repeats v):
  //   7d000113 100413 1f41993 41f9d993 433 c00913 800b13 140413 f47413 800293 100313 499993 89e9b3 1300533
  //   2200893 73 406282b3 fe0294e3 140413 f00f93 1f47433 1c41413 800293 100313 49d993 89e9b3 1300533
  //   2200893 73 406282b3 fe0294e3 1c45413 406b0b33 b0463 f95ff06f 2b3 fff2c293 1029293 fff2e293 500533
  //   2200893 73 f5dff06f 1112023 410113 a12023 410113 812023 410113 1312023 410113 1412023 410113 1512023
  //   410113 1612023 410113 100b13 300a13 100a93 1600433 441413 14469b3 1300533 2200893 73 fe0416e3
  //   415a0a33 fe0a10e3 ffc10113 12b03 ffc10113 12a83 ffc10113 12a03 ffc10113 12983 ffc10113 12403
  //   ffc10113 12503 ffc10113 12883 200073 1112023 410113 a12023 410113 812023 410113 1312023 410113
  //   1412023 410113 1512023 410113 1612023 410113 200b13 300a13 100a93 1600433 441413 14469b3 1300533
  //   2200893 73 fe0416e3 415a0a33 fe0a10e3 ffc10113 12b03 ffc10113 12a83 ffc10113 12a03 ffc10113 12983
  //   ffc10113 12403 ffc10113 12503 ffc10113 12883 200073 1112023 410113 a12023 410113 812023 410113
  //   1312023 410113 1412023 410113 1512023 410113 1612023 410113 300b13 300a13 100a93 1600433 441413
  //   14469b3 1300533 2200893 73 fe0416e3 415a0a33 fe0a10e3 ffc10113 12b03 ffc10113 12a83 ffc10113 12a03
  //   ffc10113 12983 ffc10113 12403 ffc10113 12503 ffc10113 12883 200073
  //   JAL
  //   JALR
  //   URET
  //   Beq
  //   Bne
  //   AluOP
  //   AluSrcB
  //   RegWrite
  //   S_Type
  //   sb
  //   bge
  //   MemToReg
  //   MemWrite
  //   为方便自动评测，需要输出PC，IR，寄存器堆写如数据RDin
  //   RAM写使能MemWrite、RAM写入数据MDin等信号
  //   单级中断测试信号模拟器
  //   数据存储器
  //   控制位
  //   暂停节拍，不能为0
  //   戳工具置1进入计数暂停模式，ctrl+k时钟自动运行到对应节拍暂停
  //   ctrl+k关闭时钟连续运行，将控制位置零，进入单步调试模式调试
  //   可计数暂停的时钟源
endmodule

module \单周期_多级中断  (
  input  IR1,
  input  IR2,
  input  IR3,
  output RegWrite,
  output MemWrite,
  output [31:0] PC,
  output [31:0] IR,
  output [31:0] RDin,
  output [31:0] MDin,
  output [31:0] LedData
);

  wire alu_1_equal, alu_1_out_4, and_2_out, and_3_out, and_4_out, and_11_out, and_12_out, beq, bge, bge_ctrl,
       bne, branch, CLK, clock_1_out, comparator_1_eq, comparator_2_eq, comparator_3_eq, comparator_4_eq,
       comparator_5_eq, comparator_7_eq, comparator_8_eq, comparator_9_eq, comparator_10_eq,
       comparator_10_lt, comparator_11_eq, csrrci, csrrsi, d_ff_1_q, d_ff_2_q, decoder_2_out0,
       decoder_2_out1, decoder_2_out2, decoder_2_out3, ecall, Go, halt, INT_SIG, IR1_t, IR2_t, IR3_t, IRA,
       IRB, IRC, Jxx_ctrl, nand_1_out, not_1_out, not_2_out, or_2_out, or_3_out, or_6_out, or_8_out,
       or_10_out, priority_encoder_1_gs, pull_resistor_1_node, pull_resistor_2_node, pull_resistor_3_node,
       riscv_probe_1_p2, riscv_probe_1_p3, RST, RST1, RST2, RST3, sb, uret, W1, W2, W3, \中断按键参考电路_1_与中断屏蔽位与 ,
       \中断按键参考电路_2_与中断屏蔽位与 , \中断按键参考电路_3_与中断屏蔽位与 , \单周期硬布线控制器_1_alu_src , \单周期硬布线控制器_1_beq ,
       \单周期硬布线控制器_1_bne , \单周期硬布线控制器_1_jal , \单周期硬布线控制器_1_jalr , \单周期硬布线控制器_1_memtoreg , \单周期硬布线控制器_1_s_type ;
  wire [1:0] IntID, IntID2_q, IntID3_q, multiplexer_15_out, multiplexer_17_out, multiplexer_23_out, nextInt;
  wire [2:0] multiplexer_8_out;
  wire [3:0] \单周期硬布线控制器_1_alu_op ;
  wire [4:0] multiplexer_6_out, multiplexer_7_out;
  wire [11:0] multiplexer_9_out;
  wire [12:0] CNT_num;
  wire [15:0] \总周期数 ;
  wire [31:0] ALU_out, bit_extender_1_out, bit_extender_2_out, bit_extender_3_out, bxx_pc, EPC2_q, EPC3_q,
       INT_Handle, jal_pc, jalr_pc, mem_ld, mEPC, multiplexer_1_out, multiplexer_2_out, multiplexer_4_out,
       multiplexer_5_out, multiplexer_10_out, multiplexer_12_out, multiplexer_14_out, multiplexer_16_out,
       multiplexer_22_out, nextPC, PC_4, R1_out, R2_out, sb_word, undriven;

  Button \u_继续运行  (.out(Go));
  Button _1 (.out(IRA));
  Button _2 (.out(IRB));
  Button _3 (.out(IRC));
  LED #(.active("true")) led_1 (.in(W1));
  LED #(.active("true")) led_2 (.in(W2));
  LED #(.active("true")) led_3 (.in(W3));
  or or_1 (Jxx_ctrl, \单周期硬布线控制器_1_jal , \单周期硬布线控制器_1_jalr );
  Multiplexer #(.select(1), .width(32), .disabled("Z"), .enable("false")) multiplexer_1 (
    .in0(PC_4), .in1(bxx_pc), .out(multiplexer_1_out), .sel(branch));
  Hex_Digit_Display hex_digit_display_1 (.value(LedData[31:28]));  // open: dp
  Multiplexer #(.select(1), .width(32), .disabled("Z"), .enable("false")) multiplexer_2 (
    .in0(multiplexer_1_out), .in1(jal_pc), .out(multiplexer_2_out), .sel(\单周期硬布线控制器_1_jal ));
  Hex_Digit_Display hex_digit_display_2 (.value(LedData[27:24]));  // open: dp
  Hex_Digit_Display hex_digit_display_3 (.value(LedData[23:20]));  // open: dp
  Multiplexer #(.select(1), .width(32), .disabled("Z"), .enable("false")) multiplexer_3 (
    .in0(multiplexer_2_out), .in1(jalr_pc), .out(nextPC), .sel(\单周期硬布线控制器_1_jalr ));
  Multiplexer #(.select(1), .width(32), .disabled("Z"), .enable("false")) multiplexer_4 (
    .in0(nextPC), .in1(mEPC), .out(multiplexer_4_out), .sel(uret));
  Hex_Digit_Display hex_digit_display_4 (.value(LedData[15:12]));  // open: dp
  Hex_Digit_Display hex_digit_display_5 (.value(LedData[19:16]));  // open: dp
  Comparator #(.width(16), .mode("twosComplement")) comparator_1 (
    .a(16'h258), .b(\总周期数 ), .eq(comparator_1_eq));  // open: gt, lt
  Comparator #(.width(16), .mode("twosComplement")) comparator_2 (
    .a(\总周期数 ), .b(16'h1), .eq(comparator_2_eq));  // open: gt, lt
  Comparator #(.width(16), .mode("twosComplement")) comparator_3 (
    .a(\总周期数 ), .b(16'h4), .eq(comparator_3_eq));  // open: gt, lt
  Comparator #(.width(16), .mode("twosComplement")) comparator_4 (
    .a(\总周期数 ), .b(16'h7), .eq(comparator_4_eq));  // open: gt, lt
  or or_2 (or_2_out, comparator_4_eq, comparator_5_eq);
  Comparator #(.width(16), .mode("twosComplement")) comparator_5 (
    .a(\总周期数 ), .b(16'h241), .eq(comparator_5_eq));  // open: gt, lt
  Multiplexer #(.select(1), .width(32), .disabled("Z"), .enable("false")) multiplexer_5 (
    .in0(multiplexer_4_out), .in1(INT_Handle), .out(multiplexer_5_out), .sel(INT_SIG));
  not not_1 (not_1_out, halt);
  Hex_Digit_Display hex_digit_display_6 (.value(LedData[7:4]));  // open: dp
  Hex_Digit_Display hex_digit_display_7 (.value(LedData[11:8]));  // open: dp
  // Probe on \总周期数 
  or or_3 (or_3_out, comparator_1_eq, comparator_2_eq);
  Pull_Resistor #(.pull(0)) pull_resistor_1 (.node(pull_resistor_1_node));
  assign pull_resistor_1_node = or_3_out ? ~CLK : 1'bz;  // Controlled_Inverter controlled_inverter_1
  Pull_Resistor #(.pull(0)) pull_resistor_2 (.node(pull_resistor_2_node));
  assign pull_resistor_2_node = comparator_3_eq ? ~CLK : 1'bz;  // Controlled_Inverter controlled_inverter_2
  Pull_Resistor #(.pull(0)) pull_resistor_3 (.node(pull_resistor_3_node));
  assign pull_resistor_3_node = or_2_out ? ~CLK : 1'bz;  // Controlled_Inverter controlled_inverter_3
  Counter #(.width(16), .max('hffff), .ongoal("wrap"), .trigger("rising"), .behavior("old")) counter_1 (
    .count(not_2_out), .Q(\总周期数 ), .clk(CLK));  // open: load, D, carry, clr, preset
  not not_2 (not_2_out, halt);
  Register #(.width(32), .trigger("rising"), .Select("low")) u_PC (
    .D(multiplexer_5_out), .en(not_1_out), .Q(PC), .clk(CLK), .clr(RST));
  Hex_Digit_Display hex_digit_display_8 (.value(LedData[3:0]));  // open: dp
  // RiscV_Probe riscv_probe_1: pin names not known; wires that end beside it: IR, riscv_probe_1_p2, riscv_probe_1_p3, riscv_probe_1_p3
  Adder #(.width(32)) adder_1 (.a(PC), .b(32'h4), .out(PC_4));  // open: cin, cout
  ROM #(.addrWidth(10), .dataWidth(32), .Select("high")) rom_1 (.addr(PC[11:2]), .data(IR));
  or or_4 (IR1_t, IR1, IRA);
  \中断按键参考电路  \u_中断按键参考电路_1  (.\与中断屏蔽位与 (\中断按键参考电路_1_与中断屏蔽位与 ), .reset(RST1), .CLK(CLK), .IR(IR1_t), .\wait (W1));
  \中断按键参考电路  \u_中断按键参考电路_2  (.\与中断屏蔽位与 (\中断按键参考电路_2_与中断屏蔽位与 ), .reset(RST2), .CLK(CLK), .IR(IR2_t), .\wait (W2));
  \中断按键参考电路  \u_中断按键参考电路_3  (.\与中断屏蔽位与 (\中断按键参考电路_3_与中断屏蔽位与 ), .reset(RST3), .CLK(CLK), .IR(IR3_t), .\wait (W3));
  Comparator #(.width(32), .mode("twosComplement")) comparator_6 (.a(IR), .b(32'h200073), .eq(uret));  // open: gt, lt
  or or_5 (IR2_t, IR2, IRB);
  \单周期硬布线控制器  \u_单周期硬布线控制器_1  (
    .Funct({IR[30], IR[25], IR[14:12]}), .OP(IR[6:2]), .ALU_OP(\单周期硬布线控制器_1_alu_op ),
    .MemToReg(\单周期硬布线控制器_1_memtoreg ), .MemWrite(MemWrite), .ALU_SRC(\单周期硬布线控制器_1_alu_src ),
    .RegWrite(RegWrite), .ecall(ecall), .S_type(\单周期硬布线控制器_1_s_type ), .Jalr(\单周期硬布线控制器_1_jalr ),
    .Beq(\单周期硬布线控制器_1_beq ), .JAL(\单周期硬布线控制器_1_jal ), .Bne(\单周期硬布线控制器_1_bne ), .in_3(IR[21]),
    .uret(riscv_probe_1_p2), .sb(sb), .bge(bge_ctrl));
  Multiplexer #(.select(1), .width(5), .disabled("Z"), .enable("false")) multiplexer_6 (
    .in0(IR[19:15]), .in1(5'b10001), .out(multiplexer_6_out), .sel(ecall));
  Multiplexer #(.select(1), .width(5), .disabled("Z"), .enable("false")) multiplexer_7 (
    .in0(IR[24:20]), .in1(5'b01010), .out(multiplexer_7_out), .sel(ecall));
  Comparator #(.width(7), .mode("twosComplement")) comparator_7 (
    .a(IR[6:0]), .b(7'b1110011), .eq(comparator_7_eq));  // open: gt, lt
  Multiplexer #(.select(2), .width(3), .disabled("Z"), .enable("false")) multiplexer_8 (
    .in0(3'b000), .in1(3'b001), .in2(3'b011), .in3(3'b111), .out(multiplexer_8_out), .sel(IntID));
  or or_6 (or_6_out, csrrci, INT_SIG);
  Multiplexer #(.select(1), .width(12), .disabled("Z"), .enable("false")) multiplexer_9 (
    .in0(IR[31:20]), .in1({IR[31:25], IR[11:7]}), .out(multiplexer_9_out), .sel(\单周期硬布线控制器_1_s_type ));
  assign bit_extender_1_out = {{19{IR[31]}}, {IR[31], IR[7], IR[30:25], IR[11:8], 1'b0}};  // Bit_Extender bit_extender_1
  assign bit_extender_2_out = {{11{IR[31]}}, {IR[31], IR[19:12], IR[20], IR[30:21], 1'b0}};  // Bit_Extender bit_extender_2
  and and_1 (csrrci, comparator_7_eq, comparator_8_eq);
  Comparator #(.width(3), .mode("twosComplement")) comparator_8 (
    .a(IR[14:12]), .b(3'b111), .eq(comparator_8_eq));  // open: gt, lt
  Comparator #(.width(3), .mode("twosComplement")) comparator_9 (
    .a(IR[14:12]), .b(3'b110), .eq(comparator_9_eq));  // open: gt, lt
  or or_7 (IR3_t, IR3, IRC);
  and and_2 (and_2_out, \中断按键参考电路_2_与中断屏蔽位与 , ~multiplexer_8_out[1]);  // AND_Gate
  and and_3 (and_3_out, \中断按键参考电路_3_与中断屏蔽位与 , ~multiplexer_8_out[2]);  // AND_Gate
  D_Flip_Flop #(.trigger("rising"), .Pre_Clr_Positions("LEGACY"), .NegatePresetClear("false"), .enable("true"), .NewFFLayout("false")) d_ff_1 (
    .clk(CLK), .D(or_6_out), .Q(d_ff_1_q), .en(or_8_out));  // open: Qn, preset, reset
  or or_8 (or_8_out, uret, INT_SIG, csrrsi, csrrci);
  Regifile regifile_1 (
    .Din(RDin), .Clk(CLK), .R1(R1_out), .R2(R2_out), .WE(RegWrite), .W_num(IR[11:7]),
    .R1_num(multiplexer_6_out), .R2_num(multiplexer_7_out));
  assign bit_extender_3_out = {{20{multiplexer_9_out[11]}}, multiplexer_9_out};  // Bit_Extender bit_extender_3
  Adder #(.width(32)) adder_2 (.a(bit_extender_1_out), .b(PC), .out(bxx_pc));  // open: cin, cout
  Adder #(.width(32)) adder_3 (.a(bit_extender_2_out), .b(PC), .out(jal_pc));  // open: cin, cout
  and and_4 (and_4_out, \中断按键参考电路_1_与中断屏蔽位与 , ~multiplexer_8_out[0]);  // AND_Gate
  Multiplexer #(.select(1), .width(32), .disabled("Z"), .enable("false")) multiplexer_10 (
    .in0(R2_out), .in1(bit_extender_3_out), .out(multiplexer_10_out), .sel(\单周期硬布线控制器_1_alu_src ));
  or or_9 (branch, beq, bne, bge);
  ALU alu_1 (
    .X(R1_out), .Y(multiplexer_10_out), .AluOP(\单周期硬布线控制器_1_alu_op ), .Equal(alu_1_equal), .Result(ALU_out),
    .out_4(alu_1_out_4));  // open: Result_2, out_6
  and and_5 (csrrsi, comparator_7_eq, comparator_9_eq);
  Priority_Encoder #(.select(2), .disabled("Z")) priority_encoder_1 (
    .in1(and_4_out), .in2(and_2_out), .in3(and_3_out), .out(nextInt), .gs(priority_encoder_1_gs));  // open: in0, en_out, en_in
  and and_6 (INT_SIG, priority_encoder_1_gs, ~d_ff_1_q);  // AND_Gate
  and and_7 (beq, \单周期硬布线控制器_1_beq , alu_1_equal);
  and and_8 (bne, \单周期硬布线控制器_1_bne , ~alu_1_equal);  // AND_Gate
  and and_9 (bge, alu_1_out_4, bge_ctrl);
  Multiplexer #(.select(2), .width(32), .disabled("Z"), .enable("false")) multiplexer_11 (
    .in0(undriven), .in1(32'h30ac), .in2(32'h3158), .in3(32'h3204), .out(INT_Handle), .sel(nextInt));
  assign jalr_pc = ALU_out & ~32'h1;  // AND_Gate and_10, 32 bits wide
  RAM #(.addrWidth(10), .dataWidth(32), .bus("separate"), .Select("high")) ram_1 (
    .addr(ALU_out[11:2]), .din(MDin), .data(mem_ld), .str(MemWrite), .clk(CLK));  // open: sel, ld, clr
  D_Flip_Flop #(.trigger("high"), .Pre_Clr_Positions("LEGACY"), .NegatePresetClear("false"), .enable("true"), .NewFFLayout("false")) d_ff_2 (.Q(d_ff_2_q));  // open: clk, D, Qn, preset, en, reset
  // Probe on 13'hcd
  Decoder #(.select(2), .tristate("false"), .disabled("Z"), .enable("true")) decoder_1 (
    .out1(RST1), .out2(RST2), .out3(RST3), .sel(nextInt), .en(INT_SIG));  // open: out0
  or or_10 (or_10_out, INT_SIG, uret);
  Multiplexer #(.select(1), .width(32), .disabled("Z"), .enable("false")) multiplexer_12 (
    .in0(ALU_out), .in1(mem_ld), .out(multiplexer_12_out), .sel(\单周期硬布线控制器_1_memtoreg ));
  Comparator #(.width(13), .mode("twosComplement")) comparator_10 (
    .a(CNT_num), .b(13'hcd), .eq(comparator_10_eq), .lt(comparator_10_lt));  // open: gt
  Clock #(.highDuration(1), .lowDuration(1)) clock_1 (.out(clock_1_out));
  Multiplexer #(.select(1), .width(32), .disabled("Z"), .enable("false")) multiplexer_13 (
    .in0(multiplexer_12_out), .in1(PC_4), .out(RDin), .sel(Jxx_ctrl));
  Counter #(.width(13), .max('h1fff), .ongoal("stay"), .trigger("rising"), .behavior("old")) counter_2 (
    .count(comparator_10_lt), .Q(CNT_num), .clk(clock_1_out));  // open: load, D, carry, clr, preset
  nand nand_1 (nand_1_out, d_ff_2_q, comparator_10_eq);
  Multiplexer #(.select(1), .width(32), .disabled("Z"), .enable("false")) multiplexer_14 (
    .in0(nextPC), .in1(EPC2_q), .out(multiplexer_14_out), .sel(uret));
  Multiplexer #(.select(1), .width(2), .disabled("Z"), .enable("false")) multiplexer_15 (
    .in0(nextInt), .in1(IntID2_q), .out(multiplexer_15_out), .sel(uret));
  Comparator #(.width(32), .mode("twosComplement")) comparator_11 (
    .a(R1_out), .b(32'h22), .eq(comparator_11_eq));  // open: gt, lt
  Decoder #(.select(2), .tristate("false"), .disabled("Z"), .enable("false")) decoder_2 (
    .out0(decoder_2_out0), .out1(decoder_2_out1), .out2(decoder_2_out2), .out3(decoder_2_out3),
    .sel(ALU_out[1:0]));
  assign CLK = nand_1_out ? clock_1_out : 1'bz;  // Controlled_Buffer controlled_buffer_1
  Pull_Resistor #(.pull(1)) pull_resistor_4 (.node(CLK));
  Register #(.width(32), .trigger("rising"), .Select("low")) EPC1 (
    .D(multiplexer_14_out), .en(or_10_out), .Q(mEPC), .clk(CLK));  // open: clr
  Register #(.width(2), .trigger("rising"), .Select("low")) IntID1 (
    .D(multiplexer_15_out), .en(or_10_out), .Q(IntID), .clk(CLK));  // open: clr
  and and_11 (and_11_out, ecall, comparator_11_eq);
  and and_12 (and_12_out, ~comparator_11_eq, ecall);  // AND_Gate
  Multiplexer #(.select(1), .width(32), .disabled("Z"), .enable("false")) multiplexer_16 (
    .in0(mEPC), .in1(EPC3_q), .out(multiplexer_16_out), .sel(uret));
  Multiplexer #(.select(1), .width(2), .disabled("Z"), .enable("false")) multiplexer_17 (
    .in0(IntID), .in1(IntID3_q), .out(multiplexer_17_out), .sel(uret));
  Multiplexer #(.select(1), .width(8), .disabled("Z"), .enable("false")) multiplexer_18 (
    .in0(mem_ld[7:0]), .in1(R2_out[7:0]), .out(sb_word[7:0]), .sel(decoder_2_out0));
  Multiplexer #(.select(1), .width(32), .disabled("Z"), .enable("false")) multiplexer_19 (
    .in0(R2_out), .in1(sb_word), .out(MDin), .sel(sb));
  Register #(.width(32), .trigger("rising"), .Select("low")) EPC2 (
    .D(multiplexer_16_out), .en(or_10_out), .Q(EPC2_q), .clk(CLK));  // open: clr
  Register #(.width(2), .trigger("rising"), .Select("low")) IntID2 (
    .D(multiplexer_17_out), .en(or_10_out), .Q(IntID2_q), .clk(CLK));  // open: clr
  Register #(.width(32), .trigger("rising"), .Select("low")) register_1 (
    .D(R2_out), .en(and_11_out), .Q(LedData), .clk(CLK));  // open: clr
  and and_13 (halt, and_12_out, ~Go);  // AND_Gate
  Multiplexer #(.select(1), .width(8), .disabled("Z"), .enable("false")) multiplexer_20 (
    .in0(mem_ld[15:8]), .in1(R2_out[7:0]), .out(sb_word[15:8]), .sel(decoder_2_out1));
  Multiplexer #(.select(1), .width(8), .disabled("Z"), .enable("false")) multiplexer_21 (
    .in0(mem_ld[23:16]), .in1(R2_out[7:0]), .out(sb_word[23:16]), .sel(decoder_2_out2));
  Multiplexer #(.select(1), .width(32), .disabled("Z"), .enable("false")) multiplexer_22 (
    .in0(EPC2_q), .in1({32{1'b0}}), .out(multiplexer_22_out), .sel(uret));
  Multiplexer #(.select(1), .width(2), .disabled("Z"), .enable("false")) multiplexer_23 (
    .in0(IntID2_q), .in1(2'b00), .out(multiplexer_23_out), .sel(uret));
  Multiplexer #(.select(1), .width(8), .disabled("Z"), .enable("false")) multiplexer_24 (
    .in0(mem_ld[31:24]), .in1(R2_out[7:0]), .out(sb_word[31:24]), .sel(decoder_2_out3));
  Register #(.width(32), .trigger("rising"), .Select("low")) EPC3 (
    .D(multiplexer_22_out), .en(or_10_out), .Q(EPC3_q), .clk(CLK));  // open: clr
  Register #(.width(2), .trigger("rising"), .Select("low")) IntID3 (
    .D(multiplexer_23_out), .en(or_10_out), .Q(IntID3_q), .clk(CLK));  // open: clr

  // Other names for the same wires on the sheet: mem_addr[31:0] = ALU_out

  // Notes on the sheet:
  //   中断源
  //   中断等待指示
  //   总复位信号应将除ROM以外所有存储组件全部清零
  //   多级中断测试信号模拟器
  //   数码管输出
  //   数码管输出应该用寄存器锁存，否则显示数据只能一闪而过
  //   指令探针
  //   指令存储器
  //   指令字
  //   contents of rom_1 (hex, n*v repeats v):
  //   7d000113 100413 1f41993 41f9d993 433 c00913 800b13 140413 f47413 800293 100313 499993 89e9b3 1300533
  //   2200893 73 406282b3 fe0294e3 140413 f00f93 1f47433 1c41413 800293 100313 49d993 89e9b3 1300533
  //   2200893 73 406282b3 fe0294e3 1c45413 406b0b33 b0463 f95ff06f 2b3 fff2c293 1029293 fff2e293 500533
  //   2200893 73 f5dff06f 1112023 410113 a12023 410113 812023 410113 1312023 410113 1412023 410113 1512023
  //   410113 1612023 410113 40e073 100b13 300a13 100a93 1600433 441413 14469b3 1300533 2200893 73 fe0416e3
  //   415a0a33 fe0a10e3 40f073 ffc10113 12b03 ffc10113 12a83 ffc10113 12a03 ffc10113 12983 ffc10113 12403
  //   ffc10113 12503 ffc10113 12883 200073 1112023 410113 a12023 410113 812023 410113 1312023 410113
  //   1412023 410113 1512023 410113 1612023 410113 40e073 200b13 300a13 100a93 1600433 441413 14469b3
  //   1300533 2200893 73 fe0416e3 415a0a33 fe0a10e3 40f073 ffc10113 12b03 ffc10113 12a83 ffc10113 12a03
  //   ffc10113 12983 ffc10113 12403 ffc10113 12503 ffc10113 12883 200073 1112023 410113 a12023 410113
  //   812023 410113 1312023 410113 1412023 410113 1512023 410113 1612023 410113 40e073 300b13 300a13
  //   100a93 1600433 441413 14469b3 1300533 2200893 73 fe0416e3 415a0a33 fe0a10e3 40f073 ffc10113 12b03
  //   ffc10113 12a83 ffc10113 12a03 ffc10113 12983 ffc10113 12403 ffc10113 12503 ffc10113 12883 200073
  //   JAL
  //   JALR
  //   URET
  //   Beq
  //   Bne
  //   MemToReg
  //   MemWrite
  //   AluOP
  //   AluSrcB
  //   RegWrite
  //   S_Type
  //   sb
  //   bge
  //   为方便自动评测，需要输出PC，IR，寄存器堆写如数据RDin
  //   RAM写使能MemWrite、RAM写入数据MDin等信号
  //   数据存储器
  //   控制位
  //   暂停节拍，不能为0
  //   戳工具置1进入计数暂停模式，ctrl+k时钟自动运行到对应节拍暂停
  //   ctrl+k关闭时钟连续运行，将控制位置零，进入单步调试模式调试
  //   可计数暂停的时钟源
endmodule

module \封装正确性测试  (
);

  wire IR1, IR2, IR3, MemW, RegW;
  wire [31:0] EX_PC, ID_PC, IF_PC, IR, LED, MDin, MDinr, MEM_PC, PC, RDin, RDinr, WB_PC;

  \单周期RISC_V  \u_单周期risc_v_1  (
    .IR1(IR1), .IR2(IR2), .IR3(IR3), .RegWrite(RegW), .MemWrite(MemW), .PC(PC), .IR(IR), .RDin(RDin),
    .MDin(MDin), .LedData(LED));
  \气泡流水线  \u_气泡流水线_1  (
    .RegWrite(RegW), .MemWrite(MemW), .IF_PC(IF_PC), .ID_PC(ID_PC), .EX_PC(EX_PC), .M_PC(MEM_PC),
    .WB_PC(WB_PC), .RDin(RDinr), .MDin(MDinr), .LedData(LED));
  \单周期_单级中断  \u_单周期_单级中断_1  (
    .IR1(IR1), .IR2(IR2), .IR3(IR3), .RegWrite(RegW), .MemWrite(MemW), .PC(PC), .IR(IR), .RDin(RDin),
    .MDin(MDin), .LedData(LED));
  \理想流水线  \u_理想流水线_1  (
    .RegWrite(RegW), .MemWrite(MemW), .IF_PC(IF_PC), .ID_PC(ID_PC), .EX_PC(EX_PC), .M_PC(MEM_PC),
    .WB_PC(WB_PC), .RDin(RDinr), .MDin(MDinr), .LedData(LED));
  \重定向流水线  \u_重定向流水线_1  (
    .RegWrite(RegW), .MemWrite(MemW), .IF_PC(IF_PC), .ID_PC(ID_PC), .EX_PC(EX_PC), .M_PC(MEM_PC),
    .WB_PC(WB_PC), .RDin(RDinr), .MDin(MDinr), .LedData(LED));
  \单周期_多级中断  \u_单周期_多级中断_1  (
    .IR1(IR1), .IR2(IR2), .IR3(IR3), .RegWrite(RegW), .MemWrite(MemW), .PC(PC), .IR(IR), .RDin(RDin),
    .MDin(MDin), .LedData(LED));

  // Notes on the sheet:
  //   单周期封装测试
  //   气泡流水封装测试
  //   单周期+单级中断封装测试
  //   请检查上面封装有无位宽不匹配，引脚标签是否和连接的标签相对应，否则无法在educoder平台上正确测试
  //   理想流水封装测试
  //   重定向流水封装测试
  //   单周期+多级中断封装测试
endmodule

module \理想流水寄存器  (
  input  clk,
  input  ALU_src,
  input  [3:0] ALU_op,
  input  ecall,
  input  MemWrite,
  input  RegWrite,
  input  MemToReg,
  input  [31:0] PC,
  input  [31:0] Instr,
  input  [31:0] R1,
  input  [31:0] R2,
  input  [31:0] Imm,
  input  [31:0] ALU,
  input  [31:0] MemData,
  input  [4:0] WriteReg_num,
  output ALU_src_out,
  output [3:0] ALU_op_out,
  output ecall_out,
  output MemWrite_out,
  output RegWrite_out,
  output MemToReg_out,
  output [31:0] PC_out,
  output [31:0] Instr_out,
  output [31:0] R1_out,
  output [31:0] R2_out,
  output [31:0] Imm_out,
  output [31:0] ALU_out,
  output [31:0] MemData_out,
  output [4:0] WriteReg__out
);

  Register #(.width(1), .trigger("rising"), .Select("low")) register_1 (
    .D(ALU_src), .Q(ALU_src_out), .clk(clk));  // open: en, clr
  Register #(.width(4), .trigger("rising"), .Select("low")) register_2 (
    .D(ALU_op), .Q(ALU_op_out), .clk(clk));  // open: en, clr
  Register #(.width(1), .trigger("rising"), .Select("low")) register_3 (
    .D(ecall), .Q(ecall_out), .clk(clk));  // open: en, clr
  Register #(.width(1), .trigger("rising"), .Select("low")) register_4 (
    .D(MemWrite), .Q(MemWrite_out), .clk(clk));  // open: en, clr
  Register #(.width(1), .trigger("rising"), .Select("low")) register_5 (
    .D(RegWrite), .Q(RegWrite_out), .clk(clk));  // open: en, clr
  Register #(.width(1), .trigger("rising"), .Select("low")) register_6 (
    .D(MemToReg), .Q(MemToReg_out), .clk(clk));  // open: en, clr
  Register #(.width(32), .trigger("rising"), .Select("low")) register_7 (
    .D(PC), .Q(PC_out), .clk(clk));  // open: en, clr
  Register #(.width(32), .trigger("rising"), .Select("low")) register_8 (
    .D(Instr), .Q(Instr_out), .clk(clk));  // open: en, clr
  Register #(.width(32), .trigger("rising"), .Select("low")) register_9 (
    .D(R1), .Q(R1_out), .clk(clk));  // open: en, clr
  Register #(.width(32), .trigger("rising"), .Select("low")) register_10 (
    .D(R2), .Q(R2_out), .clk(clk));  // open: en, clr
  Register #(.width(32), .trigger("rising"), .Select("low")) register_11 (
    .D(Imm), .Q(Imm_out), .clk(clk));  // open: en, clr
  Register #(.width(32), .trigger("rising"), .Select("low")) register_12 (
    .D(ALU), .Q(ALU_out), .clk(clk));  // open: en, clr
  Register #(.width(32), .trigger("rising"), .Select("low")) register_13 (
    .D(MemData), .Q(MemData_out), .clk(clk));  // open: en, clr
  Register #(.width(5), .trigger("rising"), .Select("low")) register_14 (
    .D(WriteReg_num), .Q(WriteReg__out), .clk(clk));  // open: en, clr

  // Notes on the sheet:
  //   EX->MEM: MemWrite
  //   ID->EX: ALU_src, ALU_op, ecall
  //   MEM->WB: RegWrite, MemToReg
endmodule

module \气泡流水线寄存器  (
  input  Flush,
  input  Enable,
  input  clk,
  input  ALU_src,
  input  [3:0] ALU_op,
  input  BGE,
  input  BNE,
  input  BEQ,
  input  SB,
  input  MemWrite,
  input  RegWrite,
  input  MemToReg,
  input  ecall,
  input  JAL,
  input  JALR,
  input  [31:0] PC,
  input  [31:0] Instr,
  input  [31:0] R1,
  input  [31:0] R2,
  input  [31:0] Imm,
  input  [31:0] ALU,
  input  [31:0] MemData,
  input  [4:0] WriteReg_num,
  output ALU_src_out,
  output [3:0] ALU_op_out,
  output BGE_out,
  output BNE_out,
  output BEQ_out,
  output SB_out,
  output MemWrite_out,
  output RegWrite_out,
  output MemToReg_out,
  output ecall_out,
  output JAL_out,
  output JALR_out,
  output [31:0] PC_out,
  output [31:0] Instr_out,
  output [31:0] R1_out,
  output [31:0] R2_out,
  output [31:0] Imm_out,
  output [31:0] ALU_out,
  output [31:0] MemData_out,
  output [4:0] WriteReg__out
);

  wire multiplexer_1_out, multiplexer_3_out, multiplexer_4_out, multiplexer_5_out, multiplexer_6_out,
       multiplexer_7_out, multiplexer_8_out, multiplexer_9_out, multiplexer_10_out, multiplexer_11_out,
       multiplexer_12_out, or_1_out;
  wire [3:0] multiplexer_2_out;
  wire [4:0] multiplexer_20_out;
  wire [31:0] multiplexer_13_out, multiplexer_14_out, multiplexer_15_out, multiplexer_16_out,
       multiplexer_17_out, multiplexer_18_out, multiplexer_19_out;

  or or_1 (or_1_out, Flush, Enable);
  Multiplexer #(.select(1), .width(1), .disabled("Z"), .enable("false")) multiplexer_1 (
    .in0(ALU_src), .in1(1'b0), .out(multiplexer_1_out), .sel(Flush));
  Multiplexer #(.select(1), .width(4), .disabled("Z"), .enable("false")) multiplexer_2 (
    .in0(ALU_op), .in1(4'b0000), .out(multiplexer_2_out), .sel(Flush));
  Multiplexer #(.select(1), .width(1), .disabled("Z"), .enable("false")) multiplexer_3 (
    .in0(BGE), .in1(1'b0), .out(multiplexer_3_out), .sel(Flush));
  Multiplexer #(.select(1), .width(1), .disabled("Z"), .enable("false")) multiplexer_4 (
    .in0(BNE), .in1(1'b0), .out(multiplexer_4_out), .sel(Flush));
  Multiplexer #(.select(1), .width(1), .disabled("Z"), .enable("false")) multiplexer_5 (
    .in0(BEQ), .in1(1'b0), .out(multiplexer_5_out), .sel(Flush));
  Multiplexer #(.select(1), .width(1), .disabled("Z"), .enable("false")) multiplexer_6 (
    .in0(SB), .in1(1'b0), .out(multiplexer_6_out), .sel(Flush));
  Multiplexer #(.select(1), .width(1), .disabled("Z"), .enable("false")) multiplexer_7 (
    .in0(MemWrite), .in1(1'b0), .out(multiplexer_7_out), .sel(Flush));
  Multiplexer #(.select(1), .width(1), .disabled("Z"), .enable("false")) multiplexer_8 (
    .in0(RegWrite), .in1(1'b0), .out(multiplexer_8_out), .sel(Flush));
  Multiplexer #(.select(1), .width(1), .disabled("Z"), .enable("false")) multiplexer_9 (
    .in0(MemToReg), .in1(1'b0), .out(multiplexer_9_out), .sel(Flush));
  Multiplexer #(.select(1), .width(1), .disabled("Z"), .enable("false")) multiplexer_10 (
    .in0(ecall), .in1(1'b0), .out(multiplexer_10_out), .sel(Flush));
  Multiplexer #(.select(1), .width(1), .disabled("Z"), .enable("false")) multiplexer_11 (
    .in0(JAL), .in1(1'b0), .out(multiplexer_11_out), .sel(Flush));
  Multiplexer #(.select(1), .width(1), .disabled("Z"), .enable("false")) multiplexer_12 (
    .in0(JALR), .in1(1'b0), .out(multiplexer_12_out), .sel(Flush));
  Multiplexer #(.select(1), .width(32), .disabled("Z"), .enable("false")) multiplexer_13 (
    .in0(PC), .in1({32{1'b0}}), .out(multiplexer_13_out), .sel(Flush));
  Multiplexer #(.select(1), .width(32), .disabled("Z"), .enable("false")) multiplexer_14 (
    .in0(Instr), .in1({32{1'b0}}), .out(multiplexer_14_out), .sel(Flush));
  Multiplexer #(.select(1), .width(32), .disabled("Z"), .enable("false")) multiplexer_15 (
    .in0(R1), .in1({32{1'b0}}), .out(multiplexer_15_out), .sel(Flush));
  Multiplexer #(.select(1), .width(32), .disabled("Z"), .enable("false")) multiplexer_16 (
    .in0(R2), .in1({32{1'b0}}), .out(multiplexer_16_out), .sel(Flush));
  Multiplexer #(.select(1), .width(32), .disabled("Z"), .enable("false")) multiplexer_17 (
    .in0(Imm), .in1({32{1'b0}}), .out(multiplexer_17_out), .sel(Flush));
  Multiplexer #(.select(1), .width(32), .disabled("Z"), .enable("false")) multiplexer_18 (
    .in0(ALU), .in1({32{1'b0}}), .out(multiplexer_18_out), .sel(Flush));
  Multiplexer #(.select(1), .width(32), .disabled("Z"), .enable("false")) multiplexer_19 (
    .in0(MemData), .in1({32{1'b0}}), .out(multiplexer_19_out), .sel(Flush));
  Multiplexer #(.select(1), .width(5), .disabled("Z"), .enable("false")) multiplexer_20 (
    .in0(WriteReg_num), .in1({5{1'b0}}), .out(multiplexer_20_out), .sel(Flush));
  Register #(.width(1), .trigger("rising"), .Select("low")) register_1 (
    .D(multiplexer_1_out), .en(or_1_out), .Q(ALU_src_out), .clk(clk));  // open: clr
  Register #(.width(4), .trigger("rising"), .Select("low")) register_2 (
    .D(multiplexer_2_out), .en(or_1_out), .Q(ALU_op_out), .clk(clk));  // open: clr
  Register #(.width(1), .trigger("rising"), .Select("low")) register_3 (
    .D(multiplexer_3_out), .en(or_1_out), .Q(BGE_out), .clk(clk));  // open: clr
  Register #(.width(1), .trigger("rising"), .Select("low")) register_4 (
    .D(multiplexer_4_out), .en(or_1_out), .Q(BNE_out), .clk(clk));  // open: clr
  Register #(.width(1), .trigger("rising"), .Select("low")) register_5 (
    .D(multiplexer_5_out), .en(or_1_out), .Q(BEQ_out), .clk(clk));  // open: clr
  Register #(.width(1), .trigger("rising"), .Select("low")) register_6 (
    .D(multiplexer_6_out), .en(or_1_out), .Q(SB_out), .clk(clk));  // open: clr
  Register #(.width(1), .trigger("rising"), .Select("low")) register_7 (
    .D(multiplexer_7_out), .en(or_1_out), .Q(MemWrite_out), .clk(clk));  // open: clr
  Register #(.width(1), .trigger("rising"), .Select("low")) register_8 (
    .D(multiplexer_8_out), .en(or_1_out), .Q(RegWrite_out), .clk(clk));  // open: clr
  Register #(.width(1), .trigger("rising"), .Select("low")) register_9 (
    .D(multiplexer_9_out), .en(or_1_out), .Q(MemToReg_out), .clk(clk));  // open: clr
  Register #(.width(1), .trigger("rising"), .Select("low")) register_10 (
    .D(multiplexer_10_out), .en(or_1_out), .Q(ecall_out), .clk(clk));  // open: clr
  Register #(.width(1), .trigger("rising"), .Select("low")) register_11 (
    .D(multiplexer_11_out), .en(or_1_out), .Q(JAL_out), .clk(clk));  // open: clr
  Register #(.width(1), .trigger("rising"), .Select("low")) register_12 (
    .D(multiplexer_12_out), .en(or_1_out), .Q(JALR_out), .clk(clk));  // open: clr
  Register #(.width(32), .trigger("rising"), .Select("low")) register_13 (
    .D(multiplexer_13_out), .en(or_1_out), .Q(PC_out), .clk(clk));  // open: clr
  Register #(.width(32), .trigger("rising"), .Select("low")) register_14 (
    .D(multiplexer_14_out), .en(or_1_out), .Q(Instr_out), .clk(clk));  // open: clr
  Register #(.width(32), .trigger("rising"), .Select("low")) register_15 (
    .D(multiplexer_15_out), .en(or_1_out), .Q(R1_out), .clk(clk));  // open: clr
  Register #(.width(32), .trigger("rising"), .Select("low")) register_16 (
    .D(multiplexer_16_out), .en(or_1_out), .Q(R2_out), .clk(clk));  // open: clr
  Register #(.width(32), .trigger("rising"), .Select("low")) register_17 (
    .D(multiplexer_17_out), .en(or_1_out), .Q(Imm_out), .clk(clk));  // open: clr
  Register #(.width(32), .trigger("rising"), .Select("low")) register_18 (
    .D(multiplexer_18_out), .en(or_1_out), .Q(ALU_out), .clk(clk));  // open: clr
  Register #(.width(32), .trigger("rising"), .Select("low")) register_19 (
    .D(multiplexer_19_out), .en(or_1_out), .Q(MemData_out), .clk(clk));  // open: clr
  Register #(.width(5), .trigger("rising"), .Select("low")) register_20 (
    .D(multiplexer_20_out), .en(or_1_out), .Q(WriteReg__out), .clk(clk));  // open: clr

  // Notes on the sheet:
  //   EX->MEM: MemWrite, sb
  //   ID->EX: ALU_src, ALU_op, bge, bne, beq
  //   MEM->WB: RegWrite, MemToReg, JAL, JARL, ecall
endmodule

module DataHazzard (
  input  rs_used,
  input  rt_used,
  input  [4:0] rs,
  input  [4:0] rt,
  input  EX_RW,
  input  MEM_RW,
  input  [4:0] EX_Reg,
  input  [4:0] MEM_Reg,
  output DataHazzard
);

  wire and_1_out, and_2_out, and_3_out, and_4_out, comparator_1_eq, comparator_2_eq, comparator_3_eq,
       comparator_4_eq, comparator_5_eq, comparator_6_eq;

  Comparator #(.width(5), .mode("twosComplement")) comparator_1 (
    .a({5{1'b0}}), .b(rs), .eq(comparator_1_eq));  // open: gt, lt
  Comparator #(.width(5), .mode("twosComplement")) comparator_2 (
    .a({5{1'b0}}), .b(rt), .eq(comparator_2_eq));  // open: gt, lt
  Comparator #(.width(5), .mode("twosComplement")) comparator_3 (
    .a(rs), .b(EX_Reg), .eq(comparator_3_eq));  // open: gt, lt
  Comparator #(.width(5), .mode("twosComplement")) comparator_4 (
    .a(rt), .b(EX_Reg), .eq(comparator_4_eq));  // open: gt, lt
  Comparator #(.width(5), .mode("twosComplement")) comparator_5 (
    .a(rs), .b(MEM_Reg), .eq(comparator_5_eq));  // open: gt, lt
  Comparator #(.width(5), .mode("twosComplement")) comparator_6 (
    .a(rt), .b(MEM_Reg), .eq(comparator_6_eq));  // open: gt, lt
  and and_1 (and_1_out, ~comparator_2_eq, rt_used, MEM_RW, comparator_6_eq);  // AND_Gate
  and and_2 (and_2_out, ~comparator_1_eq, rs_used, EX_RW, comparator_3_eq);  // AND_Gate
  and and_3 (and_3_out, ~comparator_1_eq, rs_used, MEM_RW, comparator_5_eq);  // AND_Gate
  and and_4 (and_4_out, ~comparator_2_eq, rt_used, EX_RW, comparator_4_eq);  // AND_Gate
  or or_1 (DataHazzard, and_2_out, and_3_out, and_1_out, and_4_out);

  // Other names for the same wires on the sheet: rs_t = rs_used; rt_t = rt_used
endmodule

module foward (
  input  rs_used,
  input  EX_MemToReg,
  input  rt_used,
  input  [4:0] ID_rs,
  input  [4:0] ID_rt,
  input  EX_RW,
  input  MEM_RW,
  input  [4:0] EX_Reg,
  input  [4:0] MEM_Reg,
  output Load_Use,
  output [1:0] ID_rs_forward,
  output [1:0] ID_rt_forward
);

  wire comparator_1_eq, comparator_2_eq, comparator_3_eq, comparator_4_eq, comparator_5_eq, comparator_6_eq,
       or_1_out;

  Comparator #(.width(5), .mode("twosComplement")) comparator_1 (
    .a({5{1'b0}}), .b(ID_rs), .eq(comparator_1_eq));  // open: gt, lt
  Comparator #(.width(5), .mode("twosComplement")) comparator_2 (
    .a({5{1'b0}}), .b(ID_rt), .eq(comparator_2_eq));  // open: gt, lt
  Comparator #(.width(5), .mode("twosComplement")) comparator_3 (
    .a(ID_rs), .b(EX_Reg), .eq(comparator_3_eq));  // open: gt, lt
  Comparator #(.width(5), .mode("twosComplement")) comparator_4 (
    .a(ID_rt), .b(EX_Reg), .eq(comparator_4_eq));  // open: gt, lt
  Comparator #(.width(5), .mode("twosComplement")) comparator_5 (
    .a(ID_rs), .b(MEM_Reg), .eq(comparator_5_eq));  // open: gt, lt
  Comparator #(.width(5), .mode("twosComplement")) comparator_6 (
    .a(ID_rt), .b(MEM_Reg), .eq(comparator_6_eq));  // open: gt, lt
  and and_1 (ID_rs_forward[0], ~comparator_1_eq, rs_used, EX_RW, comparator_3_eq);  // AND_Gate
  and and_2 (ID_rs_forward[1], ~comparator_1_eq, rs_used, MEM_RW, comparator_5_eq);  // AND_Gate
  and and_3 (ID_rt_forward[1], ~comparator_2_eq, rt_used, MEM_RW, comparator_6_eq);  // AND_Gate
  and and_4 (ID_rt_forward[0], ~comparator_2_eq, rt_used, EX_RW, comparator_4_eq);  // AND_Gate
  or or_1 (or_1_out, ID_rs_forward[0], ID_rt_forward[0]);
  and and_5 (Load_Use, EX_MemToReg, or_1_out);

  // Other names for the same wires on the sheet: rs = rs_used; rt = rt_used
endmodule

module \重定向流水寄存器  (
  input  Flush,
  input  Enable,
  input  clk,
  input  ALU_src,
  input  [3:0] ALU_op,
  input  BGE,
  input  BNE,
  input  BEQ,
  input  SB,
  input  MemWrite,
  input  RegWrite,
  input  MemToReg,
  input  ecall,
  input  JAL,
  input  JALR,
  input  [31:0] PC,
  input  [31:0] Instr,
  input  [31:0] R1,
  input  [31:0] R2,
  input  [31:0] Imm,
  input  [31:0] ALU,
  input  [31:0] MemData,
  input  [4:0] WriteReg_num,
  input  [1:0] Rs_fwd,
  input  [1:0] Rt_fwd,
  output ALU_src_out,
  output [3:0] ALU_op_out,
  output BGE_out,
  output BNE_out,
  output BEQ_out,
  output SB_out,
  output MemWrite_out,
  output RegWrite_out,
  output MemToReg_out,
  output ecall_out,
  output JAL_out,
  output JALR_out,
  output [31:0] PC_out,
  output [31:0] Instr_out,
  output [31:0] R1_out,
  output [31:0] R2_out,
  output [31:0] Imm_out,
  output [31:0] ALU_out,
  output [31:0] MemData_out,
  output [4:0] WriteReg__out,
  output [1:0] Rs_fwd_out,
  output [1:0] Rt_fwd_out
);

  wire multiplexer_1_out, multiplexer_3_out, multiplexer_4_out, multiplexer_5_out, multiplexer_6_out,
       multiplexer_7_out, multiplexer_8_out, multiplexer_9_out, multiplexer_10_out, multiplexer_11_out,
       multiplexer_12_out, or_1_out;
  wire [1:0] multiplexer_21_out, multiplexer_22_out;
  wire [3:0] multiplexer_2_out;
  wire [4:0] multiplexer_20_out;
  wire [31:0] multiplexer_13_out, multiplexer_14_out, multiplexer_15_out, multiplexer_16_out,
       multiplexer_17_out, multiplexer_18_out, multiplexer_19_out;

  or or_1 (or_1_out, Flush, Enable);
  Multiplexer #(.select(1), .width(1), .disabled("Z"), .enable("false")) multiplexer_1 (
    .in0(ALU_src), .in1(1'b0), .out(multiplexer_1_out), .sel(Flush));
  Multiplexer #(.select(1), .width(4), .disabled("Z"), .enable("false")) multiplexer_2 (
    .in0(ALU_op), .in1(4'b0000), .out(multiplexer_2_out), .sel(Flush));
  Multiplexer #(.select(1), .width(1), .disabled("Z"), .enable("false")) multiplexer_3 (
    .in0(BGE), .in1(1'b0), .out(multiplexer_3_out), .sel(Flush));
  Multiplexer #(.select(1), .width(1), .disabled("Z"), .enable("false")) multiplexer_4 (
    .in0(BNE), .in1(1'b0), .out(multiplexer_4_out), .sel(Flush));
  Multiplexer #(.select(1), .width(1), .disabled("Z"), .enable("false")) multiplexer_5 (
    .in0(BEQ), .in1(1'b0), .out(multiplexer_5_out), .sel(Flush));
  Multiplexer #(.select(1), .width(1), .disabled("Z"), .enable("false")) multiplexer_6 (
    .in0(SB), .in1(1'b0), .out(multiplexer_6_out), .sel(Flush));
  Multiplexer #(.select(1), .width(1), .disabled("Z"), .enable("false")) multiplexer_7 (
    .in0(MemWrite), .in1(1'b0), .out(multiplexer_7_out), .sel(Flush));
  Multiplexer #(.select(1), .width(1), .disabled("Z"), .enable("false")) multiplexer_8 (
    .in0(RegWrite), .in1(1'b0), .out(multiplexer_8_out), .sel(Flush));
  Multiplexer #(.select(1), .width(1), .disabled("Z"), .enable("false")) multiplexer_9 (
    .in0(MemToReg), .in1(1'b0), .out(multiplexer_9_out), .sel(Flush));
  Multiplexer #(.select(1), .width(1), .disabled("Z"), .enable("false")) multiplexer_10 (
    .in0(ecall), .in1(1'b0), .out(multiplexer_10_out), .sel(Flush));
  Multiplexer #(.select(1), .width(1), .disabled("Z"), .enable("false")) multiplexer_11 (
    .in0(JAL), .in1(1'b0), .out(multiplexer_11_out), .sel(Flush));
  Multiplexer #(.select(1), .width(1), .disabled("Z"), .enable("false")) multiplexer_12 (
    .in0(JALR), .in1(1'b0), .out(multiplexer_12_out), .sel(Flush));
  Multiplexer #(.select(1), .width(32), .disabled("Z"), .enable("false")) multiplexer_13 (
    .in0(PC), .in1({32{1'b0}}), .out(multiplexer_13_out), .sel(Flush));
  Multiplexer #(.select(1), .width(32), .disabled("Z"), .enable("false")) multiplexer_14 (
    .in0(Instr), .in1({32{1'b0}}), .out(multiplexer_14_out), .sel(Flush));
  Multiplexer #(.select(1), .width(32), .disabled("Z"), .enable("false")) multiplexer_15 (
    .in0(R1), .in1({32{1'b0}}), .out(multiplexer_15_out), .sel(Flush));
  Multiplexer #(.select(1), .width(32), .disabled("Z"), .enable("false")) multiplexer_16 (
    .in0(R2), .in1({32{1'b0}}), .out(multiplexer_16_out), .sel(Flush));
  Multiplexer #(.select(1), .width(32), .disabled("Z"), .enable("false")) multiplexer_17 (
    .in0(Imm), .in1({32{1'b0}}), .out(multiplexer_17_out), .sel(Flush));
  Multiplexer #(.select(1), .width(32), .disabled("Z"), .enable("false")) multiplexer_18 (
    .in0(ALU), .in1({32{1'b0}}), .out(multiplexer_18_out), .sel(Flush));
  Multiplexer #(.select(1), .width(32), .disabled("Z"), .enable("false")) multiplexer_19 (
    .in0(MemData), .in1({32{1'b0}}), .out(multiplexer_19_out), .sel(Flush));
  Multiplexer #(.select(1), .width(5), .disabled("Z"), .enable("false")) multiplexer_20 (
    .in0(WriteReg_num), .in1({5{1'b0}}), .out(multiplexer_20_out), .sel(Flush));
  Multiplexer #(.select(1), .width(2), .disabled("Z"), .enable("false")) multiplexer_21 (
    .in0(Rs_fwd), .in1(2'b00), .out(multiplexer_21_out), .sel(Flush));
  Multiplexer #(.select(1), .width(2), .disabled("Z"), .enable("false")) multiplexer_22 (
    .in0(Rt_fwd), .in1(2'b00), .out(multiplexer_22_out), .sel(Flush));
  Register #(.width(1), .trigger("rising"), .Select("low")) register_1 (
    .D(multiplexer_1_out), .en(or_1_out), .Q(ALU_src_out), .clk(clk));  // open: clr
  Register #(.width(4), .trigger("rising"), .Select("low")) register_2 (
    .D(multiplexer_2_out), .en(or_1_out), .Q(ALU_op_out), .clk(clk));  // open: clr
  Register #(.width(1), .trigger("rising"), .Select("low")) register_3 (
    .D(multiplexer_3_out), .en(or_1_out), .Q(BGE_out), .clk(clk));  // open: clr
  Register #(.width(1), .trigger("rising"), .Select("low")) register_4 (
    .D(multiplexer_4_out), .en(or_1_out), .Q(BNE_out), .clk(clk));  // open: clr
  Register #(.width(1), .trigger("rising"), .Select("low")) register_5 (
    .D(multiplexer_5_out), .en(or_1_out), .Q(BEQ_out), .clk(clk));  // open: clr
  Register #(.width(1), .trigger("rising"), .Select("low")) register_6 (
    .D(multiplexer_6_out), .en(or_1_out), .Q(SB_out), .clk(clk));  // open: clr
  Register #(.width(1), .trigger("rising"), .Select("low")) register_7 (
    .D(multiplexer_7_out), .en(or_1_out), .Q(MemWrite_out), .clk(clk));  // open: clr
  Register #(.width(1), .trigger("rising"), .Select("low")) register_8 (
    .D(multiplexer_8_out), .en(or_1_out), .Q(RegWrite_out), .clk(clk));  // open: clr
  Register #(.width(1), .trigger("rising"), .Select("low")) register_9 (
    .D(multiplexer_9_out), .en(or_1_out), .Q(MemToReg_out), .clk(clk));  // open: clr
  Register #(.width(1), .trigger("rising"), .Select("low")) register_10 (
    .D(multiplexer_10_out), .en(or_1_out), .Q(ecall_out), .clk(clk));  // open: clr
  Register #(.width(1), .trigger("rising"), .Select("low")) register_11 (
    .D(multiplexer_11_out), .en(or_1_out), .Q(JAL_out), .clk(clk));  // open: clr
  Register #(.width(1), .trigger("rising"), .Select("low")) register_12 (
    .D(multiplexer_12_out), .en(or_1_out), .Q(JALR_out), .clk(clk));  // open: clr
  Register #(.width(32), .trigger("rising"), .Select("low")) register_13 (
    .D(multiplexer_13_out), .en(or_1_out), .Q(PC_out), .clk(clk));  // open: clr
  Register #(.width(32), .trigger("rising"), .Select("low")) register_14 (
    .D(multiplexer_14_out), .en(or_1_out), .Q(Instr_out), .clk(clk));  // open: clr
  Register #(.width(32), .trigger("rising"), .Select("low")) register_15 (
    .D(multiplexer_15_out), .en(or_1_out), .Q(R1_out), .clk(clk));  // open: clr
  Register #(.width(32), .trigger("rising"), .Select("low")) register_16 (
    .D(multiplexer_16_out), .en(or_1_out), .Q(R2_out), .clk(clk));  // open: clr
  Register #(.width(32), .trigger("rising"), .Select("low")) register_17 (
    .D(multiplexer_17_out), .en(or_1_out), .Q(Imm_out), .clk(clk));  // open: clr
  Register #(.width(32), .trigger("rising"), .Select("low")) register_18 (
    .D(multiplexer_18_out), .en(or_1_out), .Q(ALU_out), .clk(clk));  // open: clr
  Register #(.width(32), .trigger("rising"), .Select("low")) register_19 (
    .D(multiplexer_19_out), .en(or_1_out), .Q(MemData_out), .clk(clk));  // open: clr
  Register #(.width(5), .trigger("rising"), .Select("low")) register_20 (
    .D(multiplexer_20_out), .en(or_1_out), .Q(WriteReg__out), .clk(clk));  // open: clr
  Register #(.width(2), .trigger("rising"), .Select("low")) register_21 (
    .D(multiplexer_21_out), .en(or_1_out), .Q(Rs_fwd_out), .clk(clk));  // open: clr
  Register #(.width(2), .trigger("rising"), .Select("low")) register_22 (
    .D(multiplexer_22_out), .en(or_1_out), .Q(Rt_fwd_out), .clk(clk));  // open: clr

  // Notes on the sheet:
  //   EX->MEM: MemWrite, sb
  //   ID->EX: ALU_src, ALU_op, bge, bne, beq
  //   MEM->WB: RegWrite, MemToReg, JAL, JARL, ecall
endmodule
